// Logisim project RapidRoll.circ as structural Verilog: 12 circuits, main circuit main
module main (
  input  in_1
);

  wire and_1_out, and_3_out, clock_1_out, clock_2_out, clock_3_out, clock_4_out, clock_5_out, clock_6_out,
       colision, cols1, cols2, cols3, cols4, cols5, cols6, cols7, cols8, cols9, cols10, cols11, cols12,
       cols13, cols14, cols15, cols16, comparator_1_lt, d_ff_1_q, d_ff_2_q, d_ff_3_q, da, db, dc, dd, de,
       destroy, detector_colision_1_destroy, detector_colision_2_destroy, detector_colision_3_destroy,
       detector_colision_4_destroy, detector_colision_5_destroy, detector_colision_6_destroy,
       detector_colision_7_destroy, detector_colision_8_destroy, detector_colision_9_destroy,
       detector_colision_10_destroy, detector_colision_11_destroy, detector_colision_12_destroy,
       detector_colision_13_destroy, detector_colision_14_destroy, detector_colision_15_p1,
       detector_colision_16_p1, df, dg, enable, lim_sup, mov, not_1_out, not_2_out, or_10_out, per,
       stop_personaje, ua, ub, uc, ud, ue, uf, ug;
  wire [1:0] dir;
  wire [3:0] contador_1_decenas, contador_1_unidades;
  wire [6:0] keyboard_1_data;
  wire [7:0] cont;
  wire [31:0] _1, _2, _3, _4, _5, _6, _7, _8, _9, _10, _11, _12, _13, _14, _15, _16, ABUNAI, m1, m2, m3, m4,
       m5, m6, m7, m8, m9, m10, m11, m12, m13, m14, m15, m16, multiplexer_1_out, multiplexer_2_out,
       multiplexer_3_out, multiplexer_4_out, multiplexer_5_out, multiplexer_6_out, multiplexer_7_out,
       multiplexer_8_out, multiplexer_9_out, multiplexer_10_out, multiplexer_11_out, multiplexer_12_out,
       multiplexer_13_out, multiplexer_14_out, multiplexer_15_out, multiplexer_16_out, or_5_out, p1, p2, p3,
       p4, p5, p6, p7, p8, p9, p10, p11, p12, p13, p14, p15, p16, random_1_out;

  Clock clock_1 (.out(clock_1_out));
  Keyboard keyboard_1 (.clk(clock_1_out), .avail(mov), .data(keyboard_1_data));  // open: re, clr
  Button button_1 (.out(per));
  Comparator #(.mode("unsigned")) comparator_1 (.a(cont), .b(8'h63), .lt(comparator_1_lt));  // open: gt, eq
  not not_1 (not_1_out, destroy);
  malla malla_1 (
    .dir(dir), .inf(and_1_out), .pos(and_1_out), .c1(p1), .c2(p2), .c3(p3), .c4(p4), .c5(p5), .c6(p6),
    .c7(p7), .c8(p8), .c9(p9), .c10(p10), .c11(p11), .c12(p12), .c13(p13), .c14(p14), .c15(p15), .c16(p16),
    .ZA_WARUDO(not_2_out), .reset(d_ff_1_q));
  and and_1 (and_1_out, per, enable);
  and and_2 (enable, comparator_1_lt, not_1_out);
  Multiplexer #(.width(32), .enable("false")) multiplexer_1 (
    .in0({32{1'b0}}), .in1(_1), .out(multiplexer_1_out), .sel(enable));
  not not_2 (not_2_out, stop_personaje);
  teclado teclado_1 (
    .e6(keyboard_1_data[6]), .e5(keyboard_1_data[5]), .e4(keyboard_1_data[4]), .e3(keyboard_1_data[3]),
    .e2(keyboard_1_data[2]), .e1(keyboard_1_data[1]), .e0(keyboard_1_data[0]), .s1(dir[1]), .s0(dir[0]));
  Multiplexer #(.width(32), .enable("false")) multiplexer_2 (
    .in0({32{1'b0}}), .in1(_2), .out(multiplexer_2_out), .sel(enable));
  Multiplexer #(.width(32), .enable("false")) multiplexer_3 (
    .in0({32{1'b0}}), .in1(_3), .out(multiplexer_3_out), .sel(enable));
  Clock clock_2 (.out(clock_2_out));
  Multiplexer #(.width(32), .enable("false")) multiplexer_4 (
    .in0({32{1'b0}}), .in1(_4), .out(multiplexer_4_out), .sel(enable));
  D_Flip_Flop d_ff_1 (.clk(clock_2_out), .D(lim_sup), .Q(d_ff_1_q));  // open: Qn, preset, en, reset
  Multiplexer #(.width(32), .enable("false")) multiplexer_5 (
    .in0(32'hfc0000), .in1(_5), .out(multiplexer_5_out), .sel(enable));
  and and_3 (and_3_out, colision, ~mov);  // AND_Gate
  or or_1 (colision, cols1, cols2, cols3, cols4, cols5, cols6, cols7, cols8, cols9, cols10, cols11, cols12, cols13, cols14, cols15, cols16);
  DotMatrix #(.matrixcols(16), .matrixrows(32)) dotmatrix_1 (
    .col0(multiplexer_1_out), .col1(multiplexer_2_out), .col2(multiplexer_3_out), .col3(multiplexer_4_out),
    .col4(multiplexer_5_out), .col5(multiplexer_7_out), .col6(multiplexer_6_out), .col7(multiplexer_8_out),
    .col8(multiplexer_9_out), .col9(multiplexer_11_out), .col10(multiplexer_10_out),
    .col11(multiplexer_12_out), .col12(multiplexer_13_out), .col13(multiplexer_14_out),
    .col14(multiplexer_15_out), .col15(multiplexer_16_out));
  Multiplexer #(.width(32), .enable("false")) multiplexer_6 (
    .in0({32{1'b0}}), .in1(_7), .out(multiplexer_6_out), .sel(enable));
  Multiplexer #(.width(32), .enable("false")) multiplexer_7 (
    .in0(32'ha00000), .in1(_6), .out(multiplexer_7_out), .sel(enable));
  Register #(.width(1), .trigger("high")) register_1 (
    .D(and_3_out), .Q(stop_personaje), .clk(clock_3_out));  // open: en, clr
  Clock clock_3 (.out(clock_3_out));
  Multiplexer #(.width(32), .enable("false")) multiplexer_8 (
    .in0(32'h3c0000), .in1(_8), .out(multiplexer_8_out), .sel(enable));
  DotMatrix #(.matrixcols(1), .matrixrows(32)) dotmatrix_2 (.col0(ABUNAI));
  Multiplexer #(.width(32), .enable("false")) multiplexer_9 (
    .in0({32{1'b0}}), .in1(_9), .out(multiplexer_9_out), .sel(enable));
  memoria memoria_1 (
    .click(clock_4_out), .reiniciar(lim_sup), .enable(enable), .columna1(m1), .columna2(m2), .columna3(m3),
    .columna4(m4), .columna5(m5), .columna6(m6), .columna7(m7), .columna8(m8), .columna9(m9),
    .columna10(m10), .columna11(m11), .columna12(m12), .columna13(m13), .columna14(m14), .columna15(m15),
    .columna16(m16));
  Clock clock_4 (.out(clock_4_out));
  _7_Segment_Display u_7_segment_display_1 (.g(ua), .f(ub), .a(uc), .b(ud), .e(ue), .d(uf), .c(ug));  // open: dp
  _7_Segment_Display u_7_segment_display_2 (.g(da), .f(db), .a(dc), .b(dd), .e(de), .d(df), .c(dg));  // open: dp
  Multiplexer #(.width(32), .enable("false")) multiplexer_10 (
    .in0(32'h100000), .in1(_11), .out(multiplexer_10_out), .sel(enable));
  Multiplexer #(.width(32), .enable("false")) multiplexer_11 (
    .in0(32'h3c0000), .in1(_10), .out(multiplexer_11_out), .sel(enable));
  Multiplexer #(.width(32), .enable("false")) multiplexer_12 (
    .in0(32'h80000), .in1(_12), .out(multiplexer_12_out), .sel(enable));
  Multiplexer #(.width(32), .enable("false")) multiplexer_13 (
    .in0(32'h3c0000), .in1(_13), .out(multiplexer_13_out), .sel(enable));
  detector_colision detector_colision_1 (
    .columna(m1), .peligro(ABUNAI), .colision(cols1), .destroy(detector_colision_1_destroy), .personaje(p1));
  Multiplexer #(.width(32), .enable("false")) multiplexer_14 (
    .in0({32{1'b0}}), .in1(_14), .out(multiplexer_14_out), .sel(enable));
  Multiplexer #(.width(32), .enable("false")) multiplexer_15 (
    .in0({32{1'b0}}), .in1(_15), .out(multiplexer_15_out), .sel(enable));
  Clock clock_5 (.out(clock_5_out));
  assign _1 = p1 | m1;  // OR_Gate or_2, 32 bits wide
  detector_colision detector_colision_2 (
    .columna(m2), .peligro(ABUNAI), .colision(cols2), .destroy(detector_colision_2_destroy), .personaje(p2));
  Multiplexer #(.width(32), .enable("false")) multiplexer_16 (
    .in0({32{1'b0}}), .in1(_16), .out(multiplexer_16_out), .sel(enable));
  Random #(.width(32)) random_1 (.clk(clock_5_out), .next(in_1), .out(random_1_out));  // open: clr
  assign _2 = p2 | m2;  // OR_Gate or_3, 32 bits wide
  detector_colision detector_colision_3 (
    .columna(m3), .peligro(ABUNAI), .colision(cols3), .destroy(detector_colision_3_destroy), .personaje(p3));
  assign ABUNAI = random_1_out & or_5_out;  // AND_Gate and_4, 32 bits wide
  assign _3 = p3 | m3;  // OR_Gate or_4, 32 bits wide
  detector_colision detector_colision_4 (
    .columna(m4), .peligro(ABUNAI), .colision(cols4), .destroy(detector_colision_4_destroy), .personaje(p4));
  assign or_5_out = m1 | m2 | m3 | m4 | m5 | m6 | m7 | m8 | m9 | m10 | m11 | m12 | m13 | m14 | m15 | m16;  // OR_Gate or_5, 32 bits wide
  assign _4 = p4 | m4;  // OR_Gate or_6, 32 bits wide
  detector_colision detector_colision_5 (
    .columna(m5), .peligro(ABUNAI), .colision(cols5), .destroy(detector_colision_5_destroy), .personaje(p5));
  assign _5 = p5 | m5;  // OR_Gate or_7, 32 bits wide
  detector_colision detector_colision_6 (
    .columna(m6), .peligro(ABUNAI), .colision(cols6), .destroy(detector_colision_6_destroy), .personaje(p6));
  assign _6 = p6 | m6;  // OR_Gate or_8, 32 bits wide
  detector_colision detector_colision_7 (
    .columna(m7), .peligro(ABUNAI), .colision(cols7), .destroy(detector_colision_7_destroy), .personaje(p7));
  segmentos segmentos_1 (.in_1(contador_1_decenas), .c(dc), .d(dd), .b(db), .a(da), .g(dg), .f(df), .e(de));
  assign _7 = p7 | m7;  // OR_Gate or_9, 32 bits wide
  detector_colision detector_colision_8 (
    .columna(m8), .peligro(ABUNAI), .colision(cols8), .destroy(detector_colision_8_destroy), .personaje(p8));
  contador contador_1 (
    .diez_en_diez(lim_sup), .decenas(contador_1_decenas), .unidades(contador_1_unidades),
    .generar(or_10_out), .numero(cont));
  or or_10 (or_10_out, d_ff_2_q, d_ff_3_q);
  assign _8 = p8 | m8;  // OR_Gate or_11, 32 bits wide
  detector_colision detector_colision_9 (
    .columna(m9), .peligro(ABUNAI), .colision(cols9), .destroy(detector_colision_9_destroy), .personaje(p9));
  or or_12 (destroy, detector_colision_1_destroy, detector_colision_2_destroy, detector_colision_3_destroy, detector_colision_4_destroy, detector_colision_5_destroy, detector_colision_6_destroy, detector_colision_7_destroy, detector_colision_8_destroy, detector_colision_9_destroy, detector_colision_10_destroy, detector_colision_11_destroy, detector_colision_12_destroy, detector_colision_13_destroy, detector_colision_14_destroy, detector_colision_15_p1, detector_colision_16_p1);
  assign _9 = p9 | m9;  // OR_Gate or_13, 32 bits wide
  detector_colision detector_colision_10 (
    .columna(m10), .peligro(ABUNAI), .colision(cols10), .destroy(detector_colision_10_destroy),
    .personaje(p10));
  segmentos segmentos_2 (.in_1(contador_1_unidades), .c(uc), .d(ud), .b(ub), .a(ua), .g(ug), .f(uf), .e(ue));
  Clock clock_6 (.out(clock_6_out));
  assign _10 = p10 | m10;  // OR_Gate or_14, 32 bits wide
  D_Flip_Flop d_ff_2 (.clk(clock_6_out), .D(colision), .Q(d_ff_2_q));  // open: Qn, preset, en, reset
  assign _11 = p11 | m11;  // OR_Gate or_15, 32 bits wide
  detector_colision detector_colision_11 (
    .columna(m11), .peligro(ABUNAI), .colision(cols11), .destroy(detector_colision_11_destroy),
    .personaje(p11));
  D_Flip_Flop d_ff_3 (.clk(clock_6_out), .D(lim_sup), .Q(d_ff_3_q));  // open: Qn, preset, en, reset
  assign _12 = p12 | m12;  // OR_Gate or_16, 32 bits wide
  detector_colision detector_colision_12 (
    .columna(m12), .peligro(ABUNAI), .colision(cols12), .destroy(detector_colision_12_destroy),
    .personaje(p12));
  assign _13 = p13 | m13;  // OR_Gate or_17, 32 bits wide
  detector_colision detector_colision_13 (
    .columna(m13), .peligro(ABUNAI), .colision(cols13), .destroy(detector_colision_13_destroy),
    .personaje(p13));
  assign _14 = p14 | m14;  // OR_Gate or_18, 32 bits wide
  detector_colision detector_colision_14 (
    .columna(m14), .peligro(ABUNAI), .colision(cols14), .destroy(detector_colision_14_destroy),
    .personaje(p14));
  assign _15 = p15 | m15;  // OR_Gate or_19, 32 bits wide
  // detector_colision detector_colision_15: pin names not known; wires that end beside it: detector_colision_15_p1, ABUNAI, cols15, p15, m15
  // detector_colision detector_colision_16: pin names not known; wires that end beside it: detector_colision_16_p1, ABUNAI, cols16, p16, m16
  assign _16 = p16 | m16;  // OR_Gate or_20, 32 bits wide
  or or_21 (lim_sup, p16[0], p15[0], p14[0], p13[0], p12[0], p11[0], p10[0], p9[0], p8[0], p7[0], p6[0], p5[0], p4[0], p3[0], p2[0], p1[0]);
endmodule

module memoria (
  input  click,
  input  reiniciar,
  input  enable,
  output [31:0] columna1,
  output [31:0] columna2,
  output [31:0] columna3,
  output [31:0] columna4,
  output [31:0] columna5,
  output [31:0] columna6,
  output [31:0] columna7,
  output [31:0] columna8,
  output [31:0] columna9,
  output [31:0] columna10,
  output [31:0] columna11,
  output [31:0] columna12,
  output [31:0] columna13,
  output [31:0] columna14,
  output [31:0] columna15,
  output [31:0] columna16
);

  wire [31:0] generar_barrera_1_columna1, generar_barrera_1_columna2, generar_barrera_1_columna3,
       generar_barrera_1_columna4, generar_barrera_1_columna5, generar_barrera_1_columna6,
       generar_barrera_1_columna7, generar_barrera_1_columna8, generar_barrera_1_columna9,
       generar_barrera_1_columna10, generar_barrera_1_columna11, generar_barrera_1_columna12,
       generar_barrera_1_columna13, generar_barrera_1_columna14, generar_barrera_1_columna15,
       generar_barrera_1_columna16;

  generar_barrera generar_barrera_1 (
    .generar(click), .reset(reiniciar), .activo(enable), .columna1(generar_barrera_1_columna1),
    .columna2(generar_barrera_1_columna2), .columna3(generar_barrera_1_columna3),
    .columna4(generar_barrera_1_columna4), .columna5(generar_barrera_1_columna5),
    .columna6(generar_barrera_1_columna6), .columna7(generar_barrera_1_columna7),
    .columna8(generar_barrera_1_columna8), .columna9(generar_barrera_1_columna9),
    .columna10(generar_barrera_1_columna10), .columna11(generar_barrera_1_columna11),
    .columna12(generar_barrera_1_columna12), .columna13(generar_barrera_1_columna13),
    .columna14(generar_barrera_1_columna14), .columna15(generar_barrera_1_columna15),
    .columna16(generar_barrera_1_columna16));
  columna columna_1 (.reset(reiniciar), .entrada(generar_barrera_1_columna1), .click(click), .salida(columna1));
  columna columna_2 (.reset(reiniciar), .entrada(generar_barrera_1_columna2), .click(click), .salida(columna2));
  columna columna_3 (.reset(reiniciar), .entrada(generar_barrera_1_columna3), .click(click), .salida(columna3));
  columna columna_4 (.reset(reiniciar), .entrada(generar_barrera_1_columna4), .click(click), .salida(columna4));
  columna columna_5 (.reset(reiniciar), .entrada(generar_barrera_1_columna5), .click(click), .salida(columna5));
  columna columna_6 (.reset(reiniciar), .entrada(generar_barrera_1_columna6), .click(click), .salida(columna6));
  columna columna_7 (.reset(reiniciar), .entrada(generar_barrera_1_columna7), .click(click), .salida(columna7));
  columna columna_8 (.reset(reiniciar), .entrada(generar_barrera_1_columna8), .click(click), .salida(columna8));
  columna columna_9 (.reset(reiniciar), .entrada(generar_barrera_1_columna9), .click(click), .salida(columna9));
  columna columna_10 (.reset(reiniciar), .entrada(generar_barrera_1_columna10), .click(click), .salida(columna10));
  columna columna_11 (.reset(reiniciar), .entrada(generar_barrera_1_columna11), .click(click), .salida(columna11));
  columna columna_12 (.reset(reiniciar), .entrada(generar_barrera_1_columna12), .click(click), .salida(columna12));
  columna columna_13 (.reset(reiniciar), .entrada(generar_barrera_1_columna13), .click(click), .salida(columna13));
  columna columna_14 (.reset(reiniciar), .entrada(generar_barrera_1_columna14), .click(click), .salida(columna14));
  columna columna_15 (.reset(reiniciar), .entrada(generar_barrera_1_columna15), .click(click), .salida(columna15));
  columna columna_16 (.reset(reiniciar), .entrada(generar_barrera_1_columna16), .click(click), .salida(columna16));
endmodule

// pix
module pixel_cuadrito (
  input  clk,
  input  abajo,
  input  izq,
  input  der,
  input  reset,
  input  [1:0] dir,
  input  in_7,
  input  ZA_WARUDO,
  output sar,
  output siz,
  output sde
);

  wire multiplexer_1_out;

  Multiplexer #(.select(2)) multiplexer_1 (
    .in0(sar), .in1(abajo), .in2(izq), .in3(der), .out(multiplexer_1_out), .sel(dir));  // open: en
  D_Flip_Flop d_ff_1 (
    .clk(clk), .D(multiplexer_1_out), .Q(sar), .preset(in_7), .en(ZA_WARUDO), .reset(reset));  // open: Qn

  assign sde = sar;
  assign siz = sar;
endmodule
// per
module malla (
  input  [1:0] dir,
  input  ZA_WARUDO,
  input  reset,
  input  inf,
  input  pos,
  output [31:0] c1,
  output [31:0] c2,
  output [31:0] c3,
  output [31:0] c4,
  output [31:0] c5,
  output [31:0] c6,
  output [31:0] c7,
  output [31:0] c8,
  output [31:0] c9,
  output [31:0] c10,
  output [31:0] c11,
  output [31:0] c12,
  output [31:0] c13,
  output [31:0] c14,
  output [31:0] c15,
  output [31:0] c16
);

  wire clk, clock_1_out, demultiplexer_1_out1, demultiplexer_1_out2, demultiplexer_1_out3,
       demultiplexer_1_out4, demultiplexer_1_out5, demultiplexer_1_out6, demultiplexer_1_out7,
       demultiplexer_1_out8, demultiplexer_1_out9, demultiplexer_1_out10, demultiplexer_1_out11,
       demultiplexer_1_out12, demultiplexer_1_out13, demultiplexer_1_out14, pixel_cuadrito_2_sar,
       pixel_cuadrito_3_sar, pixel_cuadrito_4_sar, pixel_cuadrito_5_sar, pixel_cuadrito_6_sar,
       pixel_cuadrito_7_sar, pixel_cuadrito_8_sar, pixel_cuadrito_9_sar, pixel_cuadrito_10_sar,
       pixel_cuadrito_11_sar, pixel_cuadrito_12_sar, pixel_cuadrito_13_sar, pixel_cuadrito_14_sar,
       pixel_cuadrito_15_sar, pixel_cuadrito_16_sar, pixel_cuadrito_17_sar, pixel_cuadrito_18_sar,
       pixel_cuadrito_19_sar, pixel_cuadrito_20_sar, pixel_cuadrito_21_sar, pixel_cuadrito_22_sar,
       pixel_cuadrito_23_sar, pixel_cuadrito_24_sar, pixel_cuadrito_25_sar, pixel_cuadrito_26_sar,
       pixel_cuadrito_27_sar, pixel_cuadrito_28_sar, pixel_cuadrito_29_sar, pixel_cuadrito_30_sar,
       pixel_cuadrito_31_sar, pixel_cuadrito_32_sar, pixel_cuadrito_33_siz, pixel_cuadrito_34_sar,
       pixel_cuadrito_34_siz, pixel_cuadrito_35_sar, pixel_cuadrito_35_siz, pixel_cuadrito_36_sar,
       pixel_cuadrito_36_siz, pixel_cuadrito_37_sar, pixel_cuadrito_37_siz, pixel_cuadrito_38_sar,
       pixel_cuadrito_38_siz, pixel_cuadrito_39_sar, pixel_cuadrito_39_siz, pixel_cuadrito_40_sar,
       pixel_cuadrito_40_siz, pixel_cuadrito_41_sar, pixel_cuadrito_41_siz, pixel_cuadrito_42_sar,
       pixel_cuadrito_42_siz, pixel_cuadrito_43_sar, pixel_cuadrito_43_siz, pixel_cuadrito_44_sar,
       pixel_cuadrito_44_siz, pixel_cuadrito_45_sar, pixel_cuadrito_45_siz, pixel_cuadrito_46_sar,
       pixel_cuadrito_46_siz, pixel_cuadrito_47_sar, pixel_cuadrito_47_siz, pixel_cuadrito_48_sar,
       pixel_cuadrito_48_siz, pixel_cuadrito_49_sar, pixel_cuadrito_49_siz, pixel_cuadrito_50_sar,
       pixel_cuadrito_50_siz, pixel_cuadrito_51_sar, pixel_cuadrito_51_siz, pixel_cuadrito_52_sar,
       pixel_cuadrito_52_siz, pixel_cuadrito_53_sar, pixel_cuadrito_53_siz, pixel_cuadrito_54_sar,
       pixel_cuadrito_54_siz, pixel_cuadrito_55_sar, pixel_cuadrito_55_siz, pixel_cuadrito_56_sar,
       pixel_cuadrito_56_siz, pixel_cuadrito_57_sar, pixel_cuadrito_57_siz, pixel_cuadrito_58_sar,
       pixel_cuadrito_58_siz, pixel_cuadrito_59_sar, pixel_cuadrito_59_siz, pixel_cuadrito_60_sar,
       pixel_cuadrito_60_siz, pixel_cuadrito_61_sar, pixel_cuadrito_61_siz, pixel_cuadrito_62_sar,
       pixel_cuadrito_62_siz, pixel_cuadrito_63_sar, pixel_cuadrito_63_siz, pixel_cuadrito_64_sar,
       pixel_cuadrito_64_siz, pixel_cuadrito_65_siz, pixel_cuadrito_66_sar, pixel_cuadrito_66_siz,
       pixel_cuadrito_67_sar, pixel_cuadrito_67_siz, pixel_cuadrito_68_sar, pixel_cuadrito_68_siz,
       pixel_cuadrito_69_sar, pixel_cuadrito_69_siz, pixel_cuadrito_70_sar, pixel_cuadrito_70_siz,
       pixel_cuadrito_71_sar, pixel_cuadrito_71_siz, pixel_cuadrito_72_sar, pixel_cuadrito_72_siz,
       pixel_cuadrito_73_sar, pixel_cuadrito_73_siz, pixel_cuadrito_74_sar, pixel_cuadrito_74_siz,
       pixel_cuadrito_75_sar, pixel_cuadrito_75_siz, pixel_cuadrito_76_sar, pixel_cuadrito_76_siz,
       pixel_cuadrito_77_sar, pixel_cuadrito_77_siz, pixel_cuadrito_78_sar, pixel_cuadrito_78_siz,
       pixel_cuadrito_79_sar, pixel_cuadrito_79_siz, pixel_cuadrito_80_sar, pixel_cuadrito_80_siz,
       pixel_cuadrito_81_sar, pixel_cuadrito_81_siz, pixel_cuadrito_82_sar, pixel_cuadrito_82_siz,
       pixel_cuadrito_83_sar, pixel_cuadrito_83_siz, pixel_cuadrito_84_sar, pixel_cuadrito_84_siz,
       pixel_cuadrito_85_sar, pixel_cuadrito_85_siz, pixel_cuadrito_86_sar, pixel_cuadrito_86_siz,
       pixel_cuadrito_87_sar, pixel_cuadrito_87_siz, pixel_cuadrito_88_sar, pixel_cuadrito_88_siz,
       pixel_cuadrito_89_sar, pixel_cuadrito_89_siz, pixel_cuadrito_90_sar, pixel_cuadrito_90_siz,
       pixel_cuadrito_91_sar, pixel_cuadrito_91_siz, pixel_cuadrito_92_sar, pixel_cuadrito_92_siz,
       pixel_cuadrito_93_sar, pixel_cuadrito_93_siz, pixel_cuadrito_94_sar, pixel_cuadrito_94_siz,
       pixel_cuadrito_95_sar, pixel_cuadrito_95_siz, pixel_cuadrito_96_sar, pixel_cuadrito_96_siz,
       pixel_cuadrito_97_siz, pixel_cuadrito_98_sar, pixel_cuadrito_98_siz, pixel_cuadrito_99_sar,
       pixel_cuadrito_99_siz, pixel_cuadrito_100_sar, pixel_cuadrito_100_siz, pixel_cuadrito_101_sar,
       pixel_cuadrito_101_siz, pixel_cuadrito_102_sar, pixel_cuadrito_102_siz, pixel_cuadrito_103_sar,
       pixel_cuadrito_103_siz, pixel_cuadrito_104_sar, pixel_cuadrito_104_siz, pixel_cuadrito_105_sar,
       pixel_cuadrito_105_siz, pixel_cuadrito_106_sar, pixel_cuadrito_106_siz, pixel_cuadrito_107_sar,
       pixel_cuadrito_107_siz, pixel_cuadrito_108_sar, pixel_cuadrito_108_siz, pixel_cuadrito_109_sar,
       pixel_cuadrito_109_siz, pixel_cuadrito_110_sar, pixel_cuadrito_110_siz, pixel_cuadrito_111_sar,
       pixel_cuadrito_111_siz, pixel_cuadrito_112_sar, pixel_cuadrito_112_siz, pixel_cuadrito_113_sar,
       pixel_cuadrito_113_siz, pixel_cuadrito_114_sar, pixel_cuadrito_114_siz, pixel_cuadrito_115_sar,
       pixel_cuadrito_115_siz, pixel_cuadrito_116_sar, pixel_cuadrito_116_siz, pixel_cuadrito_117_sar,
       pixel_cuadrito_117_siz, pixel_cuadrito_118_sar, pixel_cuadrito_118_siz, pixel_cuadrito_119_sar,
       pixel_cuadrito_119_siz, pixel_cuadrito_120_sar, pixel_cuadrito_120_siz, pixel_cuadrito_121_sar,
       pixel_cuadrito_121_siz, pixel_cuadrito_122_sar, pixel_cuadrito_122_siz, pixel_cuadrito_123_sar,
       pixel_cuadrito_123_siz, pixel_cuadrito_124_sar, pixel_cuadrito_124_siz, pixel_cuadrito_125_sar,
       pixel_cuadrito_125_siz, pixel_cuadrito_126_sar, pixel_cuadrito_126_siz, pixel_cuadrito_127_sar,
       pixel_cuadrito_127_siz, pixel_cuadrito_128_sar, pixel_cuadrito_128_siz, pixel_cuadrito_129_siz,
       pixel_cuadrito_130_sar, pixel_cuadrito_130_siz, pixel_cuadrito_131_sar, pixel_cuadrito_131_siz,
       pixel_cuadrito_132_sar, pixel_cuadrito_132_siz, pixel_cuadrito_133_sar, pixel_cuadrito_133_siz,
       pixel_cuadrito_134_sar, pixel_cuadrito_134_siz, pixel_cuadrito_135_sar, pixel_cuadrito_135_siz,
       pixel_cuadrito_136_sar, pixel_cuadrito_136_siz, pixel_cuadrito_137_sar, pixel_cuadrito_137_siz,
       pixel_cuadrito_138_sar, pixel_cuadrito_138_siz, pixel_cuadrito_139_sar, pixel_cuadrito_139_siz,
       pixel_cuadrito_140_sar, pixel_cuadrito_140_siz, pixel_cuadrito_141_sar, pixel_cuadrito_141_siz,
       pixel_cuadrito_142_sar, pixel_cuadrito_142_siz, pixel_cuadrito_143_sar, pixel_cuadrito_143_siz,
       pixel_cuadrito_144_sar, pixel_cuadrito_144_siz, pixel_cuadrito_145_sar, pixel_cuadrito_145_siz,
       pixel_cuadrito_146_sar, pixel_cuadrito_146_siz, pixel_cuadrito_147_sar, pixel_cuadrito_147_siz,
       pixel_cuadrito_148_sar, pixel_cuadrito_148_siz, pixel_cuadrito_149_sar, pixel_cuadrito_149_siz,
       pixel_cuadrito_150_sar, pixel_cuadrito_150_siz, pixel_cuadrito_151_sar, pixel_cuadrito_151_siz,
       pixel_cuadrito_152_sar, pixel_cuadrito_152_siz, pixel_cuadrito_153_sar, pixel_cuadrito_153_siz,
       pixel_cuadrito_154_sar, pixel_cuadrito_154_siz, pixel_cuadrito_155_sar, pixel_cuadrito_155_siz,
       pixel_cuadrito_156_sar, pixel_cuadrito_156_siz, pixel_cuadrito_157_sar, pixel_cuadrito_157_siz,
       pixel_cuadrito_158_sar, pixel_cuadrito_158_siz, pixel_cuadrito_159_sar, pixel_cuadrito_159_siz,
       pixel_cuadrito_160_sar, pixel_cuadrito_160_siz, pixel_cuadrito_161_siz, pixel_cuadrito_162_sar,
       pixel_cuadrito_162_siz, pixel_cuadrito_163_sar, pixel_cuadrito_163_siz, pixel_cuadrito_164_sar,
       pixel_cuadrito_164_siz, pixel_cuadrito_165_sar, pixel_cuadrito_165_siz, pixel_cuadrito_166_sar,
       pixel_cuadrito_166_siz, pixel_cuadrito_167_sar, pixel_cuadrito_167_siz, pixel_cuadrito_168_sar,
       pixel_cuadrito_168_siz, pixel_cuadrito_169_sar, pixel_cuadrito_169_siz, pixel_cuadrito_170_sar,
       pixel_cuadrito_170_siz, pixel_cuadrito_171_sar, pixel_cuadrito_171_siz, pixel_cuadrito_172_sar,
       pixel_cuadrito_172_siz, pixel_cuadrito_173_sar, pixel_cuadrito_173_siz, pixel_cuadrito_174_sar,
       pixel_cuadrito_174_siz, pixel_cuadrito_175_sar, pixel_cuadrito_175_siz, pixel_cuadrito_176_sar,
       pixel_cuadrito_176_siz, pixel_cuadrito_177_sar, pixel_cuadrito_177_siz, pixel_cuadrito_178_sar,
       pixel_cuadrito_178_siz, pixel_cuadrito_179_sar, pixel_cuadrito_179_siz, pixel_cuadrito_180_sar,
       pixel_cuadrito_180_siz, pixel_cuadrito_181_sar, pixel_cuadrito_181_siz, pixel_cuadrito_182_sar,
       pixel_cuadrito_182_siz, pixel_cuadrito_183_sar, pixel_cuadrito_183_siz, pixel_cuadrito_184_sar,
       pixel_cuadrito_184_siz, pixel_cuadrito_185_sar, pixel_cuadrito_185_siz, pixel_cuadrito_186_sar,
       pixel_cuadrito_186_siz, pixel_cuadrito_187_sar, pixel_cuadrito_187_siz, pixel_cuadrito_188_sar,
       pixel_cuadrito_188_siz, pixel_cuadrito_189_sar, pixel_cuadrito_189_siz, pixel_cuadrito_190_sar,
       pixel_cuadrito_190_siz, pixel_cuadrito_191_sar, pixel_cuadrito_191_siz, pixel_cuadrito_192_sar,
       pixel_cuadrito_192_siz, pixel_cuadrito_193_siz, pixel_cuadrito_194_sar, pixel_cuadrito_194_siz,
       pixel_cuadrito_195_sar, pixel_cuadrito_195_siz, pixel_cuadrito_196_sar, pixel_cuadrito_196_siz,
       pixel_cuadrito_197_sar, pixel_cuadrito_197_siz, pixel_cuadrito_198_sar, pixel_cuadrito_198_siz,
       pixel_cuadrito_199_sar, pixel_cuadrito_199_siz, pixel_cuadrito_200_sar, pixel_cuadrito_200_siz,
       pixel_cuadrito_201_sar, pixel_cuadrito_201_siz, pixel_cuadrito_202_sar, pixel_cuadrito_202_siz,
       pixel_cuadrito_203_sar, pixel_cuadrito_203_siz, pixel_cuadrito_204_sar, pixel_cuadrito_204_siz,
       pixel_cuadrito_205_sar, pixel_cuadrito_205_siz, pixel_cuadrito_206_sar, pixel_cuadrito_206_siz,
       pixel_cuadrito_207_sar, pixel_cuadrito_207_siz, pixel_cuadrito_208_sar, pixel_cuadrito_208_siz,
       pixel_cuadrito_209_sar, pixel_cuadrito_209_siz, pixel_cuadrito_210_sar, pixel_cuadrito_210_siz,
       pixel_cuadrito_211_sar, pixel_cuadrito_211_siz, pixel_cuadrito_212_sar, pixel_cuadrito_212_siz,
       pixel_cuadrito_213_sar, pixel_cuadrito_213_siz, pixel_cuadrito_214_sar, pixel_cuadrito_214_siz,
       pixel_cuadrito_215_sar, pixel_cuadrito_215_siz, pixel_cuadrito_216_sar, pixel_cuadrito_216_siz,
       pixel_cuadrito_217_sar, pixel_cuadrito_217_siz, pixel_cuadrito_218_sar, pixel_cuadrito_218_siz,
       pixel_cuadrito_219_sar, pixel_cuadrito_219_siz, pixel_cuadrito_220_sar, pixel_cuadrito_220_siz,
       pixel_cuadrito_221_sar, pixel_cuadrito_221_siz, pixel_cuadrito_222_sar, pixel_cuadrito_222_siz,
       pixel_cuadrito_223_sar, pixel_cuadrito_223_siz, pixel_cuadrito_224_sar, pixel_cuadrito_224_siz,
       pixel_cuadrito_225_siz, pixel_cuadrito_226_sar, pixel_cuadrito_226_siz, pixel_cuadrito_227_sar,
       pixel_cuadrito_227_siz, pixel_cuadrito_228_sar, pixel_cuadrito_228_siz, pixel_cuadrito_229_sar,
       pixel_cuadrito_229_siz, pixel_cuadrito_230_sar, pixel_cuadrito_230_siz, pixel_cuadrito_231_sar,
       pixel_cuadrito_231_siz, pixel_cuadrito_232_sar, pixel_cuadrito_232_siz, pixel_cuadrito_233_sar,
       pixel_cuadrito_233_siz, pixel_cuadrito_234_sar, pixel_cuadrito_234_siz, pixel_cuadrito_235_sar,
       pixel_cuadrito_235_siz, pixel_cuadrito_236_sar, pixel_cuadrito_236_siz, pixel_cuadrito_237_sar,
       pixel_cuadrito_237_siz, pixel_cuadrito_238_sar, pixel_cuadrito_238_siz, pixel_cuadrito_239_sar,
       pixel_cuadrito_239_siz, pixel_cuadrito_240_sar, pixel_cuadrito_240_siz, pixel_cuadrito_241_sar,
       pixel_cuadrito_241_siz, pixel_cuadrito_242_sar, pixel_cuadrito_242_siz, pixel_cuadrito_243_sar,
       pixel_cuadrito_243_siz, pixel_cuadrito_244_sar, pixel_cuadrito_244_siz, pixel_cuadrito_245_sar,
       pixel_cuadrito_245_siz, pixel_cuadrito_246_sar, pixel_cuadrito_246_siz, pixel_cuadrito_247_sar,
       pixel_cuadrito_247_siz, pixel_cuadrito_248_sar, pixel_cuadrito_248_siz, pixel_cuadrito_249_sar,
       pixel_cuadrito_249_siz, pixel_cuadrito_250_sar, pixel_cuadrito_250_siz, pixel_cuadrito_251_sar,
       pixel_cuadrito_251_siz, pixel_cuadrito_252_sar, pixel_cuadrito_252_siz, pixel_cuadrito_253_sar,
       pixel_cuadrito_253_siz, pixel_cuadrito_254_sar, pixel_cuadrito_254_siz, pixel_cuadrito_255_sar,
       pixel_cuadrito_255_siz, pixel_cuadrito_256_sar, pixel_cuadrito_256_siz, pixel_cuadrito_257_siz,
       pixel_cuadrito_258_sar, pixel_cuadrito_258_siz, pixel_cuadrito_259_sar, pixel_cuadrito_259_siz,
       pixel_cuadrito_260_sar, pixel_cuadrito_260_siz, pixel_cuadrito_261_sar, pixel_cuadrito_261_siz,
       pixel_cuadrito_262_sar, pixel_cuadrito_262_siz, pixel_cuadrito_263_sar, pixel_cuadrito_263_siz,
       pixel_cuadrito_264_sar, pixel_cuadrito_264_siz, pixel_cuadrito_265_sar, pixel_cuadrito_265_siz,
       pixel_cuadrito_266_sar, pixel_cuadrito_266_siz, pixel_cuadrito_267_sar, pixel_cuadrito_267_siz,
       pixel_cuadrito_268_sar, pixel_cuadrito_268_siz, pixel_cuadrito_269_sar, pixel_cuadrito_269_siz,
       pixel_cuadrito_270_sar, pixel_cuadrito_270_siz, pixel_cuadrito_271_sar, pixel_cuadrito_271_siz,
       pixel_cuadrito_272_sar, pixel_cuadrito_272_siz, pixel_cuadrito_273_sar, pixel_cuadrito_273_siz,
       pixel_cuadrito_274_sar, pixel_cuadrito_274_siz, pixel_cuadrito_275_sar, pixel_cuadrito_275_siz,
       pixel_cuadrito_276_sar, pixel_cuadrito_276_siz, pixel_cuadrito_277_sar, pixel_cuadrito_277_siz,
       pixel_cuadrito_278_sar, pixel_cuadrito_278_siz, pixel_cuadrito_279_sar, pixel_cuadrito_279_siz,
       pixel_cuadrito_280_sar, pixel_cuadrito_280_siz, pixel_cuadrito_281_sar, pixel_cuadrito_281_siz,
       pixel_cuadrito_282_sar, pixel_cuadrito_282_siz, pixel_cuadrito_283_sar, pixel_cuadrito_283_siz,
       pixel_cuadrito_284_sar, pixel_cuadrito_284_siz, pixel_cuadrito_285_sar, pixel_cuadrito_285_siz,
       pixel_cuadrito_286_sar, pixel_cuadrito_286_siz, pixel_cuadrito_287_sar, pixel_cuadrito_287_siz,
       pixel_cuadrito_288_sar, pixel_cuadrito_288_siz, pixel_cuadrito_289_siz, pixel_cuadrito_290_sar,
       pixel_cuadrito_290_siz, pixel_cuadrito_291_sar, pixel_cuadrito_291_siz, pixel_cuadrito_292_sar,
       pixel_cuadrito_292_siz, pixel_cuadrito_293_sar, pixel_cuadrito_293_siz, pixel_cuadrito_294_sar,
       pixel_cuadrito_294_siz, pixel_cuadrito_295_sar, pixel_cuadrito_295_siz, pixel_cuadrito_296_sar,
       pixel_cuadrito_296_siz, pixel_cuadrito_297_sar, pixel_cuadrito_297_siz, pixel_cuadrito_298_sar,
       pixel_cuadrito_298_siz, pixel_cuadrito_299_sar, pixel_cuadrito_299_siz, pixel_cuadrito_300_sar,
       pixel_cuadrito_300_siz, pixel_cuadrito_301_sar, pixel_cuadrito_301_siz, pixel_cuadrito_302_sar,
       pixel_cuadrito_302_siz, pixel_cuadrito_303_sar, pixel_cuadrito_303_siz, pixel_cuadrito_304_sar,
       pixel_cuadrito_304_siz, pixel_cuadrito_305_sar, pixel_cuadrito_305_siz, pixel_cuadrito_306_sar,
       pixel_cuadrito_306_siz, pixel_cuadrito_307_sar, pixel_cuadrito_307_siz, pixel_cuadrito_308_sar,
       pixel_cuadrito_308_siz, pixel_cuadrito_309_sar, pixel_cuadrito_309_siz, pixel_cuadrito_310_sar,
       pixel_cuadrito_310_siz, pixel_cuadrito_311_sar, pixel_cuadrito_311_siz, pixel_cuadrito_312_sar,
       pixel_cuadrito_312_siz, pixel_cuadrito_313_sar, pixel_cuadrito_313_siz, pixel_cuadrito_314_sar,
       pixel_cuadrito_314_siz, pixel_cuadrito_315_sar, pixel_cuadrito_315_siz, pixel_cuadrito_316_sar,
       pixel_cuadrito_316_siz, pixel_cuadrito_317_sar, pixel_cuadrito_317_siz, pixel_cuadrito_318_sar,
       pixel_cuadrito_318_siz, pixel_cuadrito_319_sar, pixel_cuadrito_319_siz, pixel_cuadrito_320_sar,
       pixel_cuadrito_320_siz, pixel_cuadrito_321_siz, pixel_cuadrito_322_sar, pixel_cuadrito_322_siz,
       pixel_cuadrito_323_sar, pixel_cuadrito_323_siz, pixel_cuadrito_324_sar, pixel_cuadrito_324_siz,
       pixel_cuadrito_325_sar, pixel_cuadrito_325_siz, pixel_cuadrito_326_sar, pixel_cuadrito_326_siz,
       pixel_cuadrito_327_sar, pixel_cuadrito_327_siz, pixel_cuadrito_328_sar, pixel_cuadrito_328_siz,
       pixel_cuadrito_329_sar, pixel_cuadrito_329_siz, pixel_cuadrito_330_sar, pixel_cuadrito_330_siz,
       pixel_cuadrito_331_sar, pixel_cuadrito_331_siz, pixel_cuadrito_332_sar, pixel_cuadrito_332_siz,
       pixel_cuadrito_333_sar, pixel_cuadrito_333_siz, pixel_cuadrito_334_sar, pixel_cuadrito_334_siz,
       pixel_cuadrito_335_sar, pixel_cuadrito_335_siz, pixel_cuadrito_336_sar, pixel_cuadrito_336_siz,
       pixel_cuadrito_337_sar, pixel_cuadrito_337_siz, pixel_cuadrito_338_sar, pixel_cuadrito_338_siz,
       pixel_cuadrito_339_sar, pixel_cuadrito_339_siz, pixel_cuadrito_340_sar, pixel_cuadrito_340_siz,
       pixel_cuadrito_341_sar, pixel_cuadrito_341_siz, pixel_cuadrito_342_sar, pixel_cuadrito_342_siz,
       pixel_cuadrito_343_sar, pixel_cuadrito_343_siz, pixel_cuadrito_344_sar, pixel_cuadrito_344_siz,
       pixel_cuadrito_345_sar, pixel_cuadrito_345_siz, pixel_cuadrito_346_sar, pixel_cuadrito_346_siz,
       pixel_cuadrito_347_sar, pixel_cuadrito_347_siz, pixel_cuadrito_348_sar, pixel_cuadrito_348_siz,
       pixel_cuadrito_349_sar, pixel_cuadrito_349_siz, pixel_cuadrito_350_sar, pixel_cuadrito_350_siz,
       pixel_cuadrito_351_sar, pixel_cuadrito_351_siz, pixel_cuadrito_352_sar, pixel_cuadrito_352_siz,
       pixel_cuadrito_353_siz, pixel_cuadrito_354_sar, pixel_cuadrito_354_siz, pixel_cuadrito_355_sar,
       pixel_cuadrito_355_siz, pixel_cuadrito_356_sar, pixel_cuadrito_356_siz, pixel_cuadrito_357_sar,
       pixel_cuadrito_357_siz, pixel_cuadrito_358_sar, pixel_cuadrito_358_siz, pixel_cuadrito_359_sar,
       pixel_cuadrito_359_siz, pixel_cuadrito_360_sar, pixel_cuadrito_360_siz, pixel_cuadrito_361_sar,
       pixel_cuadrito_361_siz, pixel_cuadrito_362_sar, pixel_cuadrito_362_siz, pixel_cuadrito_363_sar,
       pixel_cuadrito_363_siz, pixel_cuadrito_364_sar, pixel_cuadrito_364_siz, pixel_cuadrito_365_sar,
       pixel_cuadrito_365_siz, pixel_cuadrito_366_sar, pixel_cuadrito_366_siz, pixel_cuadrito_367_sar,
       pixel_cuadrito_367_siz, pixel_cuadrito_368_sar, pixel_cuadrito_368_siz, pixel_cuadrito_369_sar,
       pixel_cuadrito_369_siz, pixel_cuadrito_370_sar, pixel_cuadrito_370_siz, pixel_cuadrito_371_sar,
       pixel_cuadrito_371_siz, pixel_cuadrito_372_sar, pixel_cuadrito_372_siz, pixel_cuadrito_373_sar,
       pixel_cuadrito_373_siz, pixel_cuadrito_374_sar, pixel_cuadrito_374_siz, pixel_cuadrito_375_sar,
       pixel_cuadrito_375_siz, pixel_cuadrito_376_sar, pixel_cuadrito_376_siz, pixel_cuadrito_377_sar,
       pixel_cuadrito_377_siz, pixel_cuadrito_378_sar, pixel_cuadrito_378_siz, pixel_cuadrito_379_sar,
       pixel_cuadrito_379_siz, pixel_cuadrito_380_sar, pixel_cuadrito_380_siz, pixel_cuadrito_381_sar,
       pixel_cuadrito_381_siz, pixel_cuadrito_382_sar, pixel_cuadrito_382_siz, pixel_cuadrito_383_sar,
       pixel_cuadrito_383_siz, pixel_cuadrito_384_sar, pixel_cuadrito_384_siz, pixel_cuadrito_385_siz,
       pixel_cuadrito_386_sar, pixel_cuadrito_386_siz, pixel_cuadrito_387_sar, pixel_cuadrito_387_siz,
       pixel_cuadrito_388_sar, pixel_cuadrito_388_siz, pixel_cuadrito_389_sar, pixel_cuadrito_389_siz,
       pixel_cuadrito_390_sar, pixel_cuadrito_390_siz, pixel_cuadrito_391_sar, pixel_cuadrito_391_siz,
       pixel_cuadrito_392_sar, pixel_cuadrito_392_siz, pixel_cuadrito_393_sar, pixel_cuadrito_393_siz,
       pixel_cuadrito_394_sar, pixel_cuadrito_394_siz, pixel_cuadrito_395_sar, pixel_cuadrito_395_siz,
       pixel_cuadrito_396_sar, pixel_cuadrito_396_siz, pixel_cuadrito_397_sar, pixel_cuadrito_397_siz,
       pixel_cuadrito_398_sar, pixel_cuadrito_398_siz, pixel_cuadrito_399_sar, pixel_cuadrito_399_siz,
       pixel_cuadrito_400_sar, pixel_cuadrito_400_siz, pixel_cuadrito_401_sar, pixel_cuadrito_401_siz,
       pixel_cuadrito_402_sar, pixel_cuadrito_402_siz, pixel_cuadrito_403_sar, pixel_cuadrito_403_siz,
       pixel_cuadrito_404_sar, pixel_cuadrito_404_siz, pixel_cuadrito_405_sar, pixel_cuadrito_405_siz,
       pixel_cuadrito_406_sar, pixel_cuadrito_406_siz, pixel_cuadrito_407_sar, pixel_cuadrito_407_siz,
       pixel_cuadrito_408_sar, pixel_cuadrito_408_siz, pixel_cuadrito_409_sar, pixel_cuadrito_409_siz,
       pixel_cuadrito_410_sar, pixel_cuadrito_410_siz, pixel_cuadrito_411_sar, pixel_cuadrito_411_siz,
       pixel_cuadrito_412_sar, pixel_cuadrito_412_siz, pixel_cuadrito_413_sar, pixel_cuadrito_413_siz,
       pixel_cuadrito_414_sar, pixel_cuadrito_414_siz, pixel_cuadrito_415_sar, pixel_cuadrito_415_siz,
       pixel_cuadrito_416_sar, pixel_cuadrito_416_siz, pixel_cuadrito_417_siz, pixel_cuadrito_418_sar,
       pixel_cuadrito_418_siz, pixel_cuadrito_419_sar, pixel_cuadrito_419_siz, pixel_cuadrito_420_sar,
       pixel_cuadrito_420_siz, pixel_cuadrito_421_sar, pixel_cuadrito_421_siz, pixel_cuadrito_422_sar,
       pixel_cuadrito_422_siz, pixel_cuadrito_423_sar, pixel_cuadrito_423_siz, pixel_cuadrito_424_sar,
       pixel_cuadrito_424_siz, pixel_cuadrito_425_sar, pixel_cuadrito_425_siz, pixel_cuadrito_426_sar,
       pixel_cuadrito_426_siz, pixel_cuadrito_427_sar, pixel_cuadrito_427_siz, pixel_cuadrito_428_sar,
       pixel_cuadrito_428_siz, pixel_cuadrito_429_sar, pixel_cuadrito_429_siz, pixel_cuadrito_430_sar,
       pixel_cuadrito_430_siz, pixel_cuadrito_431_sar, pixel_cuadrito_431_siz, pixel_cuadrito_432_sar,
       pixel_cuadrito_432_siz, pixel_cuadrito_433_sar, pixel_cuadrito_433_siz, pixel_cuadrito_434_sar,
       pixel_cuadrito_434_siz, pixel_cuadrito_435_sar, pixel_cuadrito_435_siz, pixel_cuadrito_436_sar,
       pixel_cuadrito_436_siz, pixel_cuadrito_437_sar, pixel_cuadrito_437_siz, pixel_cuadrito_438_sar,
       pixel_cuadrito_438_siz, pixel_cuadrito_439_sar, pixel_cuadrito_439_siz, pixel_cuadrito_440_sar,
       pixel_cuadrito_440_siz, pixel_cuadrito_441_sar, pixel_cuadrito_441_siz, pixel_cuadrito_442_sar,
       pixel_cuadrito_442_siz, pixel_cuadrito_443_sar, pixel_cuadrito_443_siz, pixel_cuadrito_444_sar,
       pixel_cuadrito_444_siz, pixel_cuadrito_445_sar, pixel_cuadrito_445_siz, pixel_cuadrito_446_sar,
       pixel_cuadrito_446_siz, pixel_cuadrito_447_sar, pixel_cuadrito_447_siz, pixel_cuadrito_448_sar,
       pixel_cuadrito_448_siz, pixel_cuadrito_449_siz, pixel_cuadrito_450_sar, pixel_cuadrito_450_siz,
       pixel_cuadrito_451_sar, pixel_cuadrito_451_siz, pixel_cuadrito_452_sar, pixel_cuadrito_452_siz,
       pixel_cuadrito_453_sar, pixel_cuadrito_453_siz, pixel_cuadrito_454_sar, pixel_cuadrito_454_siz,
       pixel_cuadrito_455_sar, pixel_cuadrito_455_siz, pixel_cuadrito_456_sar, pixel_cuadrito_456_siz,
       pixel_cuadrito_457_sar, pixel_cuadrito_457_siz, pixel_cuadrito_458_sar, pixel_cuadrito_458_siz,
       pixel_cuadrito_459_sar, pixel_cuadrito_459_siz, pixel_cuadrito_460_sar, pixel_cuadrito_460_siz,
       pixel_cuadrito_461_sar, pixel_cuadrito_461_siz, pixel_cuadrito_462_sar, pixel_cuadrito_462_siz,
       pixel_cuadrito_463_sar, pixel_cuadrito_463_siz, pixel_cuadrito_464_sar, pixel_cuadrito_464_siz,
       pixel_cuadrito_465_sar, pixel_cuadrito_465_siz, pixel_cuadrito_466_sar, pixel_cuadrito_466_siz,
       pixel_cuadrito_467_sar, pixel_cuadrito_467_siz, pixel_cuadrito_468_sar, pixel_cuadrito_468_siz,
       pixel_cuadrito_469_sar, pixel_cuadrito_469_siz, pixel_cuadrito_470_sar, pixel_cuadrito_470_siz,
       pixel_cuadrito_471_sar, pixel_cuadrito_471_siz, pixel_cuadrito_472_sar, pixel_cuadrito_472_siz,
       pixel_cuadrito_473_sar, pixel_cuadrito_473_siz, pixel_cuadrito_474_sar, pixel_cuadrito_474_siz,
       pixel_cuadrito_475_sar, pixel_cuadrito_475_siz, pixel_cuadrito_476_sar, pixel_cuadrito_476_siz,
       pixel_cuadrito_477_sar, pixel_cuadrito_477_siz, pixel_cuadrito_478_sar, pixel_cuadrito_478_siz,
       pixel_cuadrito_479_sar, pixel_cuadrito_479_siz, pixel_cuadrito_480_sar, pixel_cuadrito_480_siz,
       pixel_cuadrito_481_siz, pixel_cuadrito_482_sar, pixel_cuadrito_482_siz, pixel_cuadrito_483_sar,
       pixel_cuadrito_483_siz, pixel_cuadrito_484_sar, pixel_cuadrito_484_siz, pixel_cuadrito_485_sar,
       pixel_cuadrito_485_siz, pixel_cuadrito_486_sar, pixel_cuadrito_486_siz, pixel_cuadrito_487_sar,
       pixel_cuadrito_487_siz, pixel_cuadrito_488_sar, pixel_cuadrito_488_siz, pixel_cuadrito_489_sar,
       pixel_cuadrito_489_siz, pixel_cuadrito_490_sar, pixel_cuadrito_490_siz, pixel_cuadrito_491_sar,
       pixel_cuadrito_491_siz, pixel_cuadrito_492_sar, pixel_cuadrito_492_siz, pixel_cuadrito_493_sar,
       pixel_cuadrito_493_siz, pixel_cuadrito_494_sar, pixel_cuadrito_494_siz, pixel_cuadrito_495_sar,
       pixel_cuadrito_495_siz, pixel_cuadrito_496_sar, pixel_cuadrito_496_siz, pixel_cuadrito_497_sar,
       pixel_cuadrito_497_siz, pixel_cuadrito_498_sar, pixel_cuadrito_498_siz, pixel_cuadrito_499_sar,
       pixel_cuadrito_499_siz, pixel_cuadrito_500_sar, pixel_cuadrito_500_siz, pixel_cuadrito_501_sar,
       pixel_cuadrito_501_siz, pixel_cuadrito_502_sar, pixel_cuadrito_502_siz, pixel_cuadrito_503_sar,
       pixel_cuadrito_503_siz, pixel_cuadrito_504_sar, pixel_cuadrito_504_siz, pixel_cuadrito_505_sar,
       pixel_cuadrito_505_siz, pixel_cuadrito_506_sar, pixel_cuadrito_506_siz, pixel_cuadrito_507_sar,
       pixel_cuadrito_507_siz, pixel_cuadrito_508_sar, pixel_cuadrito_508_siz, pixel_cuadrito_509_sar,
       pixel_cuadrito_509_siz, pixel_cuadrito_510_sar, pixel_cuadrito_510_siz, pixel_cuadrito_511_sar,
       pixel_cuadrito_511_siz, pixel_cuadrito_512_sar, pixel_cuadrito_512_siz, s1os2, s2os3, s3os4, s4os5,
       s5os6, s6os7, s7os8, s8os9, s9os10, s10os11, s11os12, s12os13, s13os14, s14os15, start16;
  wire [3:0] random_1_out;

  pixel_cuadrito pixel_cuadrito_1 (
    .clk(clk), .abajo(pixel_cuadrito_2_sar), .izq(c16[31]), .der(pixel_cuadrito_33_siz), .dir(dir),
    .sde(c1[31]), .ZA_WARUDO(ZA_WARUDO), .reset(reset));  // open: sar, siz, in_7
  pixel_cuadrito pixel_cuadrito_2 (
    .clk(clk), .abajo(pixel_cuadrito_3_sar), .izq(c16[30]), .der(pixel_cuadrito_34_siz), .dir(dir),
    .sar(pixel_cuadrito_2_sar), .sde(c1[30]), .ZA_WARUDO(ZA_WARUDO), .reset(reset));  // open: siz, in_7
  pixel_cuadrito pixel_cuadrito_3 (
    .clk(clk), .abajo(pixel_cuadrito_4_sar), .izq(c16[29]), .der(pixel_cuadrito_35_siz), .dir(dir),
    .sar(pixel_cuadrito_3_sar), .sde(c1[29]), .ZA_WARUDO(ZA_WARUDO), .reset(reset));  // open: siz, in_7
  pixel_cuadrito pixel_cuadrito_4 (
    .clk(clk), .abajo(pixel_cuadrito_5_sar), .izq(c16[28]), .der(pixel_cuadrito_36_siz), .dir(dir),
    .sar(pixel_cuadrito_4_sar), .sde(c1[28]), .ZA_WARUDO(ZA_WARUDO), .reset(reset));  // open: siz, in_7
  pixel_cuadrito pixel_cuadrito_5 (
    .clk(clk), .abajo(pixel_cuadrito_6_sar), .izq(c16[27]), .der(pixel_cuadrito_37_siz), .dir(dir),
    .sar(pixel_cuadrito_5_sar), .sde(c1[27]), .ZA_WARUDO(ZA_WARUDO), .reset(reset));  // open: siz, in_7
  pixel_cuadrito pixel_cuadrito_6 (
    .clk(clk), .abajo(pixel_cuadrito_7_sar), .izq(c16[26]), .der(pixel_cuadrito_38_siz), .dir(dir),
    .sar(pixel_cuadrito_6_sar), .sde(c1[26]), .ZA_WARUDO(ZA_WARUDO), .reset(reset));  // open: siz, in_7
  pixel_cuadrito pixel_cuadrito_7 (
    .clk(clk), .abajo(pixel_cuadrito_8_sar), .izq(c16[25]), .der(pixel_cuadrito_39_siz), .dir(dir),
    .sar(pixel_cuadrito_7_sar), .sde(c1[25]), .ZA_WARUDO(ZA_WARUDO), .reset(reset));  // open: siz, in_7
  pixel_cuadrito pixel_cuadrito_8 (
    .clk(clk), .abajo(pixel_cuadrito_9_sar), .izq(c16[24]), .der(pixel_cuadrito_40_siz), .dir(dir),
    .sar(pixel_cuadrito_8_sar), .sde(c1[24]), .ZA_WARUDO(ZA_WARUDO), .reset(reset));  // open: siz, in_7
  pixel_cuadrito pixel_cuadrito_9 (
    .clk(clk), .abajo(pixel_cuadrito_10_sar), .izq(c16[23]), .der(pixel_cuadrito_41_siz), .dir(dir),
    .sar(pixel_cuadrito_9_sar), .sde(c1[23]), .ZA_WARUDO(ZA_WARUDO), .reset(reset));  // open: siz, in_7
  pixel_cuadrito pixel_cuadrito_10 (
    .clk(clk), .abajo(pixel_cuadrito_11_sar), .izq(c16[22]), .der(pixel_cuadrito_42_siz), .dir(dir),
    .sar(pixel_cuadrito_10_sar), .sde(c1[22]), .ZA_WARUDO(ZA_WARUDO), .reset(reset));  // open: siz, in_7
  pixel_cuadrito pixel_cuadrito_11 (
    .clk(clk), .abajo(pixel_cuadrito_12_sar), .izq(c16[21]), .der(pixel_cuadrito_43_siz), .dir(dir),
    .sar(pixel_cuadrito_11_sar), .sde(c1[21]), .ZA_WARUDO(ZA_WARUDO), .reset(reset));  // open: siz, in_7
  pixel_cuadrito pixel_cuadrito_12 (
    .clk(clk), .abajo(pixel_cuadrito_13_sar), .izq(c16[20]), .der(pixel_cuadrito_44_siz), .dir(dir),
    .sar(pixel_cuadrito_12_sar), .sde(c1[20]), .ZA_WARUDO(ZA_WARUDO), .reset(reset));  // open: siz, in_7
  pixel_cuadrito pixel_cuadrito_13 (
    .clk(clk), .abajo(pixel_cuadrito_14_sar), .izq(c16[19]), .der(pixel_cuadrito_45_siz), .dir(dir),
    .sar(pixel_cuadrito_13_sar), .sde(c1[19]), .ZA_WARUDO(ZA_WARUDO), .reset(reset));  // open: siz, in_7
  pixel_cuadrito pixel_cuadrito_14 (
    .clk(clk), .abajo(pixel_cuadrito_15_sar), .izq(c16[18]), .der(pixel_cuadrito_46_siz), .dir(dir),
    .sar(pixel_cuadrito_14_sar), .sde(c1[18]), .ZA_WARUDO(ZA_WARUDO), .reset(reset));  // open: siz, in_7
  pixel_cuadrito pixel_cuadrito_15 (
    .clk(clk), .abajo(pixel_cuadrito_16_sar), .izq(c16[17]), .der(pixel_cuadrito_47_siz), .dir(dir),
    .sar(pixel_cuadrito_15_sar), .sde(c1[17]), .ZA_WARUDO(ZA_WARUDO), .reset(reset));  // open: siz, in_7
  pixel_cuadrito pixel_cuadrito_16 (
    .clk(clk), .abajo(pixel_cuadrito_17_sar), .izq(c16[16]), .der(pixel_cuadrito_48_siz), .dir(dir),
    .sar(pixel_cuadrito_16_sar), .sde(c1[16]), .ZA_WARUDO(ZA_WARUDO), .reset(reset));  // open: siz, in_7
  pixel_cuadrito pixel_cuadrito_17 (
    .clk(clk), .abajo(pixel_cuadrito_18_sar), .izq(c16[15]), .der(pixel_cuadrito_49_siz), .dir(dir),
    .sar(pixel_cuadrito_17_sar), .sde(c1[15]), .ZA_WARUDO(ZA_WARUDO), .reset(reset));  // open: siz, in_7
  pixel_cuadrito pixel_cuadrito_18 (
    .clk(clk), .abajo(pixel_cuadrito_19_sar), .izq(c16[14]), .der(pixel_cuadrito_50_siz), .dir(dir),
    .sar(pixel_cuadrito_18_sar), .sde(c1[14]), .ZA_WARUDO(ZA_WARUDO), .reset(reset));  // open: siz, in_7
  pixel_cuadrito pixel_cuadrito_19 (
    .clk(clk), .abajo(pixel_cuadrito_20_sar), .izq(c16[13]), .der(pixel_cuadrito_51_siz), .dir(dir),
    .sar(pixel_cuadrito_19_sar), .sde(c1[13]), .ZA_WARUDO(ZA_WARUDO), .reset(reset));  // open: siz, in_7
  pixel_cuadrito pixel_cuadrito_20 (
    .clk(clk), .abajo(pixel_cuadrito_21_sar), .izq(c16[12]), .der(pixel_cuadrito_52_siz), .dir(dir),
    .sar(pixel_cuadrito_20_sar), .sde(c1[12]), .ZA_WARUDO(ZA_WARUDO), .reset(reset));  // open: siz, in_7
  pixel_cuadrito pixel_cuadrito_21 (
    .clk(clk), .abajo(pixel_cuadrito_22_sar), .izq(c16[11]), .der(pixel_cuadrito_53_siz), .dir(dir),
    .sar(pixel_cuadrito_21_sar), .sde(c1[11]), .ZA_WARUDO(ZA_WARUDO), .reset(reset));  // open: siz, in_7
  pixel_cuadrito pixel_cuadrito_22 (
    .clk(clk), .abajo(pixel_cuadrito_23_sar), .izq(c16[10]), .der(pixel_cuadrito_54_siz), .dir(dir),
    .sar(pixel_cuadrito_22_sar), .sde(c1[10]), .ZA_WARUDO(ZA_WARUDO), .reset(reset));  // open: siz, in_7
  pixel_cuadrito pixel_cuadrito_23 (
    .clk(clk), .abajo(pixel_cuadrito_24_sar), .izq(c16[9]), .der(pixel_cuadrito_55_siz), .dir(dir),
    .sar(pixel_cuadrito_23_sar), .sde(c1[9]), .ZA_WARUDO(ZA_WARUDO), .reset(reset));  // open: siz, in_7
  pixel_cuadrito pixel_cuadrito_24 (
    .clk(clk), .abajo(pixel_cuadrito_25_sar), .izq(c16[8]), .der(pixel_cuadrito_56_siz), .dir(dir),
    .sar(pixel_cuadrito_24_sar), .sde(c1[8]), .ZA_WARUDO(ZA_WARUDO), .reset(reset));  // open: siz, in_7
  pixel_cuadrito pixel_cuadrito_25 (
    .clk(clk), .abajo(pixel_cuadrito_26_sar), .izq(c16[7]), .der(pixel_cuadrito_57_siz), .dir(dir),
    .sar(pixel_cuadrito_25_sar), .sde(c1[7]), .ZA_WARUDO(ZA_WARUDO), .reset(reset));  // open: siz, in_7
  pixel_cuadrito pixel_cuadrito_26 (
    .clk(clk), .abajo(pixel_cuadrito_27_sar), .izq(c16[6]), .der(pixel_cuadrito_58_siz), .dir(dir),
    .sar(pixel_cuadrito_26_sar), .sde(c1[6]), .ZA_WARUDO(ZA_WARUDO), .reset(reset));  // open: siz, in_7
  pixel_cuadrito pixel_cuadrito_27 (
    .clk(clk), .abajo(pixel_cuadrito_28_sar), .izq(c16[5]), .der(pixel_cuadrito_59_siz), .dir(dir),
    .sar(pixel_cuadrito_27_sar), .sde(c1[5]), .ZA_WARUDO(ZA_WARUDO), .reset(reset));  // open: siz, in_7
  pixel_cuadrito pixel_cuadrito_28 (
    .clk(clk), .abajo(pixel_cuadrito_29_sar), .izq(c16[4]), .der(pixel_cuadrito_60_siz), .dir(dir),
    .sar(pixel_cuadrito_28_sar), .sde(c1[4]), .ZA_WARUDO(ZA_WARUDO), .reset(reset));  // open: siz, in_7
  pixel_cuadrito pixel_cuadrito_29 (
    .clk(clk), .abajo(pixel_cuadrito_30_sar), .izq(c16[3]), .der(pixel_cuadrito_61_siz), .dir(dir),
    .sar(pixel_cuadrito_29_sar), .sde(c1[3]), .ZA_WARUDO(ZA_WARUDO), .reset(reset));  // open: siz, in_7
  pixel_cuadrito pixel_cuadrito_30 (
    .clk(clk), .abajo(pixel_cuadrito_31_sar), .izq(c16[2]), .der(pixel_cuadrito_62_siz), .dir(dir),
    .sar(pixel_cuadrito_30_sar), .sde(c1[2]), .in_7(s1os2), .ZA_WARUDO(ZA_WARUDO), .reset(reset));  // open: siz
  pixel_cuadrito pixel_cuadrito_31 (
    .clk(clk), .abajo(pixel_cuadrito_32_sar), .izq(c16[1]), .der(pixel_cuadrito_63_siz), .dir(dir),
    .sar(pixel_cuadrito_31_sar), .sde(c1[1]), .in_7(s1os2), .ZA_WARUDO(ZA_WARUDO), .reset(reset));  // open: siz
  pixel_cuadrito pixel_cuadrito_32 (
    .clk(clk), .abajo(c1[31]), .izq(c16[0]), .der(pixel_cuadrito_64_siz), .dir(dir),
    .sar(pixel_cuadrito_32_sar), .sde(c1[0]), .ZA_WARUDO(ZA_WARUDO), .reset(reset));  // open: siz, in_7
  pixel_cuadrito pixel_cuadrito_33 (
    .clk(clk), .abajo(pixel_cuadrito_34_sar), .izq(c1[31]), .der(pixel_cuadrito_65_siz), .dir(dir),
    .siz(pixel_cuadrito_33_siz), .sde(c2[31]), .ZA_WARUDO(ZA_WARUDO), .reset(reset));  // open: sar, in_7
  pixel_cuadrito pixel_cuadrito_34 (
    .clk(clk), .abajo(pixel_cuadrito_35_sar), .izq(c1[30]), .der(pixel_cuadrito_66_siz), .dir(dir),
    .sar(pixel_cuadrito_34_sar), .siz(pixel_cuadrito_34_siz), .sde(c2[30]), .ZA_WARUDO(ZA_WARUDO),
    .reset(reset));  // open: in_7
  pixel_cuadrito pixel_cuadrito_35 (
    .clk(clk), .abajo(pixel_cuadrito_36_sar), .izq(c1[29]), .der(pixel_cuadrito_67_siz), .dir(dir),
    .sar(pixel_cuadrito_35_sar), .siz(pixel_cuadrito_35_siz), .sde(c2[29]), .ZA_WARUDO(ZA_WARUDO),
    .reset(reset));  // open: in_7
  pixel_cuadrito pixel_cuadrito_36 (
    .clk(clk), .abajo(pixel_cuadrito_37_sar), .izq(c1[28]), .der(pixel_cuadrito_68_siz), .dir(dir),
    .sar(pixel_cuadrito_36_sar), .siz(pixel_cuadrito_36_siz), .sde(c2[28]), .ZA_WARUDO(ZA_WARUDO),
    .reset(reset));  // open: in_7
  pixel_cuadrito pixel_cuadrito_37 (
    .clk(clk), .abajo(pixel_cuadrito_38_sar), .izq(c1[27]), .der(pixel_cuadrito_69_siz), .dir(dir),
    .sar(pixel_cuadrito_37_sar), .siz(pixel_cuadrito_37_siz), .sde(c2[27]), .ZA_WARUDO(ZA_WARUDO),
    .reset(reset));  // open: in_7
  pixel_cuadrito pixel_cuadrito_38 (
    .clk(clk), .abajo(pixel_cuadrito_39_sar), .izq(c1[26]), .der(pixel_cuadrito_70_siz), .dir(dir),
    .sar(pixel_cuadrito_38_sar), .siz(pixel_cuadrito_38_siz), .sde(c2[26]), .ZA_WARUDO(ZA_WARUDO),
    .reset(reset));  // open: in_7
  pixel_cuadrito pixel_cuadrito_39 (
    .clk(clk), .abajo(pixel_cuadrito_40_sar), .izq(c1[25]), .der(pixel_cuadrito_71_siz), .dir(dir),
    .sar(pixel_cuadrito_39_sar), .siz(pixel_cuadrito_39_siz), .sde(c2[25]), .ZA_WARUDO(ZA_WARUDO),
    .reset(reset));  // open: in_7
  pixel_cuadrito pixel_cuadrito_40 (
    .clk(clk), .abajo(pixel_cuadrito_41_sar), .izq(c1[24]), .der(pixel_cuadrito_72_siz), .dir(dir),
    .sar(pixel_cuadrito_40_sar), .siz(pixel_cuadrito_40_siz), .sde(c2[24]), .ZA_WARUDO(ZA_WARUDO),
    .reset(reset));  // open: in_7
  pixel_cuadrito pixel_cuadrito_41 (
    .clk(clk), .abajo(pixel_cuadrito_42_sar), .izq(c1[23]), .der(pixel_cuadrito_73_siz), .dir(dir),
    .sar(pixel_cuadrito_41_sar), .siz(pixel_cuadrito_41_siz), .sde(c2[23]), .ZA_WARUDO(ZA_WARUDO),
    .reset(reset));  // open: in_7
  pixel_cuadrito pixel_cuadrito_42 (
    .clk(clk), .abajo(pixel_cuadrito_43_sar), .izq(c1[22]), .der(pixel_cuadrito_74_siz), .dir(dir),
    .sar(pixel_cuadrito_42_sar), .siz(pixel_cuadrito_42_siz), .sde(c2[22]), .ZA_WARUDO(ZA_WARUDO),
    .reset(reset));  // open: in_7
  pixel_cuadrito pixel_cuadrito_43 (
    .clk(clk), .abajo(pixel_cuadrito_44_sar), .izq(c1[21]), .der(pixel_cuadrito_75_siz), .dir(dir),
    .sar(pixel_cuadrito_43_sar), .siz(pixel_cuadrito_43_siz), .sde(c2[21]), .ZA_WARUDO(ZA_WARUDO),
    .reset(reset));  // open: in_7
  pixel_cuadrito pixel_cuadrito_44 (
    .clk(clk), .abajo(pixel_cuadrito_45_sar), .izq(c1[20]), .der(pixel_cuadrito_76_siz), .dir(dir),
    .sar(pixel_cuadrito_44_sar), .siz(pixel_cuadrito_44_siz), .sde(c2[20]), .ZA_WARUDO(ZA_WARUDO),
    .reset(reset));  // open: in_7
  pixel_cuadrito pixel_cuadrito_45 (
    .clk(clk), .abajo(pixel_cuadrito_46_sar), .izq(c1[19]), .der(pixel_cuadrito_77_siz), .dir(dir),
    .sar(pixel_cuadrito_45_sar), .siz(pixel_cuadrito_45_siz), .sde(c2[19]), .ZA_WARUDO(ZA_WARUDO),
    .reset(reset));  // open: in_7
  pixel_cuadrito pixel_cuadrito_46 (
    .clk(clk), .abajo(pixel_cuadrito_47_sar), .izq(c1[18]), .der(pixel_cuadrito_78_siz), .dir(dir),
    .sar(pixel_cuadrito_46_sar), .siz(pixel_cuadrito_46_siz), .sde(c2[18]), .ZA_WARUDO(ZA_WARUDO),
    .reset(reset));  // open: in_7
  pixel_cuadrito pixel_cuadrito_47 (
    .clk(clk), .abajo(pixel_cuadrito_48_sar), .izq(c1[17]), .der(pixel_cuadrito_79_siz), .dir(dir),
    .sar(pixel_cuadrito_47_sar), .siz(pixel_cuadrito_47_siz), .sde(c2[17]), .ZA_WARUDO(ZA_WARUDO),
    .reset(reset));  // open: in_7
  pixel_cuadrito pixel_cuadrito_48 (
    .clk(clk), .abajo(pixel_cuadrito_49_sar), .izq(c1[16]), .der(pixel_cuadrito_80_siz), .dir(dir),
    .sar(pixel_cuadrito_48_sar), .siz(pixel_cuadrito_48_siz), .sde(c2[16]), .ZA_WARUDO(ZA_WARUDO),
    .reset(reset));  // open: in_7
  pixel_cuadrito pixel_cuadrito_49 (
    .clk(clk), .abajo(pixel_cuadrito_50_sar), .izq(c1[15]), .der(pixel_cuadrito_81_siz), .dir(dir),
    .sar(pixel_cuadrito_49_sar), .siz(pixel_cuadrito_49_siz), .sde(c2[15]), .ZA_WARUDO(ZA_WARUDO),
    .reset(reset));  // open: in_7
  pixel_cuadrito pixel_cuadrito_50 (
    .clk(clk), .abajo(pixel_cuadrito_51_sar), .izq(c1[14]), .der(pixel_cuadrito_82_siz), .dir(dir),
    .sar(pixel_cuadrito_50_sar), .siz(pixel_cuadrito_50_siz), .sde(c2[14]), .ZA_WARUDO(ZA_WARUDO),
    .reset(reset));  // open: in_7
  pixel_cuadrito pixel_cuadrito_51 (
    .clk(clk), .abajo(pixel_cuadrito_52_sar), .izq(c1[13]), .der(pixel_cuadrito_83_siz), .dir(dir),
    .sar(pixel_cuadrito_51_sar), .siz(pixel_cuadrito_51_siz), .sde(c2[13]), .ZA_WARUDO(ZA_WARUDO),
    .reset(reset));  // open: in_7
  pixel_cuadrito pixel_cuadrito_52 (
    .clk(clk), .abajo(pixel_cuadrito_53_sar), .izq(c1[12]), .der(pixel_cuadrito_84_siz), .dir(dir),
    .sar(pixel_cuadrito_52_sar), .siz(pixel_cuadrito_52_siz), .sde(c2[12]), .ZA_WARUDO(ZA_WARUDO),
    .reset(reset));  // open: in_7
  pixel_cuadrito pixel_cuadrito_53 (
    .clk(clk), .abajo(pixel_cuadrito_54_sar), .izq(c1[11]), .der(pixel_cuadrito_85_siz), .dir(dir),
    .sar(pixel_cuadrito_53_sar), .siz(pixel_cuadrito_53_siz), .sde(c2[11]), .ZA_WARUDO(ZA_WARUDO),
    .reset(reset));  // open: in_7
  pixel_cuadrito pixel_cuadrito_54 (
    .clk(clk), .abajo(pixel_cuadrito_55_sar), .izq(c1[10]), .der(pixel_cuadrito_86_siz), .dir(dir),
    .sar(pixel_cuadrito_54_sar), .siz(pixel_cuadrito_54_siz), .sde(c2[10]), .ZA_WARUDO(ZA_WARUDO),
    .reset(reset));  // open: in_7
  pixel_cuadrito pixel_cuadrito_55 (
    .clk(clk), .abajo(pixel_cuadrito_56_sar), .izq(c1[9]), .der(pixel_cuadrito_87_siz), .dir(dir),
    .sar(pixel_cuadrito_55_sar), .siz(pixel_cuadrito_55_siz), .sde(c2[9]), .ZA_WARUDO(ZA_WARUDO),
    .reset(reset));  // open: in_7
  pixel_cuadrito pixel_cuadrito_56 (
    .clk(clk), .abajo(pixel_cuadrito_57_sar), .izq(c1[8]), .der(pixel_cuadrito_88_siz), .dir(dir),
    .sar(pixel_cuadrito_56_sar), .siz(pixel_cuadrito_56_siz), .sde(c2[8]), .ZA_WARUDO(ZA_WARUDO),
    .reset(reset));  // open: in_7
  pixel_cuadrito pixel_cuadrito_57 (
    .clk(clk), .abajo(pixel_cuadrito_58_sar), .izq(c1[7]), .der(pixel_cuadrito_89_siz), .dir(dir),
    .sar(pixel_cuadrito_57_sar), .siz(pixel_cuadrito_57_siz), .sde(c2[7]), .ZA_WARUDO(ZA_WARUDO),
    .reset(reset));  // open: in_7
  pixel_cuadrito pixel_cuadrito_58 (
    .clk(clk), .abajo(pixel_cuadrito_59_sar), .izq(c1[6]), .der(pixel_cuadrito_90_siz), .dir(dir),
    .sar(pixel_cuadrito_58_sar), .siz(pixel_cuadrito_58_siz), .sde(c2[6]), .ZA_WARUDO(ZA_WARUDO),
    .reset(reset));  // open: in_7
  pixel_cuadrito pixel_cuadrito_59 (
    .clk(clk), .abajo(pixel_cuadrito_60_sar), .izq(c1[5]), .der(pixel_cuadrito_91_siz), .dir(dir),
    .sar(pixel_cuadrito_59_sar), .siz(pixel_cuadrito_59_siz), .sde(c2[5]), .ZA_WARUDO(ZA_WARUDO),
    .reset(reset));  // open: in_7
  pixel_cuadrito pixel_cuadrito_60 (
    .clk(clk), .abajo(pixel_cuadrito_61_sar), .izq(c1[4]), .der(pixel_cuadrito_92_siz), .dir(dir),
    .sar(pixel_cuadrito_60_sar), .siz(pixel_cuadrito_60_siz), .sde(c2[4]), .ZA_WARUDO(ZA_WARUDO),
    .reset(reset));  // open: in_7
  pixel_cuadrito pixel_cuadrito_61 (
    .clk(clk), .abajo(pixel_cuadrito_62_sar), .izq(c1[3]), .der(pixel_cuadrito_93_siz), .dir(dir),
    .sar(pixel_cuadrito_61_sar), .siz(pixel_cuadrito_61_siz), .sde(c2[3]), .ZA_WARUDO(ZA_WARUDO),
    .reset(reset));  // open: in_7
  pixel_cuadrito pixel_cuadrito_62 (
    .clk(clk), .abajo(pixel_cuadrito_63_sar), .izq(c1[2]), .der(pixel_cuadrito_94_siz), .dir(dir),
    .sar(pixel_cuadrito_62_sar), .siz(pixel_cuadrito_62_siz), .sde(c2[2]), .in_7(s1os2),
    .ZA_WARUDO(ZA_WARUDO), .reset(reset));
  pixel_cuadrito pixel_cuadrito_63 (
    .clk(clk), .abajo(pixel_cuadrito_64_sar), .izq(c1[1]), .der(pixel_cuadrito_95_siz), .dir(dir),
    .sar(pixel_cuadrito_63_sar), .siz(pixel_cuadrito_63_siz), .sde(c2[1]), .in_7(s1os2),
    .ZA_WARUDO(ZA_WARUDO), .reset(reset));
  pixel_cuadrito pixel_cuadrito_64 (
    .clk(clk), .abajo(c2[31]), .izq(c1[0]), .der(pixel_cuadrito_96_siz), .dir(dir),
    .sar(pixel_cuadrito_64_sar), .siz(pixel_cuadrito_64_siz), .sde(c2[0]), .ZA_WARUDO(ZA_WARUDO),
    .reset(reset));  // open: in_7
  pixel_cuadrito pixel_cuadrito_65 (
    .clk(clk), .abajo(pixel_cuadrito_66_sar), .izq(c2[31]), .der(pixel_cuadrito_97_siz), .dir(dir),
    .siz(pixel_cuadrito_65_siz), .sde(c3[31]), .ZA_WARUDO(ZA_WARUDO), .reset(reset));  // open: sar, in_7
  pixel_cuadrito pixel_cuadrito_66 (
    .clk(clk), .abajo(pixel_cuadrito_67_sar), .izq(c2[30]), .der(pixel_cuadrito_98_siz), .dir(dir),
    .sar(pixel_cuadrito_66_sar), .siz(pixel_cuadrito_66_siz), .sde(c3[30]), .ZA_WARUDO(ZA_WARUDO),
    .reset(reset));  // open: in_7
  pixel_cuadrito pixel_cuadrito_67 (
    .clk(clk), .abajo(pixel_cuadrito_68_sar), .izq(c2[29]), .der(pixel_cuadrito_99_siz), .dir(dir),
    .sar(pixel_cuadrito_67_sar), .siz(pixel_cuadrito_67_siz), .sde(c3[29]), .ZA_WARUDO(ZA_WARUDO),
    .reset(reset));  // open: in_7
  pixel_cuadrito pixel_cuadrito_68 (
    .clk(clk), .abajo(pixel_cuadrito_69_sar), .izq(c2[28]), .der(pixel_cuadrito_100_siz), .dir(dir),
    .sar(pixel_cuadrito_68_sar), .siz(pixel_cuadrito_68_siz), .sde(c3[28]), .ZA_WARUDO(ZA_WARUDO),
    .reset(reset));  // open: in_7
  pixel_cuadrito pixel_cuadrito_69 (
    .clk(clk), .abajo(pixel_cuadrito_70_sar), .izq(c2[27]), .der(pixel_cuadrito_101_siz), .dir(dir),
    .sar(pixel_cuadrito_69_sar), .siz(pixel_cuadrito_69_siz), .sde(c3[27]), .ZA_WARUDO(ZA_WARUDO),
    .reset(reset));  // open: in_7
  pixel_cuadrito pixel_cuadrito_70 (
    .clk(clk), .abajo(pixel_cuadrito_71_sar), .izq(c2[26]), .der(pixel_cuadrito_102_siz), .dir(dir),
    .sar(pixel_cuadrito_70_sar), .siz(pixel_cuadrito_70_siz), .sde(c3[26]), .ZA_WARUDO(ZA_WARUDO),
    .reset(reset));  // open: in_7
  pixel_cuadrito pixel_cuadrito_71 (
    .clk(clk), .abajo(pixel_cuadrito_72_sar), .izq(c2[25]), .der(pixel_cuadrito_103_siz), .dir(dir),
    .sar(pixel_cuadrito_71_sar), .siz(pixel_cuadrito_71_siz), .sde(c3[25]), .ZA_WARUDO(ZA_WARUDO),
    .reset(reset));  // open: in_7
  pixel_cuadrito pixel_cuadrito_72 (
    .clk(clk), .abajo(pixel_cuadrito_73_sar), .izq(c2[24]), .der(pixel_cuadrito_104_siz), .dir(dir),
    .sar(pixel_cuadrito_72_sar), .siz(pixel_cuadrito_72_siz), .sde(c3[24]), .ZA_WARUDO(ZA_WARUDO),
    .reset(reset));  // open: in_7
  pixel_cuadrito pixel_cuadrito_73 (
    .clk(clk), .abajo(pixel_cuadrito_74_sar), .izq(c2[23]), .der(pixel_cuadrito_105_siz), .dir(dir),
    .sar(pixel_cuadrito_73_sar), .siz(pixel_cuadrito_73_siz), .sde(c3[23]), .ZA_WARUDO(ZA_WARUDO),
    .reset(reset));  // open: in_7
  pixel_cuadrito pixel_cuadrito_74 (
    .clk(clk), .abajo(pixel_cuadrito_75_sar), .izq(c2[22]), .der(pixel_cuadrito_106_siz), .dir(dir),
    .sar(pixel_cuadrito_74_sar), .siz(pixel_cuadrito_74_siz), .sde(c3[22]), .ZA_WARUDO(ZA_WARUDO),
    .reset(reset));  // open: in_7
  pixel_cuadrito pixel_cuadrito_75 (
    .clk(clk), .abajo(pixel_cuadrito_76_sar), .izq(c2[21]), .der(pixel_cuadrito_107_siz), .dir(dir),
    .sar(pixel_cuadrito_75_sar), .siz(pixel_cuadrito_75_siz), .sde(c3[21]), .ZA_WARUDO(ZA_WARUDO),
    .reset(reset));  // open: in_7
  pixel_cuadrito pixel_cuadrito_76 (
    .clk(clk), .abajo(pixel_cuadrito_77_sar), .izq(c2[20]), .der(pixel_cuadrito_108_siz), .dir(dir),
    .sar(pixel_cuadrito_76_sar), .siz(pixel_cuadrito_76_siz), .sde(c3[20]), .ZA_WARUDO(ZA_WARUDO),
    .reset(reset));  // open: in_7
  pixel_cuadrito pixel_cuadrito_77 (
    .clk(clk), .abajo(pixel_cuadrito_78_sar), .izq(c2[19]), .der(pixel_cuadrito_109_siz), .dir(dir),
    .sar(pixel_cuadrito_77_sar), .siz(pixel_cuadrito_77_siz), .sde(c3[19]), .ZA_WARUDO(ZA_WARUDO),
    .reset(reset));  // open: in_7
  pixel_cuadrito pixel_cuadrito_78 (
    .clk(clk), .abajo(pixel_cuadrito_79_sar), .izq(c2[18]), .der(pixel_cuadrito_110_siz), .dir(dir),
    .sar(pixel_cuadrito_78_sar), .siz(pixel_cuadrito_78_siz), .sde(c3[18]), .ZA_WARUDO(ZA_WARUDO),
    .reset(reset));  // open: in_7
  pixel_cuadrito pixel_cuadrito_79 (
    .clk(clk), .abajo(pixel_cuadrito_80_sar), .izq(c2[17]), .der(pixel_cuadrito_111_siz), .dir(dir),
    .sar(pixel_cuadrito_79_sar), .siz(pixel_cuadrito_79_siz), .sde(c3[17]), .ZA_WARUDO(ZA_WARUDO),
    .reset(reset));  // open: in_7
  pixel_cuadrito pixel_cuadrito_80 (
    .clk(clk), .abajo(pixel_cuadrito_81_sar), .izq(c2[16]), .der(pixel_cuadrito_112_siz), .dir(dir),
    .sar(pixel_cuadrito_80_sar), .siz(pixel_cuadrito_80_siz), .sde(c3[16]), .ZA_WARUDO(ZA_WARUDO),
    .reset(reset));  // open: in_7
  pixel_cuadrito pixel_cuadrito_81 (
    .clk(clk), .abajo(pixel_cuadrito_82_sar), .izq(c2[15]), .der(pixel_cuadrito_113_siz), .dir(dir),
    .sar(pixel_cuadrito_81_sar), .siz(pixel_cuadrito_81_siz), .sde(c3[15]), .ZA_WARUDO(ZA_WARUDO),
    .reset(reset));  // open: in_7
  pixel_cuadrito pixel_cuadrito_82 (
    .clk(clk), .abajo(pixel_cuadrito_83_sar), .izq(c2[14]), .der(pixel_cuadrito_114_siz), .dir(dir),
    .sar(pixel_cuadrito_82_sar), .siz(pixel_cuadrito_82_siz), .sde(c3[14]), .ZA_WARUDO(ZA_WARUDO),
    .reset(reset));  // open: in_7
  pixel_cuadrito pixel_cuadrito_83 (
    .clk(clk), .abajo(pixel_cuadrito_84_sar), .izq(c2[13]), .der(pixel_cuadrito_115_siz), .dir(dir),
    .sar(pixel_cuadrito_83_sar), .siz(pixel_cuadrito_83_siz), .sde(c3[13]), .ZA_WARUDO(ZA_WARUDO),
    .reset(reset));  // open: in_7
  pixel_cuadrito pixel_cuadrito_84 (
    .clk(clk), .abajo(pixel_cuadrito_85_sar), .izq(c2[12]), .der(pixel_cuadrito_116_siz), .dir(dir),
    .sar(pixel_cuadrito_84_sar), .siz(pixel_cuadrito_84_siz), .sde(c3[12]), .ZA_WARUDO(ZA_WARUDO),
    .reset(reset));  // open: in_7
  pixel_cuadrito pixel_cuadrito_85 (
    .clk(clk), .abajo(pixel_cuadrito_86_sar), .izq(c2[11]), .der(pixel_cuadrito_117_siz), .dir(dir),
    .sar(pixel_cuadrito_85_sar), .siz(pixel_cuadrito_85_siz), .sde(c3[11]), .ZA_WARUDO(ZA_WARUDO),
    .reset(reset));  // open: in_7
  pixel_cuadrito pixel_cuadrito_86 (
    .clk(clk), .abajo(pixel_cuadrito_87_sar), .izq(c2[10]), .der(pixel_cuadrito_118_siz), .dir(dir),
    .sar(pixel_cuadrito_86_sar), .siz(pixel_cuadrito_86_siz), .sde(c3[10]), .ZA_WARUDO(ZA_WARUDO),
    .reset(reset));  // open: in_7
  pixel_cuadrito pixel_cuadrito_87 (
    .clk(clk), .abajo(pixel_cuadrito_88_sar), .izq(c2[9]), .der(pixel_cuadrito_119_siz), .dir(dir),
    .sar(pixel_cuadrito_87_sar), .siz(pixel_cuadrito_87_siz), .sde(c3[9]), .ZA_WARUDO(ZA_WARUDO),
    .reset(reset));  // open: in_7
  pixel_cuadrito pixel_cuadrito_88 (
    .clk(clk), .abajo(pixel_cuadrito_89_sar), .izq(c2[8]), .der(pixel_cuadrito_120_siz), .dir(dir),
    .sar(pixel_cuadrito_88_sar), .siz(pixel_cuadrito_88_siz), .sde(c3[8]), .ZA_WARUDO(ZA_WARUDO),
    .reset(reset));  // open: in_7
  pixel_cuadrito pixel_cuadrito_89 (
    .clk(clk), .abajo(pixel_cuadrito_90_sar), .izq(c2[7]), .der(pixel_cuadrito_121_siz), .dir(dir),
    .sar(pixel_cuadrito_89_sar), .siz(pixel_cuadrito_89_siz), .sde(c3[7]), .ZA_WARUDO(ZA_WARUDO),
    .reset(reset));  // open: in_7
  pixel_cuadrito pixel_cuadrito_90 (
    .clk(clk), .abajo(pixel_cuadrito_91_sar), .izq(c2[6]), .der(pixel_cuadrito_122_siz), .dir(dir),
    .sar(pixel_cuadrito_90_sar), .siz(pixel_cuadrito_90_siz), .sde(c3[6]), .ZA_WARUDO(ZA_WARUDO),
    .reset(reset));  // open: in_7
  pixel_cuadrito pixel_cuadrito_91 (
    .clk(clk), .abajo(pixel_cuadrito_92_sar), .izq(c2[5]), .der(pixel_cuadrito_123_siz), .dir(dir),
    .sar(pixel_cuadrito_91_sar), .siz(pixel_cuadrito_91_siz), .sde(c3[5]), .ZA_WARUDO(ZA_WARUDO),
    .reset(reset));  // open: in_7
  pixel_cuadrito pixel_cuadrito_92 (
    .clk(clk), .abajo(pixel_cuadrito_93_sar), .izq(c2[4]), .der(pixel_cuadrito_124_siz), .dir(dir),
    .sar(pixel_cuadrito_92_sar), .siz(pixel_cuadrito_92_siz), .sde(c3[4]), .ZA_WARUDO(ZA_WARUDO),
    .reset(reset));  // open: in_7
  pixel_cuadrito pixel_cuadrito_93 (
    .clk(clk), .abajo(pixel_cuadrito_94_sar), .izq(c2[3]), .der(pixel_cuadrito_125_siz), .dir(dir),
    .sar(pixel_cuadrito_93_sar), .siz(pixel_cuadrito_93_siz), .sde(c3[3]), .ZA_WARUDO(ZA_WARUDO),
    .reset(reset));  // open: in_7
  pixel_cuadrito pixel_cuadrito_94 (
    .clk(clk), .abajo(pixel_cuadrito_95_sar), .izq(c2[2]), .der(pixel_cuadrito_126_siz), .dir(dir),
    .sar(pixel_cuadrito_94_sar), .siz(pixel_cuadrito_94_siz), .sde(c3[2]), .in_7(s2os3),
    .ZA_WARUDO(ZA_WARUDO), .reset(reset));
  pixel_cuadrito pixel_cuadrito_95 (
    .clk(clk), .abajo(pixel_cuadrito_96_sar), .izq(c2[1]), .der(pixel_cuadrito_127_siz), .dir(dir),
    .sar(pixel_cuadrito_95_sar), .siz(pixel_cuadrito_95_siz), .sde(c3[1]), .in_7(s2os3),
    .ZA_WARUDO(ZA_WARUDO), .reset(reset));
  pixel_cuadrito pixel_cuadrito_96 (
    .clk(clk), .abajo(c3[31]), .izq(c2[0]), .der(pixel_cuadrito_128_siz), .dir(dir),
    .sar(pixel_cuadrito_96_sar), .siz(pixel_cuadrito_96_siz), .sde(c3[0]), .ZA_WARUDO(ZA_WARUDO),
    .reset(reset));  // open: in_7
  pixel_cuadrito pixel_cuadrito_97 (
    .clk(clk), .abajo(pixel_cuadrito_98_sar), .izq(c3[31]), .der(pixel_cuadrito_129_siz), .dir(dir),
    .siz(pixel_cuadrito_97_siz), .sde(c4[31]), .ZA_WARUDO(ZA_WARUDO), .reset(reset));  // open: sar, in_7
  pixel_cuadrito pixel_cuadrito_98 (
    .clk(clk), .abajo(pixel_cuadrito_99_sar), .izq(c3[30]), .der(pixel_cuadrito_130_siz), .dir(dir),
    .sar(pixel_cuadrito_98_sar), .siz(pixel_cuadrito_98_siz), .sde(c4[30]), .ZA_WARUDO(ZA_WARUDO),
    .reset(reset));  // open: in_7
  pixel_cuadrito pixel_cuadrito_99 (
    .clk(clk), .abajo(pixel_cuadrito_100_sar), .izq(c3[29]), .der(pixel_cuadrito_131_siz), .dir(dir),
    .sar(pixel_cuadrito_99_sar), .siz(pixel_cuadrito_99_siz), .sde(c4[29]), .ZA_WARUDO(ZA_WARUDO),
    .reset(reset));  // open: in_7
  pixel_cuadrito pixel_cuadrito_100 (
    .clk(clk), .abajo(pixel_cuadrito_101_sar), .izq(c3[28]), .der(pixel_cuadrito_132_siz), .dir(dir),
    .sar(pixel_cuadrito_100_sar), .siz(pixel_cuadrito_100_siz), .sde(c4[28]), .ZA_WARUDO(ZA_WARUDO),
    .reset(reset));  // open: in_7
  pixel_cuadrito pixel_cuadrito_101 (
    .clk(clk), .abajo(pixel_cuadrito_102_sar), .izq(c3[27]), .der(pixel_cuadrito_133_siz), .dir(dir),
    .sar(pixel_cuadrito_101_sar), .siz(pixel_cuadrito_101_siz), .sde(c4[27]), .ZA_WARUDO(ZA_WARUDO),
    .reset(reset));  // open: in_7
  pixel_cuadrito pixel_cuadrito_102 (
    .clk(clk), .abajo(pixel_cuadrito_103_sar), .izq(c3[26]), .der(pixel_cuadrito_134_siz), .dir(dir),
    .sar(pixel_cuadrito_102_sar), .siz(pixel_cuadrito_102_siz), .sde(c4[26]), .ZA_WARUDO(ZA_WARUDO),
    .reset(reset));  // open: in_7
  pixel_cuadrito pixel_cuadrito_103 (
    .clk(clk), .abajo(pixel_cuadrito_104_sar), .izq(c3[25]), .der(pixel_cuadrito_135_siz), .dir(dir),
    .sar(pixel_cuadrito_103_sar), .siz(pixel_cuadrito_103_siz), .sde(c4[25]), .ZA_WARUDO(ZA_WARUDO),
    .reset(reset));  // open: in_7
  pixel_cuadrito pixel_cuadrito_104 (
    .clk(clk), .abajo(pixel_cuadrito_105_sar), .izq(c3[24]), .der(pixel_cuadrito_136_siz), .dir(dir),
    .sar(pixel_cuadrito_104_sar), .siz(pixel_cuadrito_104_siz), .sde(c4[24]), .ZA_WARUDO(ZA_WARUDO),
    .reset(reset));  // open: in_7
  pixel_cuadrito pixel_cuadrito_105 (
    .clk(clk), .abajo(pixel_cuadrito_106_sar), .izq(c3[23]), .der(pixel_cuadrito_137_siz), .dir(dir),
    .sar(pixel_cuadrito_105_sar), .siz(pixel_cuadrito_105_siz), .sde(c4[23]), .ZA_WARUDO(ZA_WARUDO),
    .reset(reset));  // open: in_7
  pixel_cuadrito pixel_cuadrito_106 (
    .clk(clk), .abajo(pixel_cuadrito_107_sar), .izq(c3[22]), .der(pixel_cuadrito_138_siz), .dir(dir),
    .sar(pixel_cuadrito_106_sar), .siz(pixel_cuadrito_106_siz), .sde(c4[22]), .ZA_WARUDO(ZA_WARUDO),
    .reset(reset));  // open: in_7
  pixel_cuadrito pixel_cuadrito_107 (
    .clk(clk), .abajo(pixel_cuadrito_108_sar), .izq(c3[21]), .der(pixel_cuadrito_139_siz), .dir(dir),
    .sar(pixel_cuadrito_107_sar), .siz(pixel_cuadrito_107_siz), .sde(c4[21]), .ZA_WARUDO(ZA_WARUDO),
    .reset(reset));  // open: in_7
  pixel_cuadrito pixel_cuadrito_108 (
    .clk(clk), .abajo(pixel_cuadrito_109_sar), .izq(c3[20]), .der(pixel_cuadrito_140_siz), .dir(dir),
    .sar(pixel_cuadrito_108_sar), .siz(pixel_cuadrito_108_siz), .sde(c4[20]), .ZA_WARUDO(ZA_WARUDO),
    .reset(reset));  // open: in_7
  pixel_cuadrito pixel_cuadrito_109 (
    .clk(clk), .abajo(pixel_cuadrito_110_sar), .izq(c3[19]), .der(pixel_cuadrito_141_siz), .dir(dir),
    .sar(pixel_cuadrito_109_sar), .siz(pixel_cuadrito_109_siz), .sde(c4[19]), .ZA_WARUDO(ZA_WARUDO),
    .reset(reset));  // open: in_7
  pixel_cuadrito pixel_cuadrito_110 (
    .clk(clk), .abajo(pixel_cuadrito_111_sar), .izq(c3[18]), .der(pixel_cuadrito_142_siz), .dir(dir),
    .sar(pixel_cuadrito_110_sar), .siz(pixel_cuadrito_110_siz), .sde(c4[18]), .ZA_WARUDO(ZA_WARUDO),
    .reset(reset));  // open: in_7
  pixel_cuadrito pixel_cuadrito_111 (
    .clk(clk), .abajo(pixel_cuadrito_112_sar), .izq(c3[17]), .der(pixel_cuadrito_143_siz), .dir(dir),
    .sar(pixel_cuadrito_111_sar), .siz(pixel_cuadrito_111_siz), .sde(c4[17]), .ZA_WARUDO(ZA_WARUDO),
    .reset(reset));  // open: in_7
  pixel_cuadrito pixel_cuadrito_112 (
    .clk(clk), .abajo(pixel_cuadrito_113_sar), .izq(c3[16]), .der(pixel_cuadrito_144_siz), .dir(dir),
    .sar(pixel_cuadrito_112_sar), .siz(pixel_cuadrito_112_siz), .sde(c4[16]), .ZA_WARUDO(ZA_WARUDO),
    .reset(reset));  // open: in_7
  pixel_cuadrito pixel_cuadrito_113 (
    .clk(clk), .abajo(pixel_cuadrito_114_sar), .izq(c3[15]), .der(pixel_cuadrito_145_siz), .dir(dir),
    .sar(pixel_cuadrito_113_sar), .siz(pixel_cuadrito_113_siz), .sde(c4[15]), .ZA_WARUDO(ZA_WARUDO),
    .reset(reset));  // open: in_7
  pixel_cuadrito pixel_cuadrito_114 (
    .clk(clk), .abajo(pixel_cuadrito_115_sar), .izq(c3[14]), .der(pixel_cuadrito_146_siz), .dir(dir),
    .sar(pixel_cuadrito_114_sar), .siz(pixel_cuadrito_114_siz), .sde(c4[14]), .ZA_WARUDO(ZA_WARUDO),
    .reset(reset));  // open: in_7
  pixel_cuadrito pixel_cuadrito_115 (
    .clk(clk), .abajo(pixel_cuadrito_116_sar), .izq(c3[13]), .der(pixel_cuadrito_147_siz), .dir(dir),
    .sar(pixel_cuadrito_115_sar), .siz(pixel_cuadrito_115_siz), .sde(c4[13]), .ZA_WARUDO(ZA_WARUDO),
    .reset(reset));  // open: in_7
  pixel_cuadrito pixel_cuadrito_116 (
    .clk(clk), .abajo(pixel_cuadrito_117_sar), .izq(c3[12]), .der(pixel_cuadrito_148_siz), .dir(dir),
    .sar(pixel_cuadrito_116_sar), .siz(pixel_cuadrito_116_siz), .sde(c4[12]), .ZA_WARUDO(ZA_WARUDO),
    .reset(reset));  // open: in_7
  pixel_cuadrito pixel_cuadrito_117 (
    .clk(clk), .abajo(pixel_cuadrito_118_sar), .izq(c3[11]), .der(pixel_cuadrito_149_siz), .dir(dir),
    .sar(pixel_cuadrito_117_sar), .siz(pixel_cuadrito_117_siz), .sde(c4[11]), .ZA_WARUDO(ZA_WARUDO),
    .reset(reset));  // open: in_7
  pixel_cuadrito pixel_cuadrito_118 (
    .clk(clk), .abajo(pixel_cuadrito_119_sar), .izq(c3[10]), .der(pixel_cuadrito_150_siz), .dir(dir),
    .sar(pixel_cuadrito_118_sar), .siz(pixel_cuadrito_118_siz), .sde(c4[10]), .ZA_WARUDO(ZA_WARUDO),
    .reset(reset));  // open: in_7
  pixel_cuadrito pixel_cuadrito_119 (
    .clk(clk), .abajo(pixel_cuadrito_120_sar), .izq(c3[9]), .der(pixel_cuadrito_151_siz), .dir(dir),
    .sar(pixel_cuadrito_119_sar), .siz(pixel_cuadrito_119_siz), .sde(c4[9]), .ZA_WARUDO(ZA_WARUDO),
    .reset(reset));  // open: in_7
  pixel_cuadrito pixel_cuadrito_120 (
    .clk(clk), .abajo(pixel_cuadrito_121_sar), .izq(c3[8]), .der(pixel_cuadrito_152_siz), .dir(dir),
    .sar(pixel_cuadrito_120_sar), .siz(pixel_cuadrito_120_siz), .sde(c4[8]), .ZA_WARUDO(ZA_WARUDO),
    .reset(reset));  // open: in_7
  pixel_cuadrito pixel_cuadrito_121 (
    .clk(clk), .abajo(pixel_cuadrito_122_sar), .izq(c3[7]), .der(pixel_cuadrito_153_siz), .dir(dir),
    .sar(pixel_cuadrito_121_sar), .siz(pixel_cuadrito_121_siz), .sde(c4[7]), .ZA_WARUDO(ZA_WARUDO),
    .reset(reset));  // open: in_7
  pixel_cuadrito pixel_cuadrito_122 (
    .clk(clk), .abajo(pixel_cuadrito_123_sar), .izq(c3[6]), .der(pixel_cuadrito_154_siz), .dir(dir),
    .sar(pixel_cuadrito_122_sar), .siz(pixel_cuadrito_122_siz), .sde(c4[6]), .ZA_WARUDO(ZA_WARUDO),
    .reset(reset));  // open: in_7
  pixel_cuadrito pixel_cuadrito_123 (
    .clk(clk), .abajo(pixel_cuadrito_124_sar), .izq(c3[5]), .der(pixel_cuadrito_155_siz), .dir(dir),
    .sar(pixel_cuadrito_123_sar), .siz(pixel_cuadrito_123_siz), .sde(c4[5]), .ZA_WARUDO(ZA_WARUDO),
    .reset(reset));  // open: in_7
  pixel_cuadrito pixel_cuadrito_124 (
    .clk(clk), .abajo(pixel_cuadrito_125_sar), .izq(c3[4]), .der(pixel_cuadrito_156_siz), .dir(dir),
    .sar(pixel_cuadrito_124_sar), .siz(pixel_cuadrito_124_siz), .sde(c4[4]), .ZA_WARUDO(ZA_WARUDO),
    .reset(reset));  // open: in_7
  pixel_cuadrito pixel_cuadrito_125 (
    .clk(clk), .abajo(pixel_cuadrito_126_sar), .izq(c3[3]), .der(pixel_cuadrito_157_siz), .dir(dir),
    .sar(pixel_cuadrito_125_sar), .siz(pixel_cuadrito_125_siz), .sde(c4[3]), .ZA_WARUDO(ZA_WARUDO),
    .reset(reset));  // open: in_7
  pixel_cuadrito pixel_cuadrito_126 (
    .clk(clk), .abajo(pixel_cuadrito_127_sar), .izq(c3[2]), .der(pixel_cuadrito_158_siz), .dir(dir),
    .sar(pixel_cuadrito_126_sar), .siz(pixel_cuadrito_126_siz), .sde(c4[2]), .in_7(s3os4),
    .ZA_WARUDO(ZA_WARUDO), .reset(reset));
  pixel_cuadrito pixel_cuadrito_127 (
    .clk(clk), .abajo(pixel_cuadrito_128_sar), .izq(c3[1]), .der(pixel_cuadrito_159_siz), .dir(dir),
    .sar(pixel_cuadrito_127_sar), .siz(pixel_cuadrito_127_siz), .sde(c4[1]), .in_7(s3os4),
    .ZA_WARUDO(ZA_WARUDO), .reset(reset));
  pixel_cuadrito pixel_cuadrito_128 (
    .clk(clk), .abajo(c4[31]), .izq(c3[0]), .der(pixel_cuadrito_160_siz), .dir(dir),
    .sar(pixel_cuadrito_128_sar), .siz(pixel_cuadrito_128_siz), .sde(c4[0]), .ZA_WARUDO(ZA_WARUDO),
    .reset(reset));  // open: in_7
  pixel_cuadrito pixel_cuadrito_129 (
    .clk(clk), .abajo(pixel_cuadrito_130_sar), .izq(c4[31]), .der(pixel_cuadrito_161_siz), .dir(dir),
    .siz(pixel_cuadrito_129_siz), .sde(c5[31]), .ZA_WARUDO(ZA_WARUDO), .reset(reset));  // open: sar, in_7
  pixel_cuadrito pixel_cuadrito_130 (
    .clk(clk), .abajo(pixel_cuadrito_131_sar), .izq(c4[30]), .der(pixel_cuadrito_162_siz), .dir(dir),
    .sar(pixel_cuadrito_130_sar), .siz(pixel_cuadrito_130_siz), .sde(c5[30]), .ZA_WARUDO(ZA_WARUDO),
    .reset(reset));  // open: in_7
  pixel_cuadrito pixel_cuadrito_131 (
    .clk(clk), .abajo(pixel_cuadrito_132_sar), .izq(c4[29]), .der(pixel_cuadrito_163_siz), .dir(dir),
    .sar(pixel_cuadrito_131_sar), .siz(pixel_cuadrito_131_siz), .sde(c5[29]), .ZA_WARUDO(ZA_WARUDO),
    .reset(reset));  // open: in_7
  pixel_cuadrito pixel_cuadrito_132 (
    .clk(clk), .abajo(pixel_cuadrito_133_sar), .izq(c4[28]), .der(pixel_cuadrito_164_siz), .dir(dir),
    .sar(pixel_cuadrito_132_sar), .siz(pixel_cuadrito_132_siz), .sde(c5[28]), .ZA_WARUDO(ZA_WARUDO),
    .reset(reset));  // open: in_7
  pixel_cuadrito pixel_cuadrito_133 (
    .clk(clk), .abajo(pixel_cuadrito_134_sar), .izq(c4[27]), .der(pixel_cuadrito_165_siz), .dir(dir),
    .sar(pixel_cuadrito_133_sar), .siz(pixel_cuadrito_133_siz), .sde(c5[27]), .ZA_WARUDO(ZA_WARUDO),
    .reset(reset));  // open: in_7
  pixel_cuadrito pixel_cuadrito_134 (
    .clk(clk), .abajo(pixel_cuadrito_135_sar), .izq(c4[26]), .der(pixel_cuadrito_166_siz), .dir(dir),
    .sar(pixel_cuadrito_134_sar), .siz(pixel_cuadrito_134_siz), .sde(c5[26]), .ZA_WARUDO(ZA_WARUDO),
    .reset(reset));  // open: in_7
  pixel_cuadrito pixel_cuadrito_135 (
    .clk(clk), .abajo(pixel_cuadrito_136_sar), .izq(c4[25]), .der(pixel_cuadrito_167_siz), .dir(dir),
    .sar(pixel_cuadrito_135_sar), .siz(pixel_cuadrito_135_siz), .sde(c5[25]), .ZA_WARUDO(ZA_WARUDO),
    .reset(reset));  // open: in_7
  pixel_cuadrito pixel_cuadrito_136 (
    .clk(clk), .abajo(pixel_cuadrito_137_sar), .izq(c4[24]), .der(pixel_cuadrito_168_siz), .dir(dir),
    .sar(pixel_cuadrito_136_sar), .siz(pixel_cuadrito_136_siz), .sde(c5[24]), .ZA_WARUDO(ZA_WARUDO),
    .reset(reset));  // open: in_7
  pixel_cuadrito pixel_cuadrito_137 (
    .clk(clk), .abajo(pixel_cuadrito_138_sar), .izq(c4[23]), .der(pixel_cuadrito_169_siz), .dir(dir),
    .sar(pixel_cuadrito_137_sar), .siz(pixel_cuadrito_137_siz), .sde(c5[23]), .ZA_WARUDO(ZA_WARUDO),
    .reset(reset));  // open: in_7
  pixel_cuadrito pixel_cuadrito_138 (
    .clk(clk), .abajo(pixel_cuadrito_139_sar), .izq(c4[22]), .der(pixel_cuadrito_170_siz), .dir(dir),
    .sar(pixel_cuadrito_138_sar), .siz(pixel_cuadrito_138_siz), .sde(c5[22]), .ZA_WARUDO(ZA_WARUDO),
    .reset(reset));  // open: in_7
  pixel_cuadrito pixel_cuadrito_139 (
    .clk(clk), .abajo(pixel_cuadrito_140_sar), .izq(c4[21]), .der(pixel_cuadrito_171_siz), .dir(dir),
    .sar(pixel_cuadrito_139_sar), .siz(pixel_cuadrito_139_siz), .sde(c5[21]), .ZA_WARUDO(ZA_WARUDO),
    .reset(reset));  // open: in_7
  pixel_cuadrito pixel_cuadrito_140 (
    .clk(clk), .abajo(pixel_cuadrito_141_sar), .izq(c4[20]), .der(pixel_cuadrito_172_siz), .dir(dir),
    .sar(pixel_cuadrito_140_sar), .siz(pixel_cuadrito_140_siz), .sde(c5[20]), .ZA_WARUDO(ZA_WARUDO),
    .reset(reset));  // open: in_7
  pixel_cuadrito pixel_cuadrito_141 (
    .clk(clk), .abajo(pixel_cuadrito_142_sar), .izq(c4[19]), .der(pixel_cuadrito_173_siz), .dir(dir),
    .sar(pixel_cuadrito_141_sar), .siz(pixel_cuadrito_141_siz), .sde(c5[19]), .ZA_WARUDO(ZA_WARUDO),
    .reset(reset));  // open: in_7
  pixel_cuadrito pixel_cuadrito_142 (
    .clk(clk), .abajo(pixel_cuadrito_143_sar), .izq(c4[18]), .der(pixel_cuadrito_174_siz), .dir(dir),
    .sar(pixel_cuadrito_142_sar), .siz(pixel_cuadrito_142_siz), .sde(c5[18]), .ZA_WARUDO(ZA_WARUDO),
    .reset(reset));  // open: in_7
  pixel_cuadrito pixel_cuadrito_143 (
    .clk(clk), .abajo(pixel_cuadrito_144_sar), .izq(c4[17]), .der(pixel_cuadrito_175_siz), .dir(dir),
    .sar(pixel_cuadrito_143_sar), .siz(pixel_cuadrito_143_siz), .sde(c5[17]), .ZA_WARUDO(ZA_WARUDO),
    .reset(reset));  // open: in_7
  pixel_cuadrito pixel_cuadrito_144 (
    .clk(clk), .abajo(pixel_cuadrito_145_sar), .izq(c4[16]), .der(pixel_cuadrito_176_siz), .dir(dir),
    .sar(pixel_cuadrito_144_sar), .siz(pixel_cuadrito_144_siz), .sde(c5[16]), .ZA_WARUDO(ZA_WARUDO),
    .reset(reset));  // open: in_7
  pixel_cuadrito pixel_cuadrito_145 (
    .clk(clk), .abajo(pixel_cuadrito_146_sar), .izq(c4[15]), .der(pixel_cuadrito_177_siz), .dir(dir),
    .sar(pixel_cuadrito_145_sar), .siz(pixel_cuadrito_145_siz), .sde(c5[15]), .ZA_WARUDO(ZA_WARUDO),
    .reset(reset));  // open: in_7
  pixel_cuadrito pixel_cuadrito_146 (
    .clk(clk), .abajo(pixel_cuadrito_147_sar), .izq(c4[14]), .der(pixel_cuadrito_178_siz), .dir(dir),
    .sar(pixel_cuadrito_146_sar), .siz(pixel_cuadrito_146_siz), .sde(c5[14]), .ZA_WARUDO(ZA_WARUDO),
    .reset(reset));  // open: in_7
  pixel_cuadrito pixel_cuadrito_147 (
    .clk(clk), .abajo(pixel_cuadrito_148_sar), .izq(c4[13]), .der(pixel_cuadrito_179_siz), .dir(dir),
    .sar(pixel_cuadrito_147_sar), .siz(pixel_cuadrito_147_siz), .sde(c5[13]), .ZA_WARUDO(ZA_WARUDO),
    .reset(reset));  // open: in_7
  pixel_cuadrito pixel_cuadrito_148 (
    .clk(clk), .abajo(pixel_cuadrito_149_sar), .izq(c4[12]), .der(pixel_cuadrito_180_siz), .dir(dir),
    .sar(pixel_cuadrito_148_sar), .siz(pixel_cuadrito_148_siz), .sde(c5[12]), .ZA_WARUDO(ZA_WARUDO),
    .reset(reset));  // open: in_7
  pixel_cuadrito pixel_cuadrito_149 (
    .clk(clk), .abajo(pixel_cuadrito_150_sar), .izq(c4[11]), .der(pixel_cuadrito_181_siz), .dir(dir),
    .sar(pixel_cuadrito_149_sar), .siz(pixel_cuadrito_149_siz), .sde(c5[11]), .ZA_WARUDO(ZA_WARUDO),
    .reset(reset));  // open: in_7
  pixel_cuadrito pixel_cuadrito_150 (
    .clk(clk), .abajo(pixel_cuadrito_151_sar), .izq(c4[10]), .der(pixel_cuadrito_182_siz), .dir(dir),
    .sar(pixel_cuadrito_150_sar), .siz(pixel_cuadrito_150_siz), .sde(c5[10]), .ZA_WARUDO(ZA_WARUDO),
    .reset(reset));  // open: in_7
  pixel_cuadrito pixel_cuadrito_151 (
    .clk(clk), .abajo(pixel_cuadrito_152_sar), .izq(c4[9]), .der(pixel_cuadrito_183_siz), .dir(dir),
    .sar(pixel_cuadrito_151_sar), .siz(pixel_cuadrito_151_siz), .sde(c5[9]), .ZA_WARUDO(ZA_WARUDO),
    .reset(reset));  // open: in_7
  pixel_cuadrito pixel_cuadrito_152 (
    .clk(clk), .abajo(pixel_cuadrito_153_sar), .izq(c4[8]), .der(pixel_cuadrito_184_siz), .dir(dir),
    .sar(pixel_cuadrito_152_sar), .siz(pixel_cuadrito_152_siz), .sde(c5[8]), .ZA_WARUDO(ZA_WARUDO),
    .reset(reset));  // open: in_7
  pixel_cuadrito pixel_cuadrito_153 (
    .clk(clk), .abajo(pixel_cuadrito_154_sar), .izq(c4[7]), .der(pixel_cuadrito_185_siz), .dir(dir),
    .sar(pixel_cuadrito_153_sar), .siz(pixel_cuadrito_153_siz), .sde(c5[7]), .ZA_WARUDO(ZA_WARUDO),
    .reset(reset));  // open: in_7
  pixel_cuadrito pixel_cuadrito_154 (
    .clk(clk), .abajo(pixel_cuadrito_155_sar), .izq(c4[6]), .der(pixel_cuadrito_186_siz), .dir(dir),
    .sar(pixel_cuadrito_154_sar), .siz(pixel_cuadrito_154_siz), .sde(c5[6]), .ZA_WARUDO(ZA_WARUDO),
    .reset(reset));  // open: in_7
  pixel_cuadrito pixel_cuadrito_155 (
    .clk(clk), .abajo(pixel_cuadrito_156_sar), .izq(c4[5]), .der(pixel_cuadrito_187_siz), .dir(dir),
    .sar(pixel_cuadrito_155_sar), .siz(pixel_cuadrito_155_siz), .sde(c5[5]), .ZA_WARUDO(ZA_WARUDO),
    .reset(reset));  // open: in_7
  pixel_cuadrito pixel_cuadrito_156 (
    .clk(clk), .abajo(pixel_cuadrito_157_sar), .izq(c4[4]), .der(pixel_cuadrito_188_siz), .dir(dir),
    .sar(pixel_cuadrito_156_sar), .siz(pixel_cuadrito_156_siz), .sde(c5[4]), .ZA_WARUDO(ZA_WARUDO),
    .reset(reset));  // open: in_7
  pixel_cuadrito pixel_cuadrito_157 (
    .clk(clk), .abajo(pixel_cuadrito_158_sar), .izq(c4[3]), .der(pixel_cuadrito_189_siz), .dir(dir),
    .sar(pixel_cuadrito_157_sar), .siz(pixel_cuadrito_157_siz), .sde(c5[3]), .ZA_WARUDO(ZA_WARUDO),
    .reset(reset));  // open: in_7
  pixel_cuadrito pixel_cuadrito_158 (
    .clk(clk), .abajo(pixel_cuadrito_159_sar), .izq(c4[2]), .der(pixel_cuadrito_190_siz), .dir(dir),
    .sar(pixel_cuadrito_158_sar), .siz(pixel_cuadrito_158_siz), .sde(c5[2]), .in_7(s4os5),
    .ZA_WARUDO(ZA_WARUDO), .reset(reset));
  pixel_cuadrito pixel_cuadrito_159 (
    .clk(clk), .abajo(pixel_cuadrito_160_sar), .izq(c4[1]), .der(pixel_cuadrito_191_siz), .dir(dir),
    .sar(pixel_cuadrito_159_sar), .siz(pixel_cuadrito_159_siz), .sde(c5[1]), .in_7(s4os5),
    .ZA_WARUDO(ZA_WARUDO), .reset(reset));
  pixel_cuadrito pixel_cuadrito_160 (
    .clk(clk), .abajo(c5[31]), .izq(c4[0]), .der(pixel_cuadrito_192_siz), .dir(dir),
    .sar(pixel_cuadrito_160_sar), .siz(pixel_cuadrito_160_siz), .sde(c5[0]), .ZA_WARUDO(ZA_WARUDO),
    .reset(reset));  // open: in_7
  pixel_cuadrito pixel_cuadrito_161 (
    .clk(clk), .abajo(pixel_cuadrito_162_sar), .izq(c5[31]), .der(pixel_cuadrito_193_siz), .dir(dir),
    .siz(pixel_cuadrito_161_siz), .sde(c6[31]), .ZA_WARUDO(ZA_WARUDO), .reset(reset));  // open: sar, in_7
  pixel_cuadrito pixel_cuadrito_162 (
    .clk(clk), .abajo(pixel_cuadrito_163_sar), .izq(c5[30]), .der(pixel_cuadrito_194_siz), .dir(dir),
    .sar(pixel_cuadrito_162_sar), .siz(pixel_cuadrito_162_siz), .sde(c6[30]), .ZA_WARUDO(ZA_WARUDO),
    .reset(reset));  // open: in_7
  pixel_cuadrito pixel_cuadrito_163 (
    .clk(clk), .abajo(pixel_cuadrito_164_sar), .izq(c5[29]), .der(pixel_cuadrito_195_siz), .dir(dir),
    .sar(pixel_cuadrito_163_sar), .siz(pixel_cuadrito_163_siz), .sde(c6[29]), .ZA_WARUDO(ZA_WARUDO),
    .reset(reset));  // open: in_7
  pixel_cuadrito pixel_cuadrito_164 (
    .clk(clk), .abajo(pixel_cuadrito_165_sar), .izq(c5[28]), .der(pixel_cuadrito_196_siz), .dir(dir),
    .sar(pixel_cuadrito_164_sar), .siz(pixel_cuadrito_164_siz), .sde(c6[28]), .ZA_WARUDO(ZA_WARUDO),
    .reset(reset));  // open: in_7
  pixel_cuadrito pixel_cuadrito_165 (
    .clk(clk), .abajo(pixel_cuadrito_166_sar), .izq(c5[27]), .der(pixel_cuadrito_197_siz), .dir(dir),
    .sar(pixel_cuadrito_165_sar), .siz(pixel_cuadrito_165_siz), .sde(c6[27]), .ZA_WARUDO(ZA_WARUDO),
    .reset(reset));  // open: in_7
  pixel_cuadrito pixel_cuadrito_166 (
    .clk(clk), .abajo(pixel_cuadrito_167_sar), .izq(c5[26]), .der(pixel_cuadrito_198_siz), .dir(dir),
    .sar(pixel_cuadrito_166_sar), .siz(pixel_cuadrito_166_siz), .sde(c6[26]), .ZA_WARUDO(ZA_WARUDO),
    .reset(reset));  // open: in_7
  pixel_cuadrito pixel_cuadrito_167 (
    .clk(clk), .abajo(pixel_cuadrito_168_sar), .izq(c5[25]), .der(pixel_cuadrito_199_siz), .dir(dir),
    .sar(pixel_cuadrito_167_sar), .siz(pixel_cuadrito_167_siz), .sde(c6[25]), .ZA_WARUDO(ZA_WARUDO),
    .reset(reset));  // open: in_7
  pixel_cuadrito pixel_cuadrito_168 (
    .clk(clk), .abajo(pixel_cuadrito_169_sar), .izq(c5[24]), .der(pixel_cuadrito_200_siz), .dir(dir),
    .sar(pixel_cuadrito_168_sar), .siz(pixel_cuadrito_168_siz), .sde(c6[24]), .ZA_WARUDO(ZA_WARUDO),
    .reset(reset));  // open: in_7
  pixel_cuadrito pixel_cuadrito_169 (
    .clk(clk), .abajo(pixel_cuadrito_170_sar), .izq(c5[23]), .der(pixel_cuadrito_201_siz), .dir(dir),
    .sar(pixel_cuadrito_169_sar), .siz(pixel_cuadrito_169_siz), .sde(c6[23]), .ZA_WARUDO(ZA_WARUDO),
    .reset(reset));  // open: in_7
  pixel_cuadrito pixel_cuadrito_170 (
    .clk(clk), .abajo(pixel_cuadrito_171_sar), .izq(c5[22]), .der(pixel_cuadrito_202_siz), .dir(dir),
    .sar(pixel_cuadrito_170_sar), .siz(pixel_cuadrito_170_siz), .sde(c6[22]), .ZA_WARUDO(ZA_WARUDO),
    .reset(reset));  // open: in_7
  pixel_cuadrito pixel_cuadrito_171 (
    .clk(clk), .abajo(pixel_cuadrito_172_sar), .izq(c5[21]), .der(pixel_cuadrito_203_siz), .dir(dir),
    .sar(pixel_cuadrito_171_sar), .siz(pixel_cuadrito_171_siz), .sde(c6[21]), .ZA_WARUDO(ZA_WARUDO),
    .reset(reset));  // open: in_7
  pixel_cuadrito pixel_cuadrito_172 (
    .clk(clk), .abajo(pixel_cuadrito_173_sar), .izq(c5[20]), .der(pixel_cuadrito_204_siz), .dir(dir),
    .sar(pixel_cuadrito_172_sar), .siz(pixel_cuadrito_172_siz), .sde(c6[20]), .ZA_WARUDO(ZA_WARUDO),
    .reset(reset));  // open: in_7
  pixel_cuadrito pixel_cuadrito_173 (
    .clk(clk), .abajo(pixel_cuadrito_174_sar), .izq(c5[19]), .der(pixel_cuadrito_205_siz), .dir(dir),
    .sar(pixel_cuadrito_173_sar), .siz(pixel_cuadrito_173_siz), .sde(c6[19]), .ZA_WARUDO(ZA_WARUDO),
    .reset(reset));  // open: in_7
  pixel_cuadrito pixel_cuadrito_174 (
    .clk(clk), .abajo(pixel_cuadrito_175_sar), .izq(c5[18]), .der(pixel_cuadrito_206_siz), .dir(dir),
    .sar(pixel_cuadrito_174_sar), .siz(pixel_cuadrito_174_siz), .sde(c6[18]), .ZA_WARUDO(ZA_WARUDO),
    .reset(reset));  // open: in_7
  pixel_cuadrito pixel_cuadrito_175 (
    .clk(clk), .abajo(pixel_cuadrito_176_sar), .izq(c5[17]), .der(pixel_cuadrito_207_siz), .dir(dir),
    .sar(pixel_cuadrito_175_sar), .siz(pixel_cuadrito_175_siz), .sde(c6[17]), .ZA_WARUDO(ZA_WARUDO),
    .reset(reset));  // open: in_7
  pixel_cuadrito pixel_cuadrito_176 (
    .clk(clk), .abajo(pixel_cuadrito_177_sar), .izq(c5[16]), .der(pixel_cuadrito_208_siz), .dir(dir),
    .sar(pixel_cuadrito_176_sar), .siz(pixel_cuadrito_176_siz), .sde(c6[16]), .ZA_WARUDO(ZA_WARUDO),
    .reset(reset));  // open: in_7
  pixel_cuadrito pixel_cuadrito_177 (
    .clk(clk), .abajo(pixel_cuadrito_178_sar), .izq(c5[15]), .der(pixel_cuadrito_209_siz), .dir(dir),
    .sar(pixel_cuadrito_177_sar), .siz(pixel_cuadrito_177_siz), .sde(c6[15]), .ZA_WARUDO(ZA_WARUDO),
    .reset(reset));  // open: in_7
  pixel_cuadrito pixel_cuadrito_178 (
    .clk(clk), .abajo(pixel_cuadrito_179_sar), .izq(c5[14]), .der(pixel_cuadrito_210_siz), .dir(dir),
    .sar(pixel_cuadrito_178_sar), .siz(pixel_cuadrito_178_siz), .sde(c6[14]), .ZA_WARUDO(ZA_WARUDO),
    .reset(reset));  // open: in_7
  pixel_cuadrito pixel_cuadrito_179 (
    .clk(clk), .abajo(pixel_cuadrito_180_sar), .izq(c5[13]), .der(pixel_cuadrito_211_siz), .dir(dir),
    .sar(pixel_cuadrito_179_sar), .siz(pixel_cuadrito_179_siz), .sde(c6[13]), .ZA_WARUDO(ZA_WARUDO),
    .reset(reset));  // open: in_7
  pixel_cuadrito pixel_cuadrito_180 (
    .clk(clk), .abajo(pixel_cuadrito_181_sar), .izq(c5[12]), .der(pixel_cuadrito_212_siz), .dir(dir),
    .sar(pixel_cuadrito_180_sar), .siz(pixel_cuadrito_180_siz), .sde(c6[12]), .ZA_WARUDO(ZA_WARUDO),
    .reset(reset));  // open: in_7
  pixel_cuadrito pixel_cuadrito_181 (
    .clk(clk), .abajo(pixel_cuadrito_182_sar), .izq(c5[11]), .der(pixel_cuadrito_213_siz), .dir(dir),
    .sar(pixel_cuadrito_181_sar), .siz(pixel_cuadrito_181_siz), .sde(c6[11]), .ZA_WARUDO(ZA_WARUDO),
    .reset(reset));  // open: in_7
  pixel_cuadrito pixel_cuadrito_182 (
    .clk(clk), .abajo(pixel_cuadrito_183_sar), .izq(c5[10]), .der(pixel_cuadrito_214_siz), .dir(dir),
    .sar(pixel_cuadrito_182_sar), .siz(pixel_cuadrito_182_siz), .sde(c6[10]), .ZA_WARUDO(ZA_WARUDO),
    .reset(reset));  // open: in_7
  pixel_cuadrito pixel_cuadrito_183 (
    .clk(clk), .abajo(pixel_cuadrito_184_sar), .izq(c5[9]), .der(pixel_cuadrito_215_siz), .dir(dir),
    .sar(pixel_cuadrito_183_sar), .siz(pixel_cuadrito_183_siz), .sde(c6[9]), .ZA_WARUDO(ZA_WARUDO),
    .reset(reset));  // open: in_7
  pixel_cuadrito pixel_cuadrito_184 (
    .clk(clk), .abajo(pixel_cuadrito_185_sar), .izq(c5[8]), .der(pixel_cuadrito_216_siz), .dir(dir),
    .sar(pixel_cuadrito_184_sar), .siz(pixel_cuadrito_184_siz), .sde(c6[8]), .ZA_WARUDO(ZA_WARUDO),
    .reset(reset));  // open: in_7
  pixel_cuadrito pixel_cuadrito_185 (
    .clk(clk), .abajo(pixel_cuadrito_186_sar), .izq(c5[7]), .der(pixel_cuadrito_217_siz), .dir(dir),
    .sar(pixel_cuadrito_185_sar), .siz(pixel_cuadrito_185_siz), .sde(c6[7]), .ZA_WARUDO(ZA_WARUDO),
    .reset(reset));  // open: in_7
  pixel_cuadrito pixel_cuadrito_186 (
    .clk(clk), .abajo(pixel_cuadrito_187_sar), .izq(c5[6]), .der(pixel_cuadrito_218_siz), .dir(dir),
    .sar(pixel_cuadrito_186_sar), .siz(pixel_cuadrito_186_siz), .sde(c6[6]), .ZA_WARUDO(ZA_WARUDO),
    .reset(reset));  // open: in_7
  pixel_cuadrito pixel_cuadrito_187 (
    .clk(clk), .abajo(pixel_cuadrito_188_sar), .izq(c5[5]), .der(pixel_cuadrito_219_siz), .dir(dir),
    .sar(pixel_cuadrito_187_sar), .siz(pixel_cuadrito_187_siz), .sde(c6[5]), .reset(reset));  // open: in_7, ZA_WARUDO
  pixel_cuadrito pixel_cuadrito_188 (
    .clk(clk), .abajo(pixel_cuadrito_189_sar), .izq(c5[4]), .der(pixel_cuadrito_220_siz), .dir(dir),
    .sar(pixel_cuadrito_188_sar), .siz(pixel_cuadrito_188_siz), .sde(c6[4]), .ZA_WARUDO(ZA_WARUDO),
    .reset(reset));  // open: in_7
  pixel_cuadrito pixel_cuadrito_189 (
    .clk(clk), .abajo(pixel_cuadrito_190_sar), .izq(c5[3]), .der(pixel_cuadrito_221_siz), .dir(dir),
    .sar(pixel_cuadrito_189_sar), .siz(pixel_cuadrito_189_siz), .sde(c6[3]), .ZA_WARUDO(ZA_WARUDO),
    .reset(reset));  // open: in_7
  pixel_cuadrito pixel_cuadrito_190 (
    .clk(clk), .abajo(pixel_cuadrito_191_sar), .izq(c5[2]), .der(pixel_cuadrito_222_siz), .dir(dir),
    .sar(pixel_cuadrito_190_sar), .siz(pixel_cuadrito_190_siz), .sde(c6[2]), .in_7(s5os6),
    .ZA_WARUDO(ZA_WARUDO), .reset(reset));
  pixel_cuadrito pixel_cuadrito_191 (
    .clk(clk), .abajo(pixel_cuadrito_192_sar), .izq(c5[1]), .der(pixel_cuadrito_223_siz), .dir(dir),
    .sar(pixel_cuadrito_191_sar), .siz(pixel_cuadrito_191_siz), .sde(c6[1]), .in_7(s5os6),
    .ZA_WARUDO(ZA_WARUDO), .reset(reset));
  pixel_cuadrito pixel_cuadrito_192 (
    .clk(clk), .abajo(c6[31]), .izq(c5[0]), .der(pixel_cuadrito_224_siz), .dir(dir),
    .sar(pixel_cuadrito_192_sar), .siz(pixel_cuadrito_192_siz), .sde(c6[0]), .ZA_WARUDO(ZA_WARUDO),
    .reset(reset));  // open: in_7
  Clock clock_1 (.out(clock_1_out));
  Random #(.width(4)) random_1 (.clk(clock_1_out), .next(1'b1), .out(random_1_out));  // open: clr
  pixel_cuadrito pixel_cuadrito_193 (
    .clk(clk), .abajo(pixel_cuadrito_194_sar), .izq(c6[31]), .der(pixel_cuadrito_225_siz), .dir(dir),
    .siz(pixel_cuadrito_193_siz), .sde(c7[31]), .ZA_WARUDO(ZA_WARUDO), .reset(reset));  // open: sar, in_7
  pixel_cuadrito pixel_cuadrito_194 (
    .clk(clk), .abajo(pixel_cuadrito_195_sar), .izq(c6[30]), .der(pixel_cuadrito_226_siz), .dir(dir),
    .sar(pixel_cuadrito_194_sar), .siz(pixel_cuadrito_194_siz), .sde(c7[30]), .ZA_WARUDO(ZA_WARUDO),
    .reset(reset));  // open: in_7
  pixel_cuadrito pixel_cuadrito_195 (
    .clk(clk), .abajo(pixel_cuadrito_196_sar), .izq(c6[29]), .der(pixel_cuadrito_227_siz), .dir(dir),
    .sar(pixel_cuadrito_195_sar), .siz(pixel_cuadrito_195_siz), .sde(c7[29]), .ZA_WARUDO(ZA_WARUDO),
    .reset(reset));  // open: in_7
  pixel_cuadrito pixel_cuadrito_196 (
    .clk(clk), .abajo(pixel_cuadrito_197_sar), .izq(c6[28]), .der(pixel_cuadrito_228_siz), .dir(dir),
    .sar(pixel_cuadrito_196_sar), .siz(pixel_cuadrito_196_siz), .sde(c7[28]), .ZA_WARUDO(ZA_WARUDO),
    .reset(reset));  // open: in_7
  pixel_cuadrito pixel_cuadrito_197 (
    .clk(clk), .abajo(pixel_cuadrito_198_sar), .izq(c6[27]), .der(pixel_cuadrito_229_siz), .dir(dir),
    .sar(pixel_cuadrito_197_sar), .siz(pixel_cuadrito_197_siz), .sde(c7[27]), .ZA_WARUDO(ZA_WARUDO),
    .reset(reset));  // open: in_7
  pixel_cuadrito pixel_cuadrito_198 (
    .clk(clk), .abajo(pixel_cuadrito_199_sar), .izq(c6[26]), .der(pixel_cuadrito_230_siz), .dir(dir),
    .sar(pixel_cuadrito_198_sar), .siz(pixel_cuadrito_198_siz), .sde(c7[26]), .ZA_WARUDO(ZA_WARUDO),
    .reset(reset));  // open: in_7
  pixel_cuadrito pixel_cuadrito_199 (
    .clk(clk), .abajo(pixel_cuadrito_200_sar), .izq(c6[25]), .der(pixel_cuadrito_231_siz), .dir(dir),
    .sar(pixel_cuadrito_199_sar), .siz(pixel_cuadrito_199_siz), .sde(c7[25]), .ZA_WARUDO(ZA_WARUDO),
    .reset(reset));  // open: in_7
  pixel_cuadrito pixel_cuadrito_200 (
    .clk(clk), .abajo(pixel_cuadrito_201_sar), .izq(c6[24]), .der(pixel_cuadrito_232_siz), .dir(dir),
    .sar(pixel_cuadrito_200_sar), .siz(pixel_cuadrito_200_siz), .sde(c7[24]), .ZA_WARUDO(ZA_WARUDO),
    .reset(reset));  // open: in_7
  pixel_cuadrito pixel_cuadrito_201 (
    .clk(clk), .abajo(pixel_cuadrito_202_sar), .izq(c6[23]), .der(pixel_cuadrito_233_siz), .dir(dir),
    .sar(pixel_cuadrito_201_sar), .siz(pixel_cuadrito_201_siz), .sde(c7[23]), .ZA_WARUDO(ZA_WARUDO),
    .reset(reset));  // open: in_7
  pixel_cuadrito pixel_cuadrito_202 (
    .clk(clk), .abajo(pixel_cuadrito_203_sar), .izq(c6[22]), .der(pixel_cuadrito_234_siz), .dir(dir),
    .sar(pixel_cuadrito_202_sar), .siz(pixel_cuadrito_202_siz), .sde(c7[22]), .ZA_WARUDO(ZA_WARUDO),
    .reset(reset));  // open: in_7
  pixel_cuadrito pixel_cuadrito_203 (
    .clk(clk), .abajo(pixel_cuadrito_204_sar), .izq(c6[21]), .der(pixel_cuadrito_235_siz), .dir(dir),
    .sar(pixel_cuadrito_203_sar), .siz(pixel_cuadrito_203_siz), .sde(c7[21]), .ZA_WARUDO(ZA_WARUDO),
    .reset(reset));  // open: in_7
  pixel_cuadrito pixel_cuadrito_204 (
    .clk(clk), .abajo(pixel_cuadrito_205_sar), .izq(c6[20]), .der(pixel_cuadrito_236_siz), .dir(dir),
    .sar(pixel_cuadrito_204_sar), .siz(pixel_cuadrito_204_siz), .sde(c7[20]), .ZA_WARUDO(ZA_WARUDO),
    .reset(reset));  // open: in_7
  pixel_cuadrito pixel_cuadrito_205 (
    .clk(clk), .abajo(pixel_cuadrito_206_sar), .izq(c6[19]), .der(pixel_cuadrito_237_siz), .dir(dir),
    .sar(pixel_cuadrito_205_sar), .siz(pixel_cuadrito_205_siz), .sde(c7[19]), .ZA_WARUDO(ZA_WARUDO),
    .reset(reset));  // open: in_7
  pixel_cuadrito pixel_cuadrito_206 (
    .clk(clk), .abajo(pixel_cuadrito_207_sar), .izq(c6[18]), .der(pixel_cuadrito_238_siz), .dir(dir),
    .sar(pixel_cuadrito_206_sar), .siz(pixel_cuadrito_206_siz), .sde(c7[18]), .ZA_WARUDO(ZA_WARUDO),
    .reset(reset));  // open: in_7
  pixel_cuadrito pixel_cuadrito_207 (
    .clk(clk), .abajo(pixel_cuadrito_208_sar), .izq(c6[17]), .der(pixel_cuadrito_239_siz), .dir(dir),
    .sar(pixel_cuadrito_207_sar), .siz(pixel_cuadrito_207_siz), .sde(c7[17]), .ZA_WARUDO(ZA_WARUDO),
    .reset(reset));  // open: in_7
  pixel_cuadrito pixel_cuadrito_208 (
    .clk(clk), .abajo(pixel_cuadrito_209_sar), .izq(c6[16]), .der(pixel_cuadrito_240_siz), .dir(dir),
    .sar(pixel_cuadrito_208_sar), .siz(pixel_cuadrito_208_siz), .sde(c7[16]), .ZA_WARUDO(ZA_WARUDO),
    .reset(reset));  // open: in_7
  pixel_cuadrito pixel_cuadrito_209 (
    .clk(clk), .abajo(pixel_cuadrito_210_sar), .izq(c6[15]), .der(pixel_cuadrito_241_siz), .dir(dir),
    .sar(pixel_cuadrito_209_sar), .siz(pixel_cuadrito_209_siz), .sde(c7[15]), .ZA_WARUDO(ZA_WARUDO),
    .reset(reset));  // open: in_7
  pixel_cuadrito pixel_cuadrito_210 (
    .clk(clk), .abajo(pixel_cuadrito_211_sar), .izq(c6[14]), .der(pixel_cuadrito_242_siz), .dir(dir),
    .sar(pixel_cuadrito_210_sar), .siz(pixel_cuadrito_210_siz), .sde(c7[14]), .ZA_WARUDO(ZA_WARUDO),
    .reset(reset));  // open: in_7
  pixel_cuadrito pixel_cuadrito_211 (
    .clk(clk), .abajo(pixel_cuadrito_212_sar), .izq(c6[13]), .der(pixel_cuadrito_243_siz), .dir(dir),
    .sar(pixel_cuadrito_211_sar), .siz(pixel_cuadrito_211_siz), .sde(c7[13]), .ZA_WARUDO(ZA_WARUDO),
    .reset(reset));  // open: in_7
  pixel_cuadrito pixel_cuadrito_212 (
    .clk(clk), .abajo(pixel_cuadrito_213_sar), .izq(c6[12]), .der(pixel_cuadrito_244_siz), .dir(dir),
    .sar(pixel_cuadrito_212_sar), .siz(pixel_cuadrito_212_siz), .sde(c7[12]), .ZA_WARUDO(ZA_WARUDO),
    .reset(reset));  // open: in_7
  pixel_cuadrito pixel_cuadrito_213 (
    .clk(clk), .abajo(pixel_cuadrito_214_sar), .izq(c6[11]), .der(pixel_cuadrito_245_siz), .dir(dir),
    .sar(pixel_cuadrito_213_sar), .siz(pixel_cuadrito_213_siz), .sde(c7[11]), .ZA_WARUDO(ZA_WARUDO),
    .reset(reset));  // open: in_7
  pixel_cuadrito pixel_cuadrito_214 (
    .clk(clk), .abajo(pixel_cuadrito_215_sar), .izq(c6[10]), .der(pixel_cuadrito_246_siz), .dir(dir),
    .sar(pixel_cuadrito_214_sar), .siz(pixel_cuadrito_214_siz), .sde(c7[10]), .ZA_WARUDO(ZA_WARUDO),
    .reset(reset));  // open: in_7
  pixel_cuadrito pixel_cuadrito_215 (
    .clk(clk), .abajo(pixel_cuadrito_216_sar), .izq(c6[9]), .der(pixel_cuadrito_247_siz), .dir(dir),
    .sar(pixel_cuadrito_215_sar), .siz(pixel_cuadrito_215_siz), .sde(c7[9]), .ZA_WARUDO(ZA_WARUDO),
    .reset(reset));  // open: in_7
  pixel_cuadrito pixel_cuadrito_216 (
    .clk(clk), .abajo(pixel_cuadrito_217_sar), .izq(c6[8]), .der(pixel_cuadrito_248_siz), .dir(dir),
    .sar(pixel_cuadrito_216_sar), .siz(pixel_cuadrito_216_siz), .sde(c7[8]), .ZA_WARUDO(ZA_WARUDO),
    .reset(reset));  // open: in_7
  pixel_cuadrito pixel_cuadrito_217 (
    .clk(clk), .abajo(pixel_cuadrito_218_sar), .izq(c6[7]), .der(pixel_cuadrito_249_siz), .dir(dir),
    .sar(pixel_cuadrito_217_sar), .siz(pixel_cuadrito_217_siz), .sde(c7[7]), .ZA_WARUDO(ZA_WARUDO),
    .reset(reset));  // open: in_7
  pixel_cuadrito pixel_cuadrito_218 (
    .clk(clk), .abajo(pixel_cuadrito_219_sar), .izq(c6[6]), .der(pixel_cuadrito_250_siz), .dir(dir),
    .sar(pixel_cuadrito_218_sar), .siz(pixel_cuadrito_218_siz), .sde(c7[6]), .ZA_WARUDO(ZA_WARUDO),
    .reset(reset));  // open: in_7
  pixel_cuadrito pixel_cuadrito_219 (
    .clk(clk), .abajo(pixel_cuadrito_220_sar), .izq(c6[5]), .der(pixel_cuadrito_251_siz), .dir(dir),
    .sar(pixel_cuadrito_219_sar), .siz(pixel_cuadrito_219_siz), .sde(c7[5]), .reset(reset));  // open: in_7, ZA_WARUDO
  pixel_cuadrito pixel_cuadrito_220 (
    .clk(clk), .abajo(pixel_cuadrito_221_sar), .izq(c6[4]), .der(pixel_cuadrito_252_siz), .dir(dir),
    .sar(pixel_cuadrito_220_sar), .siz(pixel_cuadrito_220_siz), .sde(c7[4]), .ZA_WARUDO(ZA_WARUDO),
    .reset(reset));  // open: in_7
  pixel_cuadrito pixel_cuadrito_221 (
    .clk(clk), .abajo(pixel_cuadrito_222_sar), .izq(c6[3]), .der(pixel_cuadrito_253_siz), .dir(dir),
    .sar(pixel_cuadrito_221_sar), .siz(pixel_cuadrito_221_siz), .sde(c7[3]), .ZA_WARUDO(ZA_WARUDO),
    .reset(reset));  // open: in_7
  pixel_cuadrito pixel_cuadrito_222 (
    .clk(clk), .abajo(pixel_cuadrito_223_sar), .izq(c6[2]), .der(pixel_cuadrito_254_siz), .dir(dir),
    .sar(pixel_cuadrito_222_sar), .siz(pixel_cuadrito_222_siz), .sde(c7[2]), .in_7(s6os7),
    .ZA_WARUDO(ZA_WARUDO), .reset(reset));
  pixel_cuadrito pixel_cuadrito_223 (
    .clk(clk), .abajo(pixel_cuadrito_224_sar), .izq(c6[1]), .der(pixel_cuadrito_255_siz), .dir(dir),
    .sar(pixel_cuadrito_223_sar), .siz(pixel_cuadrito_223_siz), .sde(c7[1]), .in_7(s6os7),
    .ZA_WARUDO(ZA_WARUDO), .reset(reset));
  pixel_cuadrito pixel_cuadrito_224 (
    .clk(clk), .abajo(c7[31]), .izq(c6[0]), .der(pixel_cuadrito_256_siz), .dir(dir),
    .sar(pixel_cuadrito_224_sar), .siz(pixel_cuadrito_224_siz), .sde(c7[0]), .ZA_WARUDO(ZA_WARUDO),
    .reset(reset));  // open: in_7
  Demultiplexer #(.select(4)) demultiplexer_1 (
    .out1(demultiplexer_1_out1), .out2(demultiplexer_1_out2), .out3(demultiplexer_1_out3),
    .out4(demultiplexer_1_out4), .out5(demultiplexer_1_out5), .out6(demultiplexer_1_out6),
    .out7(demultiplexer_1_out7), .out8(demultiplexer_1_out8), .out9(demultiplexer_1_out9),
    .out10(demultiplexer_1_out10), .out11(demultiplexer_1_out11), .out12(demultiplexer_1_out12),
    .out13(demultiplexer_1_out13), .out14(demultiplexer_1_out14), .out15(start16), .in(inf),
    .sel(random_1_out), .en(pos));  // open: out0
  pixel_cuadrito pixel_cuadrito_225 (
    .clk(clk), .abajo(pixel_cuadrito_226_sar), .izq(c7[31]), .der(pixel_cuadrito_257_siz), .dir(dir),
    .siz(pixel_cuadrito_225_siz), .sde(c8[31]), .ZA_WARUDO(ZA_WARUDO), .reset(reset));  // open: sar, in_7
  pixel_cuadrito pixel_cuadrito_226 (
    .clk(clk), .abajo(pixel_cuadrito_227_sar), .izq(c7[30]), .der(pixel_cuadrito_258_siz), .dir(dir),
    .sar(pixel_cuadrito_226_sar), .siz(pixel_cuadrito_226_siz), .sde(c8[30]), .ZA_WARUDO(ZA_WARUDO),
    .reset(reset));  // open: in_7
  pixel_cuadrito pixel_cuadrito_227 (
    .clk(clk), .abajo(pixel_cuadrito_228_sar), .izq(c7[29]), .der(pixel_cuadrito_259_siz), .dir(dir),
    .sar(pixel_cuadrito_227_sar), .siz(pixel_cuadrito_227_siz), .sde(c8[29]), .ZA_WARUDO(ZA_WARUDO),
    .reset(reset));  // open: in_7
  pixel_cuadrito pixel_cuadrito_228 (
    .clk(clk), .abajo(pixel_cuadrito_229_sar), .izq(c7[28]), .der(pixel_cuadrito_260_siz), .dir(dir),
    .sar(pixel_cuadrito_228_sar), .siz(pixel_cuadrito_228_siz), .sde(c8[28]), .ZA_WARUDO(ZA_WARUDO),
    .reset(reset));  // open: in_7
  pixel_cuadrito pixel_cuadrito_229 (
    .clk(clk), .abajo(pixel_cuadrito_230_sar), .izq(c7[27]), .der(pixel_cuadrito_261_siz), .dir(dir),
    .sar(pixel_cuadrito_229_sar), .siz(pixel_cuadrito_229_siz), .sde(c8[27]), .ZA_WARUDO(ZA_WARUDO),
    .reset(reset));  // open: in_7
  pixel_cuadrito pixel_cuadrito_230 (
    .clk(clk), .abajo(pixel_cuadrito_231_sar), .izq(c7[26]), .der(pixel_cuadrito_262_siz), .dir(dir),
    .sar(pixel_cuadrito_230_sar), .siz(pixel_cuadrito_230_siz), .sde(c8[26]), .ZA_WARUDO(ZA_WARUDO),
    .reset(reset));  // open: in_7
  pixel_cuadrito pixel_cuadrito_231 (
    .clk(clk), .abajo(pixel_cuadrito_232_sar), .izq(c7[25]), .der(pixel_cuadrito_263_siz), .dir(dir),
    .sar(pixel_cuadrito_231_sar), .siz(pixel_cuadrito_231_siz), .sde(c8[25]), .ZA_WARUDO(ZA_WARUDO),
    .reset(reset));  // open: in_7
  pixel_cuadrito pixel_cuadrito_232 (
    .clk(clk), .abajo(pixel_cuadrito_233_sar), .izq(c7[24]), .der(pixel_cuadrito_264_siz), .dir(dir),
    .sar(pixel_cuadrito_232_sar), .siz(pixel_cuadrito_232_siz), .sde(c8[24]), .ZA_WARUDO(ZA_WARUDO),
    .reset(reset));  // open: in_7
  pixel_cuadrito pixel_cuadrito_233 (
    .clk(clk), .abajo(pixel_cuadrito_234_sar), .izq(c7[23]), .der(pixel_cuadrito_265_siz), .dir(dir),
    .sar(pixel_cuadrito_233_sar), .siz(pixel_cuadrito_233_siz), .sde(c8[23]), .ZA_WARUDO(ZA_WARUDO),
    .reset(reset));  // open: in_7
  pixel_cuadrito pixel_cuadrito_234 (
    .clk(clk), .abajo(pixel_cuadrito_235_sar), .izq(c7[22]), .der(pixel_cuadrito_266_siz), .dir(dir),
    .sar(pixel_cuadrito_234_sar), .siz(pixel_cuadrito_234_siz), .sde(c8[22]), .ZA_WARUDO(ZA_WARUDO),
    .reset(reset));  // open: in_7
  pixel_cuadrito pixel_cuadrito_235 (
    .clk(clk), .abajo(pixel_cuadrito_236_sar), .izq(c7[21]), .der(pixel_cuadrito_267_siz), .dir(dir),
    .sar(pixel_cuadrito_235_sar), .siz(pixel_cuadrito_235_siz), .sde(c8[21]), .ZA_WARUDO(ZA_WARUDO),
    .reset(reset));  // open: in_7
  pixel_cuadrito pixel_cuadrito_236 (
    .clk(clk), .abajo(pixel_cuadrito_237_sar), .izq(c7[20]), .der(pixel_cuadrito_268_siz), .dir(dir),
    .sar(pixel_cuadrito_236_sar), .siz(pixel_cuadrito_236_siz), .sde(c8[20]), .ZA_WARUDO(ZA_WARUDO),
    .reset(reset));  // open: in_7
  pixel_cuadrito pixel_cuadrito_237 (
    .clk(clk), .abajo(pixel_cuadrito_238_sar), .izq(c7[19]), .der(pixel_cuadrito_269_siz), .dir(dir),
    .sar(pixel_cuadrito_237_sar), .siz(pixel_cuadrito_237_siz), .sde(c8[19]), .ZA_WARUDO(ZA_WARUDO),
    .reset(reset));  // open: in_7
  pixel_cuadrito pixel_cuadrito_238 (
    .clk(clk), .abajo(pixel_cuadrito_239_sar), .izq(c7[18]), .der(pixel_cuadrito_270_siz), .dir(dir),
    .sar(pixel_cuadrito_238_sar), .siz(pixel_cuadrito_238_siz), .sde(c8[18]), .ZA_WARUDO(ZA_WARUDO),
    .reset(reset));  // open: in_7
  pixel_cuadrito pixel_cuadrito_239 (
    .clk(clk), .abajo(pixel_cuadrito_240_sar), .izq(c7[17]), .der(pixel_cuadrito_271_siz), .dir(dir),
    .sar(pixel_cuadrito_239_sar), .siz(pixel_cuadrito_239_siz), .sde(c8[17]), .ZA_WARUDO(ZA_WARUDO),
    .reset(reset));  // open: in_7
  pixel_cuadrito pixel_cuadrito_240 (
    .clk(clk), .abajo(pixel_cuadrito_241_sar), .izq(c7[16]), .der(pixel_cuadrito_272_siz), .dir(dir),
    .sar(pixel_cuadrito_240_sar), .siz(pixel_cuadrito_240_siz), .sde(c8[16]), .ZA_WARUDO(ZA_WARUDO),
    .reset(reset));  // open: in_7
  pixel_cuadrito pixel_cuadrito_241 (
    .clk(clk), .abajo(pixel_cuadrito_242_sar), .izq(c7[15]), .der(pixel_cuadrito_273_siz), .dir(dir),
    .sar(pixel_cuadrito_241_sar), .siz(pixel_cuadrito_241_siz), .sde(c8[15]), .ZA_WARUDO(ZA_WARUDO),
    .reset(reset));  // open: in_7
  pixel_cuadrito pixel_cuadrito_242 (
    .clk(clk), .abajo(pixel_cuadrito_243_sar), .izq(c7[14]), .der(pixel_cuadrito_274_siz), .dir(dir),
    .sar(pixel_cuadrito_242_sar), .siz(pixel_cuadrito_242_siz), .sde(c8[14]), .ZA_WARUDO(ZA_WARUDO),
    .reset(reset));  // open: in_7
  pixel_cuadrito pixel_cuadrito_243 (
    .clk(clk), .abajo(pixel_cuadrito_244_sar), .izq(c7[13]), .der(pixel_cuadrito_275_siz), .dir(dir),
    .sar(pixel_cuadrito_243_sar), .siz(pixel_cuadrito_243_siz), .sde(c8[13]), .ZA_WARUDO(ZA_WARUDO),
    .reset(reset));  // open: in_7
  pixel_cuadrito pixel_cuadrito_244 (
    .clk(clk), .abajo(pixel_cuadrito_245_sar), .izq(c7[12]), .der(pixel_cuadrito_276_siz), .dir(dir),
    .sar(pixel_cuadrito_244_sar), .siz(pixel_cuadrito_244_siz), .sde(c8[12]), .ZA_WARUDO(ZA_WARUDO),
    .reset(reset));  // open: in_7
  pixel_cuadrito pixel_cuadrito_245 (
    .clk(clk), .abajo(pixel_cuadrito_246_sar), .izq(c7[11]), .der(pixel_cuadrito_277_siz), .dir(dir),
    .sar(pixel_cuadrito_245_sar), .siz(pixel_cuadrito_245_siz), .sde(c8[11]), .ZA_WARUDO(ZA_WARUDO),
    .reset(reset));  // open: in_7
  pixel_cuadrito pixel_cuadrito_246 (
    .clk(clk), .abajo(pixel_cuadrito_247_sar), .izq(c7[10]), .der(pixel_cuadrito_278_siz), .dir(dir),
    .sar(pixel_cuadrito_246_sar), .siz(pixel_cuadrito_246_siz), .sde(c8[10]), .ZA_WARUDO(ZA_WARUDO),
    .reset(reset));  // open: in_7
  pixel_cuadrito pixel_cuadrito_247 (
    .clk(clk), .abajo(pixel_cuadrito_248_sar), .izq(c7[9]), .der(pixel_cuadrito_279_siz), .dir(dir),
    .sar(pixel_cuadrito_247_sar), .siz(pixel_cuadrito_247_siz), .sde(c8[9]), .ZA_WARUDO(ZA_WARUDO),
    .reset(reset));  // open: in_7
  pixel_cuadrito pixel_cuadrito_248 (
    .clk(clk), .abajo(pixel_cuadrito_249_sar), .izq(c7[8]), .der(pixel_cuadrito_280_siz), .dir(dir),
    .sar(pixel_cuadrito_248_sar), .siz(pixel_cuadrito_248_siz), .sde(c8[8]), .ZA_WARUDO(ZA_WARUDO),
    .reset(reset));  // open: in_7
  pixel_cuadrito pixel_cuadrito_249 (
    .clk(clk), .abajo(pixel_cuadrito_250_sar), .izq(c7[7]), .der(pixel_cuadrito_281_siz), .dir(dir),
    .sar(pixel_cuadrito_249_sar), .siz(pixel_cuadrito_249_siz), .sde(c8[7]), .ZA_WARUDO(ZA_WARUDO),
    .reset(reset));  // open: in_7
  pixel_cuadrito pixel_cuadrito_250 (
    .clk(clk), .abajo(pixel_cuadrito_251_sar), .izq(c7[6]), .der(pixel_cuadrito_282_siz), .dir(dir),
    .sar(pixel_cuadrito_250_sar), .siz(pixel_cuadrito_250_siz), .sde(c8[6]), .ZA_WARUDO(ZA_WARUDO),
    .reset(reset));  // open: in_7
  pixel_cuadrito pixel_cuadrito_251 (
    .clk(clk), .abajo(pixel_cuadrito_252_sar), .izq(c7[5]), .der(pixel_cuadrito_283_siz), .dir(dir),
    .sar(pixel_cuadrito_251_sar), .siz(pixel_cuadrito_251_siz), .sde(c8[5]), .ZA_WARUDO(ZA_WARUDO),
    .reset(reset));  // open: in_7
  pixel_cuadrito pixel_cuadrito_252 (
    .clk(clk), .abajo(pixel_cuadrito_253_sar), .izq(c7[4]), .der(pixel_cuadrito_284_siz), .dir(dir),
    .sar(pixel_cuadrito_252_sar), .siz(pixel_cuadrito_252_siz), .sde(c8[4]), .ZA_WARUDO(ZA_WARUDO),
    .reset(reset));  // open: in_7
  pixel_cuadrito pixel_cuadrito_253 (
    .clk(clk), .abajo(pixel_cuadrito_254_sar), .izq(c7[3]), .der(pixel_cuadrito_285_siz), .dir(dir),
    .sar(pixel_cuadrito_253_sar), .siz(pixel_cuadrito_253_siz), .sde(c8[3]), .ZA_WARUDO(ZA_WARUDO),
    .reset(reset));  // open: in_7
  pixel_cuadrito pixel_cuadrito_254 (
    .clk(clk), .abajo(pixel_cuadrito_255_sar), .izq(c7[2]), .der(pixel_cuadrito_286_siz), .dir(dir),
    .sar(pixel_cuadrito_254_sar), .siz(pixel_cuadrito_254_siz), .sde(c8[2]), .in_7(s7os8),
    .ZA_WARUDO(ZA_WARUDO), .reset(reset));
  pixel_cuadrito pixel_cuadrito_255 (
    .clk(clk), .abajo(pixel_cuadrito_256_sar), .izq(c7[1]), .der(pixel_cuadrito_287_siz), .dir(dir),
    .sar(pixel_cuadrito_255_sar), .siz(pixel_cuadrito_255_siz), .sde(c8[1]), .in_7(s7os8),
    .ZA_WARUDO(ZA_WARUDO), .reset(reset));
  pixel_cuadrito pixel_cuadrito_256 (
    .clk(clk), .abajo(c8[31]), .izq(c7[0]), .der(pixel_cuadrito_288_siz), .dir(dir),
    .sar(pixel_cuadrito_256_sar), .siz(pixel_cuadrito_256_siz), .sde(c8[0]), .ZA_WARUDO(ZA_WARUDO),
    .reset(reset));  // open: in_7
  pixel_cuadrito pixel_cuadrito_257 (
    .clk(clk), .abajo(pixel_cuadrito_258_sar), .izq(c8[31]), .der(pixel_cuadrito_289_siz), .dir(dir),
    .siz(pixel_cuadrito_257_siz), .sde(c9[31]), .ZA_WARUDO(ZA_WARUDO), .reset(reset));  // open: sar, in_7
  pixel_cuadrito pixel_cuadrito_258 (
    .clk(clk), .abajo(pixel_cuadrito_259_sar), .izq(c8[30]), .der(pixel_cuadrito_290_siz), .dir(dir),
    .sar(pixel_cuadrito_258_sar), .siz(pixel_cuadrito_258_siz), .sde(c9[30]), .ZA_WARUDO(ZA_WARUDO),
    .reset(reset));  // open: in_7
  pixel_cuadrito pixel_cuadrito_259 (
    .clk(clk), .abajo(pixel_cuadrito_260_sar), .izq(c8[29]), .der(pixel_cuadrito_291_siz), .dir(dir),
    .sar(pixel_cuadrito_259_sar), .siz(pixel_cuadrito_259_siz), .sde(c9[29]), .ZA_WARUDO(ZA_WARUDO),
    .reset(reset));  // open: in_7
  pixel_cuadrito pixel_cuadrito_260 (
    .clk(clk), .abajo(pixel_cuadrito_261_sar), .izq(c8[28]), .der(pixel_cuadrito_292_siz), .dir(dir),
    .sar(pixel_cuadrito_260_sar), .siz(pixel_cuadrito_260_siz), .sde(c9[28]), .ZA_WARUDO(ZA_WARUDO),
    .reset(reset));  // open: in_7
  pixel_cuadrito pixel_cuadrito_261 (
    .clk(clk), .abajo(pixel_cuadrito_262_sar), .izq(c8[27]), .der(pixel_cuadrito_293_siz), .dir(dir),
    .sar(pixel_cuadrito_261_sar), .siz(pixel_cuadrito_261_siz), .sde(c9[27]), .ZA_WARUDO(ZA_WARUDO),
    .reset(reset));  // open: in_7
  pixel_cuadrito pixel_cuadrito_262 (
    .clk(clk), .abajo(pixel_cuadrito_263_sar), .izq(c8[26]), .der(pixel_cuadrito_294_siz), .dir(dir),
    .sar(pixel_cuadrito_262_sar), .siz(pixel_cuadrito_262_siz), .sde(c9[26]), .ZA_WARUDO(ZA_WARUDO),
    .reset(reset));  // open: in_7
  pixel_cuadrito pixel_cuadrito_263 (
    .clk(clk), .abajo(pixel_cuadrito_264_sar), .izq(c8[25]), .der(pixel_cuadrito_295_siz), .dir(dir),
    .sar(pixel_cuadrito_263_sar), .siz(pixel_cuadrito_263_siz), .sde(c9[25]), .ZA_WARUDO(ZA_WARUDO),
    .reset(reset));  // open: in_7
  pixel_cuadrito pixel_cuadrito_264 (
    .clk(clk), .abajo(pixel_cuadrito_265_sar), .izq(c8[24]), .der(pixel_cuadrito_296_siz), .dir(dir),
    .sar(pixel_cuadrito_264_sar), .siz(pixel_cuadrito_264_siz), .sde(c9[24]), .ZA_WARUDO(ZA_WARUDO),
    .reset(reset));  // open: in_7
  pixel_cuadrito pixel_cuadrito_265 (
    .clk(clk), .abajo(pixel_cuadrito_266_sar), .izq(c8[23]), .der(pixel_cuadrito_297_siz), .dir(dir),
    .sar(pixel_cuadrito_265_sar), .siz(pixel_cuadrito_265_siz), .sde(c9[23]), .ZA_WARUDO(ZA_WARUDO),
    .reset(reset));  // open: in_7
  pixel_cuadrito pixel_cuadrito_266 (
    .clk(clk), .abajo(pixel_cuadrito_267_sar), .izq(c8[22]), .der(pixel_cuadrito_298_siz), .dir(dir),
    .sar(pixel_cuadrito_266_sar), .siz(pixel_cuadrito_266_siz), .sde(c9[22]), .ZA_WARUDO(ZA_WARUDO),
    .reset(reset));  // open: in_7
  pixel_cuadrito pixel_cuadrito_267 (
    .clk(clk), .abajo(pixel_cuadrito_268_sar), .izq(c8[21]), .der(pixel_cuadrito_299_siz), .dir(dir),
    .sar(pixel_cuadrito_267_sar), .siz(pixel_cuadrito_267_siz), .sde(c9[21]), .ZA_WARUDO(ZA_WARUDO),
    .reset(reset));  // open: in_7
  pixel_cuadrito pixel_cuadrito_268 (
    .clk(clk), .abajo(pixel_cuadrito_269_sar), .izq(c8[20]), .der(pixel_cuadrito_300_siz), .dir(dir),
    .sar(pixel_cuadrito_268_sar), .siz(pixel_cuadrito_268_siz), .sde(c9[20]), .ZA_WARUDO(ZA_WARUDO),
    .reset(reset));  // open: in_7
  pixel_cuadrito pixel_cuadrito_269 (
    .clk(clk), .abajo(pixel_cuadrito_270_sar), .izq(c8[19]), .der(pixel_cuadrito_301_siz), .dir(dir),
    .sar(pixel_cuadrito_269_sar), .siz(pixel_cuadrito_269_siz), .sde(c9[19]), .ZA_WARUDO(ZA_WARUDO),
    .reset(reset));  // open: in_7
  pixel_cuadrito pixel_cuadrito_270 (
    .clk(clk), .abajo(pixel_cuadrito_271_sar), .izq(c8[18]), .der(pixel_cuadrito_302_siz), .dir(dir),
    .sar(pixel_cuadrito_270_sar), .siz(pixel_cuadrito_270_siz), .sde(c9[18]), .ZA_WARUDO(ZA_WARUDO),
    .reset(reset));  // open: in_7
  pixel_cuadrito pixel_cuadrito_271 (
    .clk(clk), .abajo(pixel_cuadrito_272_sar), .izq(c8[17]), .der(pixel_cuadrito_303_siz), .dir(dir),
    .sar(pixel_cuadrito_271_sar), .siz(pixel_cuadrito_271_siz), .sde(c9[17]), .ZA_WARUDO(ZA_WARUDO),
    .reset(reset));  // open: in_7
  pixel_cuadrito pixel_cuadrito_272 (
    .clk(clk), .abajo(pixel_cuadrito_273_sar), .izq(c8[16]), .der(pixel_cuadrito_304_siz), .dir(dir),
    .sar(pixel_cuadrito_272_sar), .siz(pixel_cuadrito_272_siz), .sde(c9[16]), .ZA_WARUDO(ZA_WARUDO),
    .reset(reset));  // open: in_7
  pixel_cuadrito pixel_cuadrito_273 (
    .clk(clk), .abajo(pixel_cuadrito_274_sar), .izq(c8[15]), .der(pixel_cuadrito_305_siz), .dir(dir),
    .sar(pixel_cuadrito_273_sar), .siz(pixel_cuadrito_273_siz), .sde(c9[15]), .ZA_WARUDO(ZA_WARUDO),
    .reset(reset));  // open: in_7
  pixel_cuadrito pixel_cuadrito_274 (
    .clk(clk), .abajo(pixel_cuadrito_275_sar), .izq(c8[14]), .der(pixel_cuadrito_306_siz), .dir(dir),
    .sar(pixel_cuadrito_274_sar), .siz(pixel_cuadrito_274_siz), .sde(c9[14]), .ZA_WARUDO(ZA_WARUDO),
    .reset(reset));  // open: in_7
  pixel_cuadrito pixel_cuadrito_275 (
    .clk(clk), .abajo(pixel_cuadrito_276_sar), .izq(c8[13]), .der(pixel_cuadrito_307_siz), .dir(dir),
    .sar(pixel_cuadrito_275_sar), .siz(pixel_cuadrito_275_siz), .sde(c9[13]), .ZA_WARUDO(ZA_WARUDO),
    .reset(reset));  // open: in_7
  pixel_cuadrito pixel_cuadrito_276 (
    .clk(clk), .abajo(pixel_cuadrito_277_sar), .izq(c8[12]), .der(pixel_cuadrito_308_siz), .dir(dir),
    .sar(pixel_cuadrito_276_sar), .siz(pixel_cuadrito_276_siz), .sde(c9[12]), .ZA_WARUDO(ZA_WARUDO),
    .reset(reset));  // open: in_7
  pixel_cuadrito pixel_cuadrito_277 (
    .clk(clk), .abajo(pixel_cuadrito_278_sar), .izq(c8[11]), .der(pixel_cuadrito_309_siz), .dir(dir),
    .sar(pixel_cuadrito_277_sar), .siz(pixel_cuadrito_277_siz), .sde(c9[11]), .ZA_WARUDO(ZA_WARUDO),
    .reset(reset));  // open: in_7
  pixel_cuadrito pixel_cuadrito_278 (
    .clk(clk), .abajo(pixel_cuadrito_279_sar), .izq(c8[10]), .der(pixel_cuadrito_310_siz), .dir(dir),
    .sar(pixel_cuadrito_278_sar), .siz(pixel_cuadrito_278_siz), .sde(c9[10]), .ZA_WARUDO(ZA_WARUDO),
    .reset(reset));  // open: in_7
  pixel_cuadrito pixel_cuadrito_279 (
    .clk(clk), .abajo(pixel_cuadrito_280_sar), .izq(c8[9]), .der(pixel_cuadrito_311_siz), .dir(dir),
    .sar(pixel_cuadrito_279_sar), .siz(pixel_cuadrito_279_siz), .sde(c9[9]), .ZA_WARUDO(ZA_WARUDO),
    .reset(reset));  // open: in_7
  pixel_cuadrito pixel_cuadrito_280 (
    .clk(clk), .abajo(pixel_cuadrito_281_sar), .izq(c8[8]), .der(pixel_cuadrito_312_siz), .dir(dir),
    .sar(pixel_cuadrito_280_sar), .siz(pixel_cuadrito_280_siz), .sde(c9[8]), .ZA_WARUDO(ZA_WARUDO),
    .reset(reset));  // open: in_7
  pixel_cuadrito pixel_cuadrito_281 (
    .clk(clk), .abajo(pixel_cuadrito_282_sar), .izq(c8[7]), .der(pixel_cuadrito_313_siz), .dir(dir),
    .sar(pixel_cuadrito_281_sar), .siz(pixel_cuadrito_281_siz), .sde(c9[7]), .ZA_WARUDO(ZA_WARUDO),
    .reset(reset));  // open: in_7
  pixel_cuadrito pixel_cuadrito_282 (
    .clk(clk), .abajo(pixel_cuadrito_283_sar), .izq(c8[6]), .der(pixel_cuadrito_314_siz), .dir(dir),
    .sar(pixel_cuadrito_282_sar), .siz(pixel_cuadrito_282_siz), .sde(c9[6]), .ZA_WARUDO(ZA_WARUDO),
    .reset(reset));  // open: in_7
  pixel_cuadrito pixel_cuadrito_283 (
    .clk(clk), .abajo(pixel_cuadrito_284_sar), .izq(c8[5]), .der(pixel_cuadrito_315_siz), .dir(dir),
    .sar(pixel_cuadrito_283_sar), .siz(pixel_cuadrito_283_siz), .sde(c9[5]), .ZA_WARUDO(ZA_WARUDO),
    .reset(reset));  // open: in_7
  pixel_cuadrito pixel_cuadrito_284 (
    .clk(clk), .abajo(pixel_cuadrito_285_sar), .izq(c8[4]), .der(pixel_cuadrito_316_siz), .dir(dir),
    .sar(pixel_cuadrito_284_sar), .siz(pixel_cuadrito_284_siz), .sde(c9[4]), .ZA_WARUDO(ZA_WARUDO),
    .reset(reset));  // open: in_7
  pixel_cuadrito pixel_cuadrito_285 (
    .clk(clk), .abajo(pixel_cuadrito_286_sar), .izq(c8[3]), .der(pixel_cuadrito_317_siz), .dir(dir),
    .sar(pixel_cuadrito_285_sar), .siz(pixel_cuadrito_285_siz), .sde(c9[3]), .ZA_WARUDO(ZA_WARUDO),
    .reset(reset));  // open: in_7
  pixel_cuadrito pixel_cuadrito_286 (
    .clk(clk), .abajo(pixel_cuadrito_287_sar), .izq(c8[2]), .der(pixel_cuadrito_318_siz), .dir(dir),
    .sar(pixel_cuadrito_286_sar), .siz(pixel_cuadrito_286_siz), .sde(c9[2]), .in_7(s8os9),
    .ZA_WARUDO(ZA_WARUDO), .reset(reset));
  pixel_cuadrito pixel_cuadrito_287 (
    .clk(clk), .abajo(pixel_cuadrito_288_sar), .izq(c8[1]), .der(pixel_cuadrito_319_siz), .dir(dir),
    .sar(pixel_cuadrito_287_sar), .siz(pixel_cuadrito_287_siz), .sde(c9[1]), .in_7(s8os9),
    .ZA_WARUDO(ZA_WARUDO), .reset(reset));
  pixel_cuadrito pixel_cuadrito_288 (
    .clk(clk), .abajo(c9[31]), .izq(c8[0]), .der(pixel_cuadrito_320_siz), .dir(dir),
    .sar(pixel_cuadrito_288_sar), .siz(pixel_cuadrito_288_siz), .sde(c9[0]), .ZA_WARUDO(ZA_WARUDO),
    .reset(reset));  // open: in_7
  or or_1 (s1os2, demultiplexer_1_out1, demultiplexer_1_out2);
  or or_2 (s2os3, demultiplexer_1_out2, demultiplexer_1_out3);
  or or_3 (s3os4, demultiplexer_1_out3, demultiplexer_1_out4);
  or or_4 (s4os5, demultiplexer_1_out4, demultiplexer_1_out5);
  or or_5 (s5os6, demultiplexer_1_out5, demultiplexer_1_out6);
  or or_6 (s6os7, demultiplexer_1_out6, demultiplexer_1_out7);
  or or_7 (s7os8, demultiplexer_1_out7, demultiplexer_1_out8);
  or or_8 (s8os9, demultiplexer_1_out8, demultiplexer_1_out9);
  or or_9 (s9os10, demultiplexer_1_out9, demultiplexer_1_out10);
  or or_10 (s10os11, demultiplexer_1_out10, demultiplexer_1_out11);
  or or_11 (s11os12, demultiplexer_1_out11, demultiplexer_1_out12);
  or or_12 (s12os13, demultiplexer_1_out12, demultiplexer_1_out13);
  or or_13 (s13os14, demultiplexer_1_out13, demultiplexer_1_out14);
  or or_14 (s14os15, demultiplexer_1_out14, start16);
  pixel_cuadrito pixel_cuadrito_289 (
    .clk(clk), .abajo(pixel_cuadrito_290_sar), .izq(c9[31]), .der(pixel_cuadrito_321_siz), .dir(dir),
    .siz(pixel_cuadrito_289_siz), .sde(c10[31]), .ZA_WARUDO(ZA_WARUDO), .reset(reset));  // open: sar, in_7
  pixel_cuadrito pixel_cuadrito_290 (
    .clk(clk), .abajo(pixel_cuadrito_291_sar), .izq(c9[30]), .der(pixel_cuadrito_322_siz), .dir(dir),
    .sar(pixel_cuadrito_290_sar), .siz(pixel_cuadrito_290_siz), .sde(c10[30]), .ZA_WARUDO(ZA_WARUDO),
    .reset(reset));  // open: in_7
  pixel_cuadrito pixel_cuadrito_291 (
    .clk(clk), .abajo(pixel_cuadrito_292_sar), .izq(c9[29]), .der(pixel_cuadrito_323_siz), .dir(dir),
    .sar(pixel_cuadrito_291_sar), .siz(pixel_cuadrito_291_siz), .sde(c10[29]), .ZA_WARUDO(ZA_WARUDO),
    .reset(reset));  // open: in_7
  pixel_cuadrito pixel_cuadrito_292 (
    .clk(clk), .abajo(pixel_cuadrito_293_sar), .izq(c9[28]), .der(pixel_cuadrito_324_siz), .dir(dir),
    .sar(pixel_cuadrito_292_sar), .siz(pixel_cuadrito_292_siz), .sde(c10[28]), .reset(reset));  // open: in_7, ZA_WARUDO
  pixel_cuadrito pixel_cuadrito_293 (
    .clk(clk), .abajo(pixel_cuadrito_294_sar), .izq(c9[27]), .der(pixel_cuadrito_325_siz), .dir(dir),
    .sar(pixel_cuadrito_293_sar), .siz(pixel_cuadrito_293_siz), .sde(c10[27]), .ZA_WARUDO(ZA_WARUDO),
    .reset(reset));  // open: in_7
  pixel_cuadrito pixel_cuadrito_294 (
    .clk(clk), .abajo(pixel_cuadrito_295_sar), .izq(c9[26]), .der(pixel_cuadrito_326_siz), .dir(dir),
    .sar(pixel_cuadrito_294_sar), .siz(pixel_cuadrito_294_siz), .sde(c10[26]), .ZA_WARUDO(ZA_WARUDO),
    .reset(reset));  // open: in_7
  pixel_cuadrito pixel_cuadrito_295 (
    .clk(clk), .abajo(pixel_cuadrito_296_sar), .izq(c9[25]), .der(pixel_cuadrito_327_siz), .dir(dir),
    .sar(pixel_cuadrito_295_sar), .siz(pixel_cuadrito_295_siz), .sde(c10[25]), .ZA_WARUDO(ZA_WARUDO),
    .reset(reset));  // open: in_7
  pixel_cuadrito pixel_cuadrito_296 (
    .clk(clk), .abajo(pixel_cuadrito_297_sar), .izq(c9[24]), .der(pixel_cuadrito_328_siz), .dir(dir),
    .sar(pixel_cuadrito_296_sar), .siz(pixel_cuadrito_296_siz), .sde(c10[24]), .ZA_WARUDO(ZA_WARUDO),
    .reset(reset));  // open: in_7
  pixel_cuadrito pixel_cuadrito_297 (
    .clk(clk), .abajo(pixel_cuadrito_298_sar), .izq(c9[23]), .der(pixel_cuadrito_329_siz), .dir(dir),
    .sar(pixel_cuadrito_297_sar), .siz(pixel_cuadrito_297_siz), .sde(c10[23]), .ZA_WARUDO(ZA_WARUDO),
    .reset(reset));  // open: in_7
  pixel_cuadrito pixel_cuadrito_298 (
    .clk(clk), .abajo(pixel_cuadrito_299_sar), .izq(c9[22]), .der(pixel_cuadrito_330_siz), .dir(dir),
    .sar(pixel_cuadrito_298_sar), .siz(pixel_cuadrito_298_siz), .sde(c10[22]), .ZA_WARUDO(ZA_WARUDO),
    .reset(reset));  // open: in_7
  pixel_cuadrito pixel_cuadrito_299 (
    .clk(clk), .abajo(pixel_cuadrito_300_sar), .izq(c9[21]), .der(pixel_cuadrito_331_siz), .dir(dir),
    .sar(pixel_cuadrito_299_sar), .siz(pixel_cuadrito_299_siz), .sde(c10[21]), .ZA_WARUDO(ZA_WARUDO),
    .reset(reset));  // open: in_7
  pixel_cuadrito pixel_cuadrito_300 (
    .clk(clk), .abajo(pixel_cuadrito_301_sar), .izq(c9[20]), .der(pixel_cuadrito_332_siz), .dir(dir),
    .sar(pixel_cuadrito_300_sar), .siz(pixel_cuadrito_300_siz), .sde(c10[20]), .ZA_WARUDO(ZA_WARUDO),
    .reset(reset));  // open: in_7
  pixel_cuadrito pixel_cuadrito_301 (
    .clk(clk), .abajo(pixel_cuadrito_302_sar), .izq(c9[19]), .der(pixel_cuadrito_333_siz), .dir(dir),
    .sar(pixel_cuadrito_301_sar), .siz(pixel_cuadrito_301_siz), .sde(c10[19]), .ZA_WARUDO(ZA_WARUDO),
    .reset(reset));  // open: in_7
  pixel_cuadrito pixel_cuadrito_302 (
    .clk(clk), .abajo(pixel_cuadrito_303_sar), .izq(c9[18]), .der(pixel_cuadrito_334_siz), .dir(dir),
    .sar(pixel_cuadrito_302_sar), .siz(pixel_cuadrito_302_siz), .sde(c10[18]), .ZA_WARUDO(ZA_WARUDO),
    .reset(reset));  // open: in_7
  pixel_cuadrito pixel_cuadrito_303 (
    .clk(clk), .abajo(pixel_cuadrito_304_sar), .izq(c9[17]), .der(pixel_cuadrito_335_siz), .dir(dir),
    .sar(pixel_cuadrito_303_sar), .siz(pixel_cuadrito_303_siz), .sde(c10[17]), .ZA_WARUDO(ZA_WARUDO),
    .reset(reset));  // open: in_7
  pixel_cuadrito pixel_cuadrito_304 (
    .clk(clk), .abajo(pixel_cuadrito_305_sar), .izq(c9[16]), .der(pixel_cuadrito_336_siz), .dir(dir),
    .sar(pixel_cuadrito_304_sar), .siz(pixel_cuadrito_304_siz), .sde(c10[16]), .ZA_WARUDO(ZA_WARUDO),
    .reset(reset));  // open: in_7
  pixel_cuadrito pixel_cuadrito_305 (
    .clk(clk), .abajo(pixel_cuadrito_306_sar), .izq(c9[15]), .der(pixel_cuadrito_337_siz), .dir(dir),
    .sar(pixel_cuadrito_305_sar), .siz(pixel_cuadrito_305_siz), .sde(c10[15]), .ZA_WARUDO(ZA_WARUDO),
    .reset(reset));  // open: in_7
  pixel_cuadrito pixel_cuadrito_306 (
    .clk(clk), .abajo(pixel_cuadrito_307_sar), .izq(c9[14]), .der(pixel_cuadrito_338_siz), .dir(dir),
    .sar(pixel_cuadrito_306_sar), .siz(pixel_cuadrito_306_siz), .sde(c10[14]), .ZA_WARUDO(ZA_WARUDO),
    .reset(reset));  // open: in_7
  pixel_cuadrito pixel_cuadrito_307 (
    .clk(clk), .abajo(pixel_cuadrito_308_sar), .izq(c9[13]), .der(pixel_cuadrito_339_siz), .dir(dir),
    .sar(pixel_cuadrito_307_sar), .siz(pixel_cuadrito_307_siz), .sde(c10[13]), .ZA_WARUDO(ZA_WARUDO),
    .reset(reset));  // open: in_7
  pixel_cuadrito pixel_cuadrito_308 (
    .clk(clk), .abajo(pixel_cuadrito_309_sar), .izq(c9[12]), .der(pixel_cuadrito_340_siz), .dir(dir),
    .sar(pixel_cuadrito_308_sar), .siz(pixel_cuadrito_308_siz), .sde(c10[12]), .ZA_WARUDO(ZA_WARUDO),
    .reset(reset));  // open: in_7
  pixel_cuadrito pixel_cuadrito_309 (
    .clk(clk), .abajo(pixel_cuadrito_310_sar), .izq(c9[11]), .der(pixel_cuadrito_341_siz), .dir(dir),
    .sar(pixel_cuadrito_309_sar), .siz(pixel_cuadrito_309_siz), .sde(c10[11]), .ZA_WARUDO(ZA_WARUDO),
    .reset(reset));  // open: in_7
  pixel_cuadrito pixel_cuadrito_310 (
    .clk(clk), .abajo(pixel_cuadrito_311_sar), .izq(c9[10]), .der(pixel_cuadrito_342_siz), .dir(dir),
    .sar(pixel_cuadrito_310_sar), .siz(pixel_cuadrito_310_siz), .sde(c10[10]), .ZA_WARUDO(ZA_WARUDO),
    .reset(reset));  // open: in_7
  pixel_cuadrito pixel_cuadrito_311 (
    .clk(clk), .abajo(pixel_cuadrito_312_sar), .izq(c9[9]), .der(pixel_cuadrito_343_siz), .dir(dir),
    .sar(pixel_cuadrito_311_sar), .siz(pixel_cuadrito_311_siz), .sde(c10[9]), .ZA_WARUDO(ZA_WARUDO),
    .reset(reset));  // open: in_7
  pixel_cuadrito pixel_cuadrito_312 (
    .clk(clk), .abajo(pixel_cuadrito_313_sar), .izq(c9[8]), .der(pixel_cuadrito_344_siz), .dir(dir),
    .sar(pixel_cuadrito_312_sar), .siz(pixel_cuadrito_312_siz), .sde(c10[8]), .ZA_WARUDO(ZA_WARUDO),
    .reset(reset));  // open: in_7
  pixel_cuadrito pixel_cuadrito_313 (
    .clk(clk), .abajo(pixel_cuadrito_314_sar), .izq(c9[7]), .der(pixel_cuadrito_345_siz), .dir(dir),
    .sar(pixel_cuadrito_313_sar), .siz(pixel_cuadrito_313_siz), .sde(c10[7]), .ZA_WARUDO(ZA_WARUDO),
    .reset(reset));  // open: in_7
  pixel_cuadrito pixel_cuadrito_314 (
    .clk(clk), .abajo(pixel_cuadrito_315_sar), .izq(c9[6]), .der(pixel_cuadrito_346_siz), .dir(dir),
    .sar(pixel_cuadrito_314_sar), .siz(pixel_cuadrito_314_siz), .sde(c10[6]), .ZA_WARUDO(ZA_WARUDO),
    .reset(reset));  // open: in_7
  pixel_cuadrito pixel_cuadrito_315 (
    .clk(clk), .abajo(pixel_cuadrito_316_sar), .izq(c9[5]), .der(pixel_cuadrito_347_siz), .dir(dir),
    .sar(pixel_cuadrito_315_sar), .siz(pixel_cuadrito_315_siz), .sde(c10[5]), .ZA_WARUDO(ZA_WARUDO),
    .reset(reset));  // open: in_7
  pixel_cuadrito pixel_cuadrito_316 (
    .clk(clk), .abajo(pixel_cuadrito_317_sar), .izq(c9[4]), .der(pixel_cuadrito_348_siz), .dir(dir),
    .sar(pixel_cuadrito_316_sar), .siz(pixel_cuadrito_316_siz), .sde(c10[4]), .ZA_WARUDO(ZA_WARUDO),
    .reset(reset));  // open: in_7
  pixel_cuadrito pixel_cuadrito_317 (
    .clk(clk), .abajo(pixel_cuadrito_318_sar), .izq(c9[3]), .der(pixel_cuadrito_349_siz), .dir(dir),
    .sar(pixel_cuadrito_317_sar), .siz(pixel_cuadrito_317_siz), .sde(c10[3]), .ZA_WARUDO(ZA_WARUDO),
    .reset(reset));  // open: in_7
  pixel_cuadrito pixel_cuadrito_318 (
    .clk(clk), .abajo(pixel_cuadrito_319_sar), .izq(c9[2]), .der(pixel_cuadrito_350_siz), .dir(dir),
    .sar(pixel_cuadrito_318_sar), .siz(pixel_cuadrito_318_siz), .sde(c10[2]), .in_7(s9os10),
    .ZA_WARUDO(ZA_WARUDO), .reset(reset));
  pixel_cuadrito pixel_cuadrito_319 (
    .clk(clk), .abajo(pixel_cuadrito_320_sar), .izq(c9[1]), .der(pixel_cuadrito_351_siz), .dir(dir),
    .sar(pixel_cuadrito_319_sar), .siz(pixel_cuadrito_319_siz), .sde(c10[1]), .in_7(s9os10),
    .ZA_WARUDO(ZA_WARUDO), .reset(reset));
  pixel_cuadrito pixel_cuadrito_320 (
    .clk(clk), .abajo(c10[31]), .izq(c9[0]), .der(pixel_cuadrito_352_siz), .dir(dir),
    .sar(pixel_cuadrito_320_sar), .siz(pixel_cuadrito_320_siz), .sde(c10[0]), .ZA_WARUDO(ZA_WARUDO),
    .reset(reset));  // open: in_7
  pixel_cuadrito pixel_cuadrito_321 (
    .clk(clk), .abajo(pixel_cuadrito_322_sar), .izq(c10[31]), .der(pixel_cuadrito_353_siz), .dir(dir),
    .siz(pixel_cuadrito_321_siz), .sde(c11[31]), .ZA_WARUDO(ZA_WARUDO), .reset(reset));  // open: sar, in_7
  pixel_cuadrito pixel_cuadrito_322 (
    .clk(clk), .abajo(pixel_cuadrito_323_sar), .izq(c10[30]), .der(pixel_cuadrito_354_siz), .dir(dir),
    .sar(pixel_cuadrito_322_sar), .siz(pixel_cuadrito_322_siz), .sde(c11[30]), .ZA_WARUDO(ZA_WARUDO),
    .reset(reset));  // open: in_7
  pixel_cuadrito pixel_cuadrito_323 (
    .clk(clk), .abajo(pixel_cuadrito_324_sar), .izq(c10[29]), .der(pixel_cuadrito_355_siz), .dir(dir),
    .sar(pixel_cuadrito_323_sar), .siz(pixel_cuadrito_323_siz), .sde(c11[29]), .reset(reset));  // open: in_7, ZA_WARUDO
  pixel_cuadrito pixel_cuadrito_324 (
    .clk(clk), .abajo(pixel_cuadrito_325_sar), .izq(c10[28]), .der(pixel_cuadrito_356_siz), .dir(dir),
    .sar(pixel_cuadrito_324_sar), .siz(pixel_cuadrito_324_siz), .sde(c11[28]), .ZA_WARUDO(ZA_WARUDO),
    .reset(reset));  // open: in_7
  pixel_cuadrito pixel_cuadrito_325 (
    .clk(clk), .abajo(pixel_cuadrito_326_sar), .izq(c10[27]), .der(pixel_cuadrito_357_siz), .dir(dir),
    .sar(pixel_cuadrito_325_sar), .siz(pixel_cuadrito_325_siz), .sde(c11[27]), .ZA_WARUDO(ZA_WARUDO),
    .reset(reset));  // open: in_7
  pixel_cuadrito pixel_cuadrito_326 (
    .clk(clk), .abajo(pixel_cuadrito_327_sar), .izq(c10[26]), .der(pixel_cuadrito_358_siz), .dir(dir),
    .sar(pixel_cuadrito_326_sar), .siz(pixel_cuadrito_326_siz), .sde(c11[26]), .ZA_WARUDO(ZA_WARUDO),
    .reset(reset));  // open: in_7
  pixel_cuadrito pixel_cuadrito_327 (
    .clk(clk), .abajo(pixel_cuadrito_328_sar), .izq(c10[25]), .der(pixel_cuadrito_359_siz), .dir(dir),
    .sar(pixel_cuadrito_327_sar), .siz(pixel_cuadrito_327_siz), .sde(c11[25]), .ZA_WARUDO(ZA_WARUDO),
    .reset(reset));  // open: in_7
  pixel_cuadrito pixel_cuadrito_328 (
    .clk(clk), .abajo(pixel_cuadrito_329_sar), .izq(c10[24]), .der(pixel_cuadrito_360_siz), .dir(dir),
    .sar(pixel_cuadrito_328_sar), .siz(pixel_cuadrito_328_siz), .sde(c11[24]), .ZA_WARUDO(ZA_WARUDO),
    .reset(reset));  // open: in_7
  pixel_cuadrito pixel_cuadrito_329 (
    .clk(clk), .abajo(pixel_cuadrito_330_sar), .izq(c10[23]), .der(pixel_cuadrito_361_siz), .dir(dir),
    .sar(pixel_cuadrito_329_sar), .siz(pixel_cuadrito_329_siz), .sde(c11[23]), .ZA_WARUDO(ZA_WARUDO),
    .reset(reset));  // open: in_7
  pixel_cuadrito pixel_cuadrito_330 (
    .clk(clk), .abajo(pixel_cuadrito_331_sar), .izq(c10[22]), .der(pixel_cuadrito_362_siz), .dir(dir),
    .sar(pixel_cuadrito_330_sar), .siz(pixel_cuadrito_330_siz), .sde(c11[22]), .ZA_WARUDO(ZA_WARUDO),
    .reset(reset));  // open: in_7
  pixel_cuadrito pixel_cuadrito_331 (
    .clk(clk), .abajo(pixel_cuadrito_332_sar), .izq(c10[21]), .der(pixel_cuadrito_363_siz), .dir(dir),
    .sar(pixel_cuadrito_331_sar), .siz(pixel_cuadrito_331_siz), .sde(c11[21]), .ZA_WARUDO(ZA_WARUDO),
    .reset(reset));  // open: in_7
  pixel_cuadrito pixel_cuadrito_332 (
    .clk(clk), .abajo(pixel_cuadrito_333_sar), .izq(c10[20]), .der(pixel_cuadrito_364_siz), .dir(dir),
    .sar(pixel_cuadrito_332_sar), .siz(pixel_cuadrito_332_siz), .sde(c11[20]), .ZA_WARUDO(ZA_WARUDO),
    .reset(reset));  // open: in_7
  pixel_cuadrito pixel_cuadrito_333 (
    .clk(clk), .abajo(pixel_cuadrito_334_sar), .izq(c10[19]), .der(pixel_cuadrito_365_siz), .dir(dir),
    .sar(pixel_cuadrito_333_sar), .siz(pixel_cuadrito_333_siz), .sde(c11[19]), .ZA_WARUDO(ZA_WARUDO),
    .reset(reset));  // open: in_7
  pixel_cuadrito pixel_cuadrito_334 (
    .clk(clk), .abajo(pixel_cuadrito_335_sar), .izq(c10[18]), .der(pixel_cuadrito_366_siz), .dir(dir),
    .sar(pixel_cuadrito_334_sar), .siz(pixel_cuadrito_334_siz), .sde(c11[18]), .ZA_WARUDO(ZA_WARUDO),
    .reset(reset));  // open: in_7
  pixel_cuadrito pixel_cuadrito_335 (
    .clk(clk), .abajo(pixel_cuadrito_336_sar), .izq(c10[17]), .der(pixel_cuadrito_367_siz), .dir(dir),
    .sar(pixel_cuadrito_335_sar), .siz(pixel_cuadrito_335_siz), .sde(c11[17]), .ZA_WARUDO(ZA_WARUDO),
    .reset(reset));  // open: in_7
  pixel_cuadrito pixel_cuadrito_336 (
    .clk(clk), .abajo(pixel_cuadrito_337_sar), .izq(c10[16]), .der(pixel_cuadrito_368_siz), .dir(dir),
    .sar(pixel_cuadrito_336_sar), .siz(pixel_cuadrito_336_siz), .sde(c11[16]), .ZA_WARUDO(ZA_WARUDO),
    .reset(reset));  // open: in_7
  pixel_cuadrito pixel_cuadrito_337 (
    .clk(clk), .abajo(pixel_cuadrito_338_sar), .izq(c10[15]), .der(pixel_cuadrito_369_siz), .dir(dir),
    .sar(pixel_cuadrito_337_sar), .siz(pixel_cuadrito_337_siz), .sde(c11[15]), .ZA_WARUDO(ZA_WARUDO),
    .reset(reset));  // open: in_7
  pixel_cuadrito pixel_cuadrito_338 (
    .clk(clk), .abajo(pixel_cuadrito_339_sar), .izq(c10[14]), .der(pixel_cuadrito_370_siz), .dir(dir),
    .sar(pixel_cuadrito_338_sar), .siz(pixel_cuadrito_338_siz), .sde(c11[14]), .ZA_WARUDO(ZA_WARUDO),
    .reset(reset));  // open: in_7
  pixel_cuadrito pixel_cuadrito_339 (
    .clk(clk), .abajo(pixel_cuadrito_340_sar), .izq(c10[13]), .der(pixel_cuadrito_371_siz), .dir(dir),
    .sar(pixel_cuadrito_339_sar), .siz(pixel_cuadrito_339_siz), .sde(c11[13]), .ZA_WARUDO(ZA_WARUDO),
    .reset(reset));  // open: in_7
  pixel_cuadrito pixel_cuadrito_340 (
    .clk(clk), .abajo(pixel_cuadrito_341_sar), .izq(c10[12]), .der(pixel_cuadrito_372_siz), .dir(dir),
    .sar(pixel_cuadrito_340_sar), .siz(pixel_cuadrito_340_siz), .sde(c11[12]), .ZA_WARUDO(ZA_WARUDO),
    .reset(reset));  // open: in_7
  pixel_cuadrito pixel_cuadrito_341 (
    .clk(clk), .abajo(pixel_cuadrito_342_sar), .izq(c10[11]), .der(pixel_cuadrito_373_siz), .dir(dir),
    .sar(pixel_cuadrito_341_sar), .siz(pixel_cuadrito_341_siz), .sde(c11[11]), .ZA_WARUDO(ZA_WARUDO),
    .reset(reset));  // open: in_7
  pixel_cuadrito pixel_cuadrito_342 (
    .clk(clk), .abajo(pixel_cuadrito_343_sar), .izq(c10[10]), .der(pixel_cuadrito_374_siz), .dir(dir),
    .sar(pixel_cuadrito_342_sar), .siz(pixel_cuadrito_342_siz), .sde(c11[10]), .ZA_WARUDO(ZA_WARUDO),
    .reset(reset));  // open: in_7
  pixel_cuadrito pixel_cuadrito_343 (
    .clk(clk), .abajo(pixel_cuadrito_344_sar), .izq(c10[9]), .der(pixel_cuadrito_375_siz), .dir(dir),
    .sar(pixel_cuadrito_343_sar), .siz(pixel_cuadrito_343_siz), .sde(c11[9]), .ZA_WARUDO(ZA_WARUDO),
    .reset(reset));  // open: in_7
  pixel_cuadrito pixel_cuadrito_344 (
    .clk(clk), .abajo(pixel_cuadrito_345_sar), .izq(c10[8]), .der(pixel_cuadrito_376_siz), .dir(dir),
    .sar(pixel_cuadrito_344_sar), .siz(pixel_cuadrito_344_siz), .sde(c11[8]), .ZA_WARUDO(ZA_WARUDO),
    .reset(reset));  // open: in_7
  pixel_cuadrito pixel_cuadrito_345 (
    .clk(clk), .abajo(pixel_cuadrito_346_sar), .izq(c10[7]), .der(pixel_cuadrito_377_siz), .dir(dir),
    .sar(pixel_cuadrito_345_sar), .siz(pixel_cuadrito_345_siz), .sde(c11[7]), .ZA_WARUDO(ZA_WARUDO),
    .reset(reset));  // open: in_7
  pixel_cuadrito pixel_cuadrito_346 (
    .clk(clk), .abajo(pixel_cuadrito_347_sar), .izq(c10[6]), .der(pixel_cuadrito_378_siz), .dir(dir),
    .sar(pixel_cuadrito_346_sar), .siz(pixel_cuadrito_346_siz), .sde(c11[6]), .ZA_WARUDO(ZA_WARUDO),
    .reset(reset));  // open: in_7
  pixel_cuadrito pixel_cuadrito_347 (
    .clk(clk), .abajo(pixel_cuadrito_348_sar), .izq(c10[5]), .der(pixel_cuadrito_379_siz), .dir(dir),
    .sar(pixel_cuadrito_347_sar), .siz(pixel_cuadrito_347_siz), .sde(c11[5]), .ZA_WARUDO(ZA_WARUDO),
    .reset(reset));  // open: in_7
  pixel_cuadrito pixel_cuadrito_348 (
    .clk(clk), .abajo(pixel_cuadrito_349_sar), .izq(c10[4]), .der(pixel_cuadrito_380_siz), .dir(dir),
    .sar(pixel_cuadrito_348_sar), .siz(pixel_cuadrito_348_siz), .sde(c11[4]), .ZA_WARUDO(ZA_WARUDO),
    .reset(reset));  // open: in_7
  pixel_cuadrito pixel_cuadrito_349 (
    .clk(clk), .abajo(pixel_cuadrito_350_sar), .izq(c10[3]), .der(pixel_cuadrito_381_siz), .dir(dir),
    .sar(pixel_cuadrito_349_sar), .siz(pixel_cuadrito_349_siz), .sde(c11[3]), .ZA_WARUDO(ZA_WARUDO),
    .reset(reset));  // open: in_7
  pixel_cuadrito pixel_cuadrito_350 (
    .clk(clk), .abajo(pixel_cuadrito_351_sar), .izq(c10[2]), .der(pixel_cuadrito_382_siz), .dir(dir),
    .sar(pixel_cuadrito_350_sar), .siz(pixel_cuadrito_350_siz), .sde(c11[2]), .in_7(s10os11), .reset(reset));  // open: ZA_WARUDO
  pixel_cuadrito pixel_cuadrito_351 (
    .clk(clk), .abajo(pixel_cuadrito_352_sar), .izq(c10[1]), .der(pixel_cuadrito_383_siz), .dir(dir),
    .sar(pixel_cuadrito_351_sar), .siz(pixel_cuadrito_351_siz), .sde(c11[1]), .in_7(s10os11),
    .ZA_WARUDO(ZA_WARUDO), .reset(reset));
  pixel_cuadrito pixel_cuadrito_352 (
    .clk(clk), .abajo(c11[31]), .izq(c10[0]), .der(pixel_cuadrito_384_siz), .dir(dir),
    .sar(pixel_cuadrito_352_sar), .siz(pixel_cuadrito_352_siz), .sde(c11[0]), .ZA_WARUDO(ZA_WARUDO),
    .reset(reset));  // open: in_7
  pixel_cuadrito pixel_cuadrito_353 (
    .clk(clk), .abajo(pixel_cuadrito_354_sar), .izq(c11[31]), .der(pixel_cuadrito_385_siz), .dir(dir),
    .siz(pixel_cuadrito_353_siz), .sde(c12[31]), .ZA_WARUDO(ZA_WARUDO), .reset(reset));  // open: sar, in_7
  pixel_cuadrito pixel_cuadrito_354 (
    .clk(clk), .abajo(pixel_cuadrito_355_sar), .izq(c11[30]), .der(pixel_cuadrito_386_siz), .dir(dir),
    .sar(pixel_cuadrito_354_sar), .siz(pixel_cuadrito_354_siz), .sde(c12[30]), .ZA_WARUDO(ZA_WARUDO),
    .reset(reset));  // open: in_7
  pixel_cuadrito pixel_cuadrito_355 (
    .clk(clk), .abajo(pixel_cuadrito_356_sar), .izq(c11[29]), .der(pixel_cuadrito_387_siz), .dir(dir),
    .sar(pixel_cuadrito_355_sar), .siz(pixel_cuadrito_355_siz), .sde(c12[29]), .ZA_WARUDO(ZA_WARUDO),
    .reset(reset));  // open: in_7
  pixel_cuadrito pixel_cuadrito_356 (
    .clk(clk), .abajo(pixel_cuadrito_357_sar), .izq(c11[28]), .der(pixel_cuadrito_388_siz), .dir(dir),
    .sar(pixel_cuadrito_356_sar), .siz(pixel_cuadrito_356_siz), .sde(c12[28]), .ZA_WARUDO(ZA_WARUDO),
    .reset(reset));  // open: in_7
  pixel_cuadrito pixel_cuadrito_357 (
    .clk(clk), .abajo(pixel_cuadrito_358_sar), .izq(c11[27]), .der(pixel_cuadrito_389_siz), .dir(dir),
    .sar(pixel_cuadrito_357_sar), .siz(pixel_cuadrito_357_siz), .sde(c12[27]), .ZA_WARUDO(ZA_WARUDO),
    .reset(reset));  // open: in_7
  pixel_cuadrito pixel_cuadrito_358 (
    .clk(clk), .abajo(pixel_cuadrito_359_sar), .izq(c11[26]), .der(pixel_cuadrito_390_siz), .dir(dir),
    .sar(pixel_cuadrito_358_sar), .siz(pixel_cuadrito_358_siz), .sde(c12[26]), .ZA_WARUDO(ZA_WARUDO),
    .reset(reset));  // open: in_7
  pixel_cuadrito pixel_cuadrito_359 (
    .clk(clk), .abajo(pixel_cuadrito_360_sar), .izq(c11[25]), .der(pixel_cuadrito_391_siz), .dir(dir),
    .sar(pixel_cuadrito_359_sar), .siz(pixel_cuadrito_359_siz), .sde(c12[25]), .ZA_WARUDO(ZA_WARUDO),
    .reset(reset));  // open: in_7
  pixel_cuadrito pixel_cuadrito_360 (
    .clk(clk), .abajo(pixel_cuadrito_361_sar), .izq(c11[24]), .der(pixel_cuadrito_392_siz), .dir(dir),
    .sar(pixel_cuadrito_360_sar), .siz(pixel_cuadrito_360_siz), .sde(c12[24]), .ZA_WARUDO(ZA_WARUDO),
    .reset(reset));  // open: in_7
  pixel_cuadrito pixel_cuadrito_361 (
    .clk(clk), .abajo(pixel_cuadrito_362_sar), .izq(c11[23]), .der(pixel_cuadrito_393_siz), .dir(dir),
    .sar(pixel_cuadrito_361_sar), .siz(pixel_cuadrito_361_siz), .sde(c12[23]), .ZA_WARUDO(ZA_WARUDO),
    .reset(reset));  // open: in_7
  pixel_cuadrito pixel_cuadrito_362 (
    .clk(clk), .abajo(pixel_cuadrito_363_sar), .izq(c11[22]), .der(pixel_cuadrito_394_siz), .dir(dir),
    .sar(pixel_cuadrito_362_sar), .siz(pixel_cuadrito_362_siz), .sde(c12[22]), .ZA_WARUDO(ZA_WARUDO),
    .reset(reset));  // open: in_7
  pixel_cuadrito pixel_cuadrito_363 (
    .clk(clk), .abajo(pixel_cuadrito_364_sar), .izq(c11[21]), .der(pixel_cuadrito_395_siz), .dir(dir),
    .sar(pixel_cuadrito_363_sar), .siz(pixel_cuadrito_363_siz), .sde(c12[21]), .ZA_WARUDO(ZA_WARUDO),
    .reset(reset));  // open: in_7
  pixel_cuadrito pixel_cuadrito_364 (
    .clk(clk), .abajo(pixel_cuadrito_365_sar), .izq(c11[20]), .der(pixel_cuadrito_396_siz), .dir(dir),
    .sar(pixel_cuadrito_364_sar), .siz(pixel_cuadrito_364_siz), .sde(c12[20]), .ZA_WARUDO(ZA_WARUDO),
    .reset(reset));  // open: in_7
  pixel_cuadrito pixel_cuadrito_365 (
    .clk(clk), .abajo(pixel_cuadrito_366_sar), .izq(c11[19]), .der(pixel_cuadrito_397_siz), .dir(dir),
    .sar(pixel_cuadrito_365_sar), .siz(pixel_cuadrito_365_siz), .sde(c12[19]), .ZA_WARUDO(ZA_WARUDO),
    .reset(reset));  // open: in_7
  pixel_cuadrito pixel_cuadrito_366 (
    .clk(clk), .abajo(pixel_cuadrito_367_sar), .izq(c11[18]), .der(pixel_cuadrito_398_siz), .dir(dir),
    .sar(pixel_cuadrito_366_sar), .siz(pixel_cuadrito_366_siz), .sde(c12[18]), .ZA_WARUDO(ZA_WARUDO),
    .reset(reset));  // open: in_7
  pixel_cuadrito pixel_cuadrito_367 (
    .clk(clk), .abajo(pixel_cuadrito_368_sar), .izq(c11[17]), .der(pixel_cuadrito_399_siz), .dir(dir),
    .sar(pixel_cuadrito_367_sar), .siz(pixel_cuadrito_367_siz), .sde(c12[17]), .ZA_WARUDO(ZA_WARUDO),
    .reset(reset));  // open: in_7
  pixel_cuadrito pixel_cuadrito_368 (
    .clk(clk), .abajo(pixel_cuadrito_369_sar), .izq(c11[16]), .der(pixel_cuadrito_400_siz), .dir(dir),
    .sar(pixel_cuadrito_368_sar), .siz(pixel_cuadrito_368_siz), .sde(c12[16]), .ZA_WARUDO(ZA_WARUDO),
    .reset(reset));  // open: in_7
  pixel_cuadrito pixel_cuadrito_369 (
    .clk(clk), .abajo(pixel_cuadrito_370_sar), .izq(c11[15]), .der(pixel_cuadrito_401_siz), .dir(dir),
    .sar(pixel_cuadrito_369_sar), .siz(pixel_cuadrito_369_siz), .sde(c12[15]), .ZA_WARUDO(ZA_WARUDO),
    .reset(reset));  // open: in_7
  pixel_cuadrito pixel_cuadrito_370 (
    .clk(clk), .abajo(pixel_cuadrito_371_sar), .izq(c11[14]), .der(pixel_cuadrito_402_siz), .dir(dir),
    .sar(pixel_cuadrito_370_sar), .siz(pixel_cuadrito_370_siz), .sde(c12[14]), .ZA_WARUDO(ZA_WARUDO),
    .reset(reset));  // open: in_7
  pixel_cuadrito pixel_cuadrito_371 (
    .clk(clk), .abajo(pixel_cuadrito_372_sar), .izq(c11[13]), .der(pixel_cuadrito_403_siz), .dir(dir),
    .sar(pixel_cuadrito_371_sar), .siz(pixel_cuadrito_371_siz), .sde(c12[13]), .ZA_WARUDO(ZA_WARUDO),
    .reset(reset));  // open: in_7
  pixel_cuadrito pixel_cuadrito_372 (
    .clk(clk), .abajo(pixel_cuadrito_373_sar), .izq(c11[12]), .der(pixel_cuadrito_404_siz), .dir(dir),
    .sar(pixel_cuadrito_372_sar), .siz(pixel_cuadrito_372_siz), .sde(c12[12]), .ZA_WARUDO(ZA_WARUDO),
    .reset(reset));  // open: in_7
  pixel_cuadrito pixel_cuadrito_373 (
    .clk(clk), .abajo(pixel_cuadrito_374_sar), .izq(c11[11]), .der(pixel_cuadrito_405_siz), .dir(dir),
    .sar(pixel_cuadrito_373_sar), .siz(pixel_cuadrito_373_siz), .sde(c12[11]), .ZA_WARUDO(ZA_WARUDO),
    .reset(reset));  // open: in_7
  pixel_cuadrito pixel_cuadrito_374 (
    .clk(clk), .abajo(pixel_cuadrito_375_sar), .izq(c11[10]), .der(pixel_cuadrito_406_siz), .dir(dir),
    .sar(pixel_cuadrito_374_sar), .siz(pixel_cuadrito_374_siz), .sde(c12[10]), .ZA_WARUDO(ZA_WARUDO),
    .reset(reset));  // open: in_7
  pixel_cuadrito pixel_cuadrito_375 (
    .clk(clk), .abajo(pixel_cuadrito_376_sar), .izq(c11[9]), .der(pixel_cuadrito_407_siz), .dir(dir),
    .sar(pixel_cuadrito_375_sar), .siz(pixel_cuadrito_375_siz), .sde(c12[9]), .ZA_WARUDO(ZA_WARUDO),
    .reset(reset));  // open: in_7
  pixel_cuadrito pixel_cuadrito_376 (
    .clk(clk), .abajo(pixel_cuadrito_377_sar), .izq(c11[8]), .der(pixel_cuadrito_408_siz), .dir(dir),
    .sar(pixel_cuadrito_376_sar), .siz(pixel_cuadrito_376_siz), .sde(c12[8]), .ZA_WARUDO(ZA_WARUDO),
    .reset(reset));  // open: in_7
  pixel_cuadrito pixel_cuadrito_377 (
    .clk(clk), .abajo(pixel_cuadrito_378_sar), .izq(c11[7]), .der(pixel_cuadrito_409_siz), .dir(dir),
    .sar(pixel_cuadrito_377_sar), .siz(pixel_cuadrito_377_siz), .sde(c12[7]), .ZA_WARUDO(ZA_WARUDO),
    .reset(reset));  // open: in_7
  pixel_cuadrito pixel_cuadrito_378 (
    .clk(clk), .abajo(pixel_cuadrito_379_sar), .izq(c11[6]), .der(pixel_cuadrito_410_siz), .dir(dir),
    .sar(pixel_cuadrito_378_sar), .siz(pixel_cuadrito_378_siz), .sde(c12[6]), .ZA_WARUDO(ZA_WARUDO),
    .reset(reset));  // open: in_7
  pixel_cuadrito pixel_cuadrito_379 (
    .clk(clk), .abajo(pixel_cuadrito_380_sar), .izq(c11[5]), .der(pixel_cuadrito_411_siz), .dir(dir),
    .sar(pixel_cuadrito_379_sar), .siz(pixel_cuadrito_379_siz), .sde(c12[5]), .ZA_WARUDO(ZA_WARUDO),
    .reset(reset));  // open: in_7
  pixel_cuadrito pixel_cuadrito_380 (
    .clk(clk), .abajo(pixel_cuadrito_381_sar), .izq(c11[4]), .der(pixel_cuadrito_412_siz), .dir(dir),
    .sar(pixel_cuadrito_380_sar), .siz(pixel_cuadrito_380_siz), .sde(c12[4]), .ZA_WARUDO(ZA_WARUDO),
    .reset(reset));  // open: in_7
  pixel_cuadrito pixel_cuadrito_381 (
    .clk(clk), .abajo(pixel_cuadrito_382_sar), .izq(c11[3]), .der(pixel_cuadrito_413_siz), .dir(dir),
    .sar(pixel_cuadrito_381_sar), .siz(pixel_cuadrito_381_siz), .sde(c12[3]), .ZA_WARUDO(ZA_WARUDO),
    .reset(reset));  // open: in_7
  pixel_cuadrito pixel_cuadrito_382 (
    .clk(clk), .abajo(pixel_cuadrito_383_sar), .izq(c11[2]), .der(pixel_cuadrito_414_siz), .dir(dir),
    .sar(pixel_cuadrito_382_sar), .siz(pixel_cuadrito_382_siz), .sde(c12[2]), .in_7(s11os12), .reset(reset));  // open: ZA_WARUDO
  pixel_cuadrito pixel_cuadrito_383 (
    .clk(clk), .abajo(pixel_cuadrito_384_sar), .izq(c11[1]), .der(pixel_cuadrito_415_siz), .dir(dir),
    .sar(pixel_cuadrito_383_sar), .siz(pixel_cuadrito_383_siz), .sde(c12[1]), .in_7(s11os12),
    .ZA_WARUDO(ZA_WARUDO), .reset(reset));
  pixel_cuadrito pixel_cuadrito_384 (
    .clk(clk), .abajo(c12[31]), .izq(c11[0]), .der(pixel_cuadrito_416_siz), .dir(dir),
    .sar(pixel_cuadrito_384_sar), .siz(pixel_cuadrito_384_siz), .sde(c12[0]), .ZA_WARUDO(ZA_WARUDO),
    .reset(reset));  // open: in_7
  pixel_cuadrito pixel_cuadrito_385 (
    .clk(clk), .abajo(pixel_cuadrito_386_sar), .izq(c12[31]), .der(pixel_cuadrito_417_siz), .dir(dir),
    .siz(pixel_cuadrito_385_siz), .sde(c13[31]), .ZA_WARUDO(ZA_WARUDO), .reset(reset));  // open: sar, in_7
  pixel_cuadrito pixel_cuadrito_386 (
    .clk(clk), .abajo(pixel_cuadrito_387_sar), .izq(c12[30]), .der(pixel_cuadrito_418_siz), .dir(dir),
    .sar(pixel_cuadrito_386_sar), .siz(pixel_cuadrito_386_siz), .sde(c13[30]), .ZA_WARUDO(ZA_WARUDO),
    .reset(reset));  // open: in_7
  pixel_cuadrito pixel_cuadrito_387 (
    .clk(clk), .abajo(pixel_cuadrito_388_sar), .izq(c12[29]), .der(pixel_cuadrito_419_siz), .dir(dir),
    .sar(pixel_cuadrito_387_sar), .siz(pixel_cuadrito_387_siz), .sde(c13[29]), .ZA_WARUDO(ZA_WARUDO),
    .reset(reset));  // open: in_7
  pixel_cuadrito pixel_cuadrito_388 (
    .clk(clk), .abajo(pixel_cuadrito_389_sar), .izq(c12[28]), .der(pixel_cuadrito_420_siz), .dir(dir),
    .sar(pixel_cuadrito_388_sar), .siz(pixel_cuadrito_388_siz), .sde(c13[28]), .ZA_WARUDO(ZA_WARUDO),
    .reset(reset));  // open: in_7
  pixel_cuadrito pixel_cuadrito_389 (
    .clk(clk), .abajo(pixel_cuadrito_390_sar), .izq(c12[27]), .der(pixel_cuadrito_421_siz), .dir(dir),
    .sar(pixel_cuadrito_389_sar), .siz(pixel_cuadrito_389_siz), .sde(c13[27]), .ZA_WARUDO(ZA_WARUDO),
    .reset(reset));  // open: in_7
  pixel_cuadrito pixel_cuadrito_390 (
    .clk(clk), .abajo(pixel_cuadrito_391_sar), .izq(c12[26]), .der(pixel_cuadrito_422_siz), .dir(dir),
    .sar(pixel_cuadrito_390_sar), .siz(pixel_cuadrito_390_siz), .sde(c13[26]), .ZA_WARUDO(ZA_WARUDO),
    .reset(reset));  // open: in_7
  pixel_cuadrito pixel_cuadrito_391 (
    .clk(clk), .abajo(pixel_cuadrito_392_sar), .izq(c12[25]), .der(pixel_cuadrito_423_siz), .dir(dir),
    .sar(pixel_cuadrito_391_sar), .siz(pixel_cuadrito_391_siz), .sde(c13[25]), .ZA_WARUDO(ZA_WARUDO),
    .reset(reset));  // open: in_7
  pixel_cuadrito pixel_cuadrito_392 (
    .clk(clk), .abajo(pixel_cuadrito_393_sar), .izq(c12[24]), .der(pixel_cuadrito_424_siz), .dir(dir),
    .sar(pixel_cuadrito_392_sar), .siz(pixel_cuadrito_392_siz), .sde(c13[24]), .ZA_WARUDO(ZA_WARUDO),
    .reset(reset));  // open: in_7
  pixel_cuadrito pixel_cuadrito_393 (
    .clk(clk), .abajo(pixel_cuadrito_394_sar), .izq(c12[23]), .der(pixel_cuadrito_425_siz), .dir(dir),
    .sar(pixel_cuadrito_393_sar), .siz(pixel_cuadrito_393_siz), .sde(c13[23]), .ZA_WARUDO(ZA_WARUDO),
    .reset(reset));  // open: in_7
  pixel_cuadrito pixel_cuadrito_394 (
    .clk(clk), .abajo(pixel_cuadrito_395_sar), .izq(c12[22]), .der(pixel_cuadrito_426_siz), .dir(dir),
    .sar(pixel_cuadrito_394_sar), .siz(pixel_cuadrito_394_siz), .sde(c13[22]), .ZA_WARUDO(ZA_WARUDO),
    .reset(reset));  // open: in_7
  pixel_cuadrito pixel_cuadrito_395 (
    .clk(clk), .abajo(pixel_cuadrito_396_sar), .izq(c12[21]), .der(pixel_cuadrito_427_siz), .dir(dir),
    .sar(pixel_cuadrito_395_sar), .siz(pixel_cuadrito_395_siz), .sde(c13[21]), .ZA_WARUDO(ZA_WARUDO),
    .reset(reset));  // open: in_7
  pixel_cuadrito pixel_cuadrito_396 (
    .clk(clk), .abajo(pixel_cuadrito_397_sar), .izq(c12[20]), .der(pixel_cuadrito_428_siz), .dir(dir),
    .sar(pixel_cuadrito_396_sar), .siz(pixel_cuadrito_396_siz), .sde(c13[20]), .ZA_WARUDO(ZA_WARUDO),
    .reset(reset));  // open: in_7
  pixel_cuadrito pixel_cuadrito_397 (
    .clk(clk), .abajo(pixel_cuadrito_398_sar), .izq(c12[19]), .der(pixel_cuadrito_429_siz), .dir(dir),
    .sar(pixel_cuadrito_397_sar), .siz(pixel_cuadrito_397_siz), .sde(c13[19]), .ZA_WARUDO(ZA_WARUDO),
    .reset(reset));  // open: in_7
  pixel_cuadrito pixel_cuadrito_398 (
    .clk(clk), .abajo(pixel_cuadrito_399_sar), .izq(c12[18]), .der(pixel_cuadrito_430_siz), .dir(dir),
    .sar(pixel_cuadrito_398_sar), .siz(pixel_cuadrito_398_siz), .sde(c13[18]), .ZA_WARUDO(ZA_WARUDO),
    .reset(reset));  // open: in_7
  pixel_cuadrito pixel_cuadrito_399 (
    .clk(clk), .abajo(pixel_cuadrito_400_sar), .izq(c12[17]), .der(pixel_cuadrito_431_siz), .dir(dir),
    .sar(pixel_cuadrito_399_sar), .siz(pixel_cuadrito_399_siz), .sde(c13[17]), .ZA_WARUDO(ZA_WARUDO),
    .reset(reset));  // open: in_7
  pixel_cuadrito pixel_cuadrito_400 (
    .clk(clk), .abajo(pixel_cuadrito_401_sar), .izq(c12[16]), .der(pixel_cuadrito_432_siz), .dir(dir),
    .sar(pixel_cuadrito_400_sar), .siz(pixel_cuadrito_400_siz), .sde(c13[16]), .ZA_WARUDO(ZA_WARUDO),
    .reset(reset));  // open: in_7
  pixel_cuadrito pixel_cuadrito_401 (
    .clk(clk), .abajo(pixel_cuadrito_402_sar), .izq(c12[15]), .der(pixel_cuadrito_433_siz), .dir(dir),
    .sar(pixel_cuadrito_401_sar), .siz(pixel_cuadrito_401_siz), .sde(c13[15]), .ZA_WARUDO(ZA_WARUDO),
    .reset(reset));  // open: in_7
  pixel_cuadrito pixel_cuadrito_402 (
    .clk(clk), .abajo(pixel_cuadrito_403_sar), .izq(c12[14]), .der(pixel_cuadrito_434_siz), .dir(dir),
    .sar(pixel_cuadrito_402_sar), .siz(pixel_cuadrito_402_siz), .sde(c13[14]), .ZA_WARUDO(ZA_WARUDO),
    .reset(reset));  // open: in_7
  pixel_cuadrito pixel_cuadrito_403 (
    .clk(clk), .abajo(pixel_cuadrito_404_sar), .izq(c12[13]), .der(pixel_cuadrito_435_siz), .dir(dir),
    .sar(pixel_cuadrito_403_sar), .siz(pixel_cuadrito_403_siz), .sde(c13[13]), .ZA_WARUDO(ZA_WARUDO),
    .reset(reset));  // open: in_7
  pixel_cuadrito pixel_cuadrito_404 (
    .clk(clk), .abajo(pixel_cuadrito_405_sar), .izq(c12[12]), .der(pixel_cuadrito_436_siz), .dir(dir),
    .sar(pixel_cuadrito_404_sar), .siz(pixel_cuadrito_404_siz), .sde(c13[12]), .ZA_WARUDO(ZA_WARUDO),
    .reset(reset));  // open: in_7
  pixel_cuadrito pixel_cuadrito_405 (
    .clk(clk), .abajo(pixel_cuadrito_406_sar), .izq(c12[11]), .der(pixel_cuadrito_437_siz), .dir(dir),
    .sar(pixel_cuadrito_405_sar), .siz(pixel_cuadrito_405_siz), .sde(c13[11]), .ZA_WARUDO(ZA_WARUDO),
    .reset(reset));  // open: in_7
  pixel_cuadrito pixel_cuadrito_406 (
    .clk(clk), .abajo(pixel_cuadrito_407_sar), .izq(c12[10]), .der(pixel_cuadrito_438_siz), .dir(dir),
    .sar(pixel_cuadrito_406_sar), .siz(pixel_cuadrito_406_siz), .sde(c13[10]), .ZA_WARUDO(ZA_WARUDO),
    .reset(reset));  // open: in_7
  pixel_cuadrito pixel_cuadrito_407 (
    .clk(clk), .abajo(pixel_cuadrito_408_sar), .izq(c12[9]), .der(pixel_cuadrito_439_siz), .dir(dir),
    .sar(pixel_cuadrito_407_sar), .siz(pixel_cuadrito_407_siz), .sde(c13[9]), .ZA_WARUDO(ZA_WARUDO),
    .reset(reset));  // open: in_7
  pixel_cuadrito pixel_cuadrito_408 (
    .clk(clk), .abajo(pixel_cuadrito_409_sar), .izq(c12[8]), .der(pixel_cuadrito_440_siz), .dir(dir),
    .sar(pixel_cuadrito_408_sar), .siz(pixel_cuadrito_408_siz), .sde(c13[8]), .ZA_WARUDO(ZA_WARUDO),
    .reset(reset));  // open: in_7
  pixel_cuadrito pixel_cuadrito_409 (
    .clk(clk), .abajo(pixel_cuadrito_410_sar), .izq(c12[7]), .der(pixel_cuadrito_441_siz), .dir(dir),
    .sar(pixel_cuadrito_409_sar), .siz(pixel_cuadrito_409_siz), .sde(c13[7]), .ZA_WARUDO(ZA_WARUDO),
    .reset(reset));  // open: in_7
  pixel_cuadrito pixel_cuadrito_410 (
    .clk(clk), .abajo(pixel_cuadrito_411_sar), .izq(c12[6]), .der(pixel_cuadrito_442_siz), .dir(dir),
    .sar(pixel_cuadrito_410_sar), .siz(pixel_cuadrito_410_siz), .sde(c13[6]), .ZA_WARUDO(ZA_WARUDO),
    .reset(reset));  // open: in_7
  pixel_cuadrito pixel_cuadrito_411 (
    .clk(clk), .abajo(pixel_cuadrito_412_sar), .izq(c12[5]), .der(pixel_cuadrito_443_siz), .dir(dir),
    .sar(pixel_cuadrito_411_sar), .siz(pixel_cuadrito_411_siz), .sde(c13[5]), .ZA_WARUDO(ZA_WARUDO),
    .reset(reset));  // open: in_7
  pixel_cuadrito pixel_cuadrito_412 (
    .clk(clk), .abajo(pixel_cuadrito_413_sar), .izq(c12[4]), .der(pixel_cuadrito_444_siz), .dir(dir),
    .sar(pixel_cuadrito_412_sar), .siz(pixel_cuadrito_412_siz), .sde(c13[4]), .ZA_WARUDO(ZA_WARUDO),
    .reset(reset));  // open: in_7
  pixel_cuadrito pixel_cuadrito_413 (
    .clk(clk), .abajo(pixel_cuadrito_414_sar), .izq(c12[3]), .der(pixel_cuadrito_445_siz), .dir(dir),
    .sar(pixel_cuadrito_413_sar), .siz(pixel_cuadrito_413_siz), .sde(c13[3]), .ZA_WARUDO(ZA_WARUDO),
    .reset(reset));  // open: in_7
  pixel_cuadrito pixel_cuadrito_414 (
    .clk(clk), .abajo(pixel_cuadrito_415_sar), .izq(c12[2]), .der(pixel_cuadrito_446_siz), .dir(dir),
    .sar(pixel_cuadrito_414_sar), .siz(pixel_cuadrito_414_siz), .sde(c13[2]), .in_7(s12os13),
    .ZA_WARUDO(ZA_WARUDO), .reset(reset));
  pixel_cuadrito pixel_cuadrito_415 (
    .clk(clk), .abajo(pixel_cuadrito_416_sar), .izq(c12[1]), .der(pixel_cuadrito_447_siz), .dir(dir),
    .sar(pixel_cuadrito_415_sar), .siz(pixel_cuadrito_415_siz), .sde(c13[1]), .in_7(s12os13),
    .ZA_WARUDO(ZA_WARUDO), .reset(reset));
  pixel_cuadrito pixel_cuadrito_416 (
    .clk(clk), .abajo(c13[31]), .izq(c12[0]), .der(pixel_cuadrito_448_siz), .dir(dir),
    .sar(pixel_cuadrito_416_sar), .siz(pixel_cuadrito_416_siz), .sde(c13[0]), .reset(reset));  // open: in_7, ZA_WARUDO
  pixel_cuadrito pixel_cuadrito_417 (
    .clk(clk), .abajo(pixel_cuadrito_418_sar), .izq(c13[31]), .der(pixel_cuadrito_449_siz), .dir(dir),
    .siz(pixel_cuadrito_417_siz), .sde(c14[31]), .ZA_WARUDO(ZA_WARUDO), .reset(reset));  // open: sar, in_7
  pixel_cuadrito pixel_cuadrito_418 (
    .clk(clk), .abajo(pixel_cuadrito_419_sar), .izq(c13[30]), .der(pixel_cuadrito_450_siz), .dir(dir),
    .sar(pixel_cuadrito_418_sar), .siz(pixel_cuadrito_418_siz), .sde(c14[30]), .ZA_WARUDO(ZA_WARUDO),
    .reset(reset));  // open: in_7
  pixel_cuadrito pixel_cuadrito_419 (
    .clk(clk), .abajo(pixel_cuadrito_420_sar), .izq(c13[29]), .der(pixel_cuadrito_451_siz), .dir(dir),
    .sar(pixel_cuadrito_419_sar), .siz(pixel_cuadrito_419_siz), .sde(c14[29]), .ZA_WARUDO(ZA_WARUDO),
    .reset(reset));  // open: in_7
  pixel_cuadrito pixel_cuadrito_420 (
    .clk(clk), .abajo(pixel_cuadrito_421_sar), .izq(c13[28]), .der(pixel_cuadrito_452_siz), .dir(dir),
    .sar(pixel_cuadrito_420_sar), .siz(pixel_cuadrito_420_siz), .sde(c14[28]), .ZA_WARUDO(ZA_WARUDO),
    .reset(reset));  // open: in_7
  pixel_cuadrito pixel_cuadrito_421 (
    .clk(clk), .abajo(pixel_cuadrito_422_sar), .izq(c13[27]), .der(pixel_cuadrito_453_siz), .dir(dir),
    .sar(pixel_cuadrito_421_sar), .siz(pixel_cuadrito_421_siz), .sde(c14[27]), .ZA_WARUDO(ZA_WARUDO),
    .reset(reset));  // open: in_7
  pixel_cuadrito pixel_cuadrito_422 (
    .clk(clk), .abajo(pixel_cuadrito_423_sar), .izq(c13[26]), .der(pixel_cuadrito_454_siz), .dir(dir),
    .sar(pixel_cuadrito_422_sar), .siz(pixel_cuadrito_422_siz), .sde(c14[26]), .ZA_WARUDO(ZA_WARUDO),
    .reset(reset));  // open: in_7
  pixel_cuadrito pixel_cuadrito_423 (
    .clk(clk), .abajo(pixel_cuadrito_424_sar), .izq(c13[25]), .der(pixel_cuadrito_455_siz), .dir(dir),
    .sar(pixel_cuadrito_423_sar), .siz(pixel_cuadrito_423_siz), .sde(c14[25]), .ZA_WARUDO(ZA_WARUDO),
    .reset(reset));  // open: in_7
  pixel_cuadrito pixel_cuadrito_424 (
    .clk(clk), .abajo(pixel_cuadrito_425_sar), .izq(c13[24]), .der(pixel_cuadrito_456_siz), .dir(dir),
    .sar(pixel_cuadrito_424_sar), .siz(pixel_cuadrito_424_siz), .sde(c14[24]), .ZA_WARUDO(ZA_WARUDO),
    .reset(reset));  // open: in_7
  pixel_cuadrito pixel_cuadrito_425 (
    .clk(clk), .abajo(pixel_cuadrito_426_sar), .izq(c13[23]), .der(pixel_cuadrito_457_siz), .dir(dir),
    .sar(pixel_cuadrito_425_sar), .siz(pixel_cuadrito_425_siz), .sde(c14[23]), .ZA_WARUDO(ZA_WARUDO),
    .reset(reset));  // open: in_7
  pixel_cuadrito pixel_cuadrito_426 (
    .clk(clk), .abajo(pixel_cuadrito_427_sar), .izq(c13[22]), .der(pixel_cuadrito_458_siz), .dir(dir),
    .sar(pixel_cuadrito_426_sar), .siz(pixel_cuadrito_426_siz), .sde(c14[22]), .ZA_WARUDO(ZA_WARUDO),
    .reset(reset));  // open: in_7
  pixel_cuadrito pixel_cuadrito_427 (
    .clk(clk), .abajo(pixel_cuadrito_428_sar), .izq(c13[21]), .der(pixel_cuadrito_459_siz), .dir(dir),
    .sar(pixel_cuadrito_427_sar), .siz(pixel_cuadrito_427_siz), .sde(c14[21]), .ZA_WARUDO(ZA_WARUDO),
    .reset(reset));  // open: in_7
  pixel_cuadrito pixel_cuadrito_428 (
    .clk(clk), .abajo(pixel_cuadrito_429_sar), .izq(c13[20]), .der(pixel_cuadrito_460_siz), .dir(dir),
    .sar(pixel_cuadrito_428_sar), .siz(pixel_cuadrito_428_siz), .sde(c14[20]), .ZA_WARUDO(ZA_WARUDO),
    .reset(reset));  // open: in_7
  pixel_cuadrito pixel_cuadrito_429 (
    .clk(clk), .abajo(pixel_cuadrito_430_sar), .izq(c13[19]), .der(pixel_cuadrito_461_siz), .dir(dir),
    .sar(pixel_cuadrito_429_sar), .siz(pixel_cuadrito_429_siz), .sde(c14[19]), .ZA_WARUDO(ZA_WARUDO),
    .reset(reset));  // open: in_7
  pixel_cuadrito pixel_cuadrito_430 (
    .clk(clk), .abajo(pixel_cuadrito_431_sar), .izq(c13[18]), .der(pixel_cuadrito_462_siz), .dir(dir),
    .sar(pixel_cuadrito_430_sar), .siz(pixel_cuadrito_430_siz), .sde(c14[18]), .ZA_WARUDO(ZA_WARUDO),
    .reset(reset));  // open: in_7
  pixel_cuadrito pixel_cuadrito_431 (
    .clk(clk), .abajo(pixel_cuadrito_432_sar), .izq(c13[17]), .der(pixel_cuadrito_463_siz), .dir(dir),
    .sar(pixel_cuadrito_431_sar), .siz(pixel_cuadrito_431_siz), .sde(c14[17]), .ZA_WARUDO(ZA_WARUDO),
    .reset(reset));  // open: in_7
  pixel_cuadrito pixel_cuadrito_432 (
    .clk(clk), .abajo(pixel_cuadrito_433_sar), .izq(c13[16]), .der(pixel_cuadrito_464_siz), .dir(dir),
    .sar(pixel_cuadrito_432_sar), .siz(pixel_cuadrito_432_siz), .sde(c14[16]), .ZA_WARUDO(ZA_WARUDO),
    .reset(reset));  // open: in_7
  pixel_cuadrito pixel_cuadrito_433 (
    .clk(clk), .abajo(pixel_cuadrito_434_sar), .izq(c13[15]), .der(pixel_cuadrito_465_siz), .dir(dir),
    .sar(pixel_cuadrito_433_sar), .siz(pixel_cuadrito_433_siz), .sde(c14[15]), .ZA_WARUDO(ZA_WARUDO),
    .reset(reset));  // open: in_7
  pixel_cuadrito pixel_cuadrito_434 (
    .clk(clk), .abajo(pixel_cuadrito_435_sar), .izq(c13[14]), .der(pixel_cuadrito_466_siz), .dir(dir),
    .sar(pixel_cuadrito_434_sar), .siz(pixel_cuadrito_434_siz), .sde(c14[14]), .ZA_WARUDO(ZA_WARUDO),
    .reset(reset));  // open: in_7
  pixel_cuadrito pixel_cuadrito_435 (
    .clk(clk), .abajo(pixel_cuadrito_436_sar), .izq(c13[13]), .der(pixel_cuadrito_467_siz), .dir(dir),
    .sar(pixel_cuadrito_435_sar), .siz(pixel_cuadrito_435_siz), .sde(c14[13]), .ZA_WARUDO(ZA_WARUDO),
    .reset(reset));  // open: in_7
  pixel_cuadrito pixel_cuadrito_436 (
    .clk(clk), .abajo(pixel_cuadrito_437_sar), .izq(c13[12]), .der(pixel_cuadrito_468_siz), .dir(dir),
    .sar(pixel_cuadrito_436_sar), .siz(pixel_cuadrito_436_siz), .sde(c14[12]), .ZA_WARUDO(ZA_WARUDO),
    .reset(reset));  // open: in_7
  pixel_cuadrito pixel_cuadrito_437 (
    .clk(clk), .abajo(pixel_cuadrito_438_sar), .izq(c13[11]), .der(pixel_cuadrito_469_siz), .dir(dir),
    .sar(pixel_cuadrito_437_sar), .siz(pixel_cuadrito_437_siz), .sde(c14[11]), .ZA_WARUDO(ZA_WARUDO),
    .reset(reset));  // open: in_7
  pixel_cuadrito pixel_cuadrito_438 (
    .clk(clk), .abajo(pixel_cuadrito_439_sar), .izq(c13[10]), .der(pixel_cuadrito_470_siz), .dir(dir),
    .sar(pixel_cuadrito_438_sar), .siz(pixel_cuadrito_438_siz), .sde(c14[10]), .ZA_WARUDO(ZA_WARUDO),
    .reset(reset));  // open: in_7
  pixel_cuadrito pixel_cuadrito_439 (
    .clk(clk), .abajo(pixel_cuadrito_440_sar), .izq(c13[9]), .der(pixel_cuadrito_471_siz), .dir(dir),
    .sar(pixel_cuadrito_439_sar), .siz(pixel_cuadrito_439_siz), .sde(c14[9]), .ZA_WARUDO(ZA_WARUDO),
    .reset(reset));  // open: in_7
  pixel_cuadrito pixel_cuadrito_440 (
    .clk(clk), .abajo(pixel_cuadrito_441_sar), .izq(c13[8]), .der(pixel_cuadrito_472_siz), .dir(dir),
    .sar(pixel_cuadrito_440_sar), .siz(pixel_cuadrito_440_siz), .sde(c14[8]), .ZA_WARUDO(ZA_WARUDO),
    .reset(reset));  // open: in_7
  pixel_cuadrito pixel_cuadrito_441 (
    .clk(clk), .abajo(pixel_cuadrito_442_sar), .izq(c13[7]), .der(pixel_cuadrito_473_siz), .dir(dir),
    .sar(pixel_cuadrito_441_sar), .siz(pixel_cuadrito_441_siz), .sde(c14[7]), .ZA_WARUDO(ZA_WARUDO),
    .reset(reset));  // open: in_7
  pixel_cuadrito pixel_cuadrito_442 (
    .clk(clk), .abajo(pixel_cuadrito_443_sar), .izq(c13[6]), .der(pixel_cuadrito_474_siz), .dir(dir),
    .sar(pixel_cuadrito_442_sar), .siz(pixel_cuadrito_442_siz), .sde(c14[6]), .ZA_WARUDO(ZA_WARUDO),
    .reset(reset));  // open: in_7
  pixel_cuadrito pixel_cuadrito_443 (
    .clk(clk), .abajo(pixel_cuadrito_444_sar), .izq(c13[5]), .der(pixel_cuadrito_475_siz), .dir(dir),
    .sar(pixel_cuadrito_443_sar), .siz(pixel_cuadrito_443_siz), .sde(c14[5]), .ZA_WARUDO(ZA_WARUDO),
    .reset(reset));  // open: in_7
  pixel_cuadrito pixel_cuadrito_444 (
    .clk(clk), .abajo(pixel_cuadrito_445_sar), .izq(c13[4]), .der(pixel_cuadrito_476_siz), .dir(dir),
    .sar(pixel_cuadrito_444_sar), .siz(pixel_cuadrito_444_siz), .sde(c14[4]), .ZA_WARUDO(ZA_WARUDO),
    .reset(reset));  // open: in_7
  pixel_cuadrito pixel_cuadrito_445 (
    .clk(clk), .abajo(pixel_cuadrito_446_sar), .izq(c13[3]), .der(pixel_cuadrito_477_siz), .dir(dir),
    .sar(pixel_cuadrito_445_sar), .siz(pixel_cuadrito_445_siz), .sde(c14[3]), .ZA_WARUDO(ZA_WARUDO),
    .reset(reset));  // open: in_7
  pixel_cuadrito pixel_cuadrito_446 (
    .clk(clk), .abajo(pixel_cuadrito_447_sar), .izq(c13[2]), .der(pixel_cuadrito_478_siz), .dir(dir),
    .sar(pixel_cuadrito_446_sar), .siz(pixel_cuadrito_446_siz), .sde(c14[2]), .in_7(s13os14),
    .ZA_WARUDO(ZA_WARUDO), .reset(reset));
  pixel_cuadrito pixel_cuadrito_447 (
    .clk(clk), .abajo(pixel_cuadrito_448_sar), .izq(c13[1]), .der(pixel_cuadrito_479_siz), .dir(dir),
    .sar(pixel_cuadrito_447_sar), .siz(pixel_cuadrito_447_siz), .sde(c14[1]), .in_7(s13os14),
    .ZA_WARUDO(ZA_WARUDO), .reset(reset));
  pixel_cuadrito pixel_cuadrito_448 (
    .clk(clk), .abajo(c14[31]), .izq(c13[0]), .der(pixel_cuadrito_480_siz), .dir(dir),
    .sar(pixel_cuadrito_448_sar), .siz(pixel_cuadrito_448_siz), .sde(c14[0]), .ZA_WARUDO(ZA_WARUDO),
    .reset(reset));  // open: in_7
  pixel_cuadrito pixel_cuadrito_449 (
    .clk(clk), .abajo(pixel_cuadrito_450_sar), .izq(c14[31]), .der(pixel_cuadrito_481_siz), .dir(dir),
    .siz(pixel_cuadrito_449_siz), .sde(c15[31]), .ZA_WARUDO(ZA_WARUDO), .reset(reset));  // open: sar, in_7
  pixel_cuadrito pixel_cuadrito_450 (
    .clk(clk), .abajo(pixel_cuadrito_451_sar), .izq(c14[30]), .der(pixel_cuadrito_482_siz), .dir(dir),
    .sar(pixel_cuadrito_450_sar), .siz(pixel_cuadrito_450_siz), .sde(c15[30]), .ZA_WARUDO(ZA_WARUDO),
    .reset(reset));  // open: in_7
  pixel_cuadrito pixel_cuadrito_451 (
    .clk(clk), .abajo(pixel_cuadrito_452_sar), .izq(c14[29]), .der(pixel_cuadrito_483_siz), .dir(dir),
    .sar(pixel_cuadrito_451_sar), .siz(pixel_cuadrito_451_siz), .sde(c15[29]), .ZA_WARUDO(ZA_WARUDO),
    .reset(reset));  // open: in_7
  pixel_cuadrito pixel_cuadrito_452 (
    .clk(clk), .abajo(pixel_cuadrito_453_sar), .izq(c14[28]), .der(pixel_cuadrito_484_siz), .dir(dir),
    .sar(pixel_cuadrito_452_sar), .siz(pixel_cuadrito_452_siz), .sde(c15[28]), .ZA_WARUDO(ZA_WARUDO),
    .reset(reset));  // open: in_7
  pixel_cuadrito pixel_cuadrito_453 (
    .clk(clk), .abajo(pixel_cuadrito_454_sar), .izq(c14[27]), .der(pixel_cuadrito_485_siz), .dir(dir),
    .sar(pixel_cuadrito_453_sar), .siz(pixel_cuadrito_453_siz), .sde(c15[27]), .ZA_WARUDO(ZA_WARUDO),
    .reset(reset));  // open: in_7
  pixel_cuadrito pixel_cuadrito_454 (
    .clk(clk), .abajo(pixel_cuadrito_455_sar), .izq(c14[26]), .der(pixel_cuadrito_486_siz), .dir(dir),
    .sar(pixel_cuadrito_454_sar), .siz(pixel_cuadrito_454_siz), .sde(c15[26]), .ZA_WARUDO(ZA_WARUDO),
    .reset(reset));  // open: in_7
  pixel_cuadrito pixel_cuadrito_455 (
    .clk(clk), .abajo(pixel_cuadrito_456_sar), .izq(c14[25]), .der(pixel_cuadrito_487_siz), .dir(dir),
    .sar(pixel_cuadrito_455_sar), .siz(pixel_cuadrito_455_siz), .sde(c15[25]), .ZA_WARUDO(ZA_WARUDO),
    .reset(reset));  // open: in_7
  pixel_cuadrito pixel_cuadrito_456 (
    .clk(clk), .abajo(pixel_cuadrito_457_sar), .izq(c14[24]), .der(pixel_cuadrito_488_siz), .dir(dir),
    .sar(pixel_cuadrito_456_sar), .siz(pixel_cuadrito_456_siz), .sde(c15[24]), .ZA_WARUDO(ZA_WARUDO),
    .reset(reset));  // open: in_7
  pixel_cuadrito pixel_cuadrito_457 (
    .clk(clk), .abajo(pixel_cuadrito_458_sar), .izq(c14[23]), .der(pixel_cuadrito_489_siz), .dir(dir),
    .sar(pixel_cuadrito_457_sar), .siz(pixel_cuadrito_457_siz), .sde(c15[23]), .ZA_WARUDO(ZA_WARUDO),
    .reset(reset));  // open: in_7
  pixel_cuadrito pixel_cuadrito_458 (
    .clk(clk), .abajo(pixel_cuadrito_459_sar), .izq(c14[22]), .der(pixel_cuadrito_490_siz), .dir(dir),
    .sar(pixel_cuadrito_458_sar), .siz(pixel_cuadrito_458_siz), .sde(c15[22]), .ZA_WARUDO(ZA_WARUDO),
    .reset(reset));  // open: in_7
  pixel_cuadrito pixel_cuadrito_459 (
    .clk(clk), .abajo(pixel_cuadrito_460_sar), .izq(c14[21]), .der(pixel_cuadrito_491_siz), .dir(dir),
    .sar(pixel_cuadrito_459_sar), .siz(pixel_cuadrito_459_siz), .sde(c15[21]), .ZA_WARUDO(ZA_WARUDO),
    .reset(reset));  // open: in_7
  pixel_cuadrito pixel_cuadrito_460 (
    .clk(clk), .abajo(pixel_cuadrito_461_sar), .izq(c14[20]), .der(pixel_cuadrito_492_siz), .dir(dir),
    .sar(pixel_cuadrito_460_sar), .siz(pixel_cuadrito_460_siz), .sde(c15[20]), .ZA_WARUDO(ZA_WARUDO),
    .reset(reset));  // open: in_7
  pixel_cuadrito pixel_cuadrito_461 (
    .clk(clk), .abajo(pixel_cuadrito_462_sar), .izq(c14[19]), .der(pixel_cuadrito_493_siz), .dir(dir),
    .sar(pixel_cuadrito_461_sar), .siz(pixel_cuadrito_461_siz), .sde(c15[19]), .ZA_WARUDO(ZA_WARUDO),
    .reset(reset));  // open: in_7
  pixel_cuadrito pixel_cuadrito_462 (
    .clk(clk), .abajo(pixel_cuadrito_463_sar), .izq(c14[18]), .der(pixel_cuadrito_494_siz), .dir(dir),
    .sar(pixel_cuadrito_462_sar), .siz(pixel_cuadrito_462_siz), .sde(c15[18]), .ZA_WARUDO(ZA_WARUDO),
    .reset(reset));  // open: in_7
  pixel_cuadrito pixel_cuadrito_463 (
    .clk(clk), .abajo(pixel_cuadrito_464_sar), .izq(c14[17]), .der(pixel_cuadrito_495_siz), .dir(dir),
    .sar(pixel_cuadrito_463_sar), .siz(pixel_cuadrito_463_siz), .sde(c15[17]), .ZA_WARUDO(ZA_WARUDO),
    .reset(reset));  // open: in_7
  pixel_cuadrito pixel_cuadrito_464 (
    .clk(clk), .abajo(pixel_cuadrito_465_sar), .izq(c14[16]), .der(pixel_cuadrito_496_siz), .dir(dir),
    .sar(pixel_cuadrito_464_sar), .siz(pixel_cuadrito_464_siz), .sde(c15[16]), .ZA_WARUDO(ZA_WARUDO),
    .reset(reset));  // open: in_7
  pixel_cuadrito pixel_cuadrito_465 (
    .clk(clk), .abajo(pixel_cuadrito_466_sar), .izq(c14[15]), .der(pixel_cuadrito_497_siz), .dir(dir),
    .sar(pixel_cuadrito_465_sar), .siz(pixel_cuadrito_465_siz), .sde(c15[15]), .ZA_WARUDO(ZA_WARUDO),
    .reset(reset));  // open: in_7
  pixel_cuadrito pixel_cuadrito_466 (
    .clk(clk), .abajo(pixel_cuadrito_467_sar), .izq(c14[14]), .der(pixel_cuadrito_498_siz), .dir(dir),
    .sar(pixel_cuadrito_466_sar), .siz(pixel_cuadrito_466_siz), .sde(c15[14]), .ZA_WARUDO(ZA_WARUDO),
    .reset(reset));  // open: in_7
  pixel_cuadrito pixel_cuadrito_467 (
    .clk(clk), .abajo(pixel_cuadrito_468_sar), .izq(c14[13]), .der(pixel_cuadrito_499_siz), .dir(dir),
    .sar(pixel_cuadrito_467_sar), .siz(pixel_cuadrito_467_siz), .sde(c15[13]), .ZA_WARUDO(ZA_WARUDO),
    .reset(reset));  // open: in_7
  pixel_cuadrito pixel_cuadrito_468 (
    .clk(clk), .abajo(pixel_cuadrito_469_sar), .izq(c14[12]), .der(pixel_cuadrito_500_siz), .dir(dir),
    .sar(pixel_cuadrito_468_sar), .siz(pixel_cuadrito_468_siz), .sde(c15[12]), .ZA_WARUDO(ZA_WARUDO),
    .reset(reset));  // open: in_7
  pixel_cuadrito pixel_cuadrito_469 (
    .clk(clk), .abajo(pixel_cuadrito_470_sar), .izq(c14[11]), .der(pixel_cuadrito_501_siz), .dir(dir),
    .sar(pixel_cuadrito_469_sar), .siz(pixel_cuadrito_469_siz), .sde(c15[11]), .ZA_WARUDO(ZA_WARUDO),
    .reset(reset));  // open: in_7
  pixel_cuadrito pixel_cuadrito_470 (
    .clk(clk), .abajo(pixel_cuadrito_471_sar), .izq(c14[10]), .der(pixel_cuadrito_502_siz), .dir(dir),
    .sar(pixel_cuadrito_470_sar), .siz(pixel_cuadrito_470_siz), .sde(c15[10]), .ZA_WARUDO(ZA_WARUDO),
    .reset(reset));  // open: in_7
  pixel_cuadrito pixel_cuadrito_471 (
    .clk(clk), .abajo(pixel_cuadrito_472_sar), .izq(c14[9]), .der(pixel_cuadrito_503_siz), .dir(dir),
    .sar(pixel_cuadrito_471_sar), .siz(pixel_cuadrito_471_siz), .sde(c15[9]), .ZA_WARUDO(ZA_WARUDO),
    .reset(reset));  // open: in_7
  pixel_cuadrito pixel_cuadrito_472 (
    .clk(clk), .abajo(pixel_cuadrito_473_sar), .izq(c14[8]), .der(pixel_cuadrito_504_siz), .dir(dir),
    .sar(pixel_cuadrito_472_sar), .siz(pixel_cuadrito_472_siz), .sde(c15[8]), .ZA_WARUDO(ZA_WARUDO),
    .reset(reset));  // open: in_7
  pixel_cuadrito pixel_cuadrito_473 (
    .clk(clk), .abajo(pixel_cuadrito_474_sar), .izq(c14[7]), .der(pixel_cuadrito_505_siz), .dir(dir),
    .sar(pixel_cuadrito_473_sar), .siz(pixel_cuadrito_473_siz), .sde(c15[7]), .ZA_WARUDO(ZA_WARUDO),
    .reset(reset));  // open: in_7
  pixel_cuadrito pixel_cuadrito_474 (
    .clk(clk), .abajo(pixel_cuadrito_475_sar), .izq(c14[6]), .der(pixel_cuadrito_506_siz), .dir(dir),
    .sar(pixel_cuadrito_474_sar), .siz(pixel_cuadrito_474_siz), .sde(c15[6]), .ZA_WARUDO(ZA_WARUDO),
    .reset(reset));  // open: in_7
  pixel_cuadrito pixel_cuadrito_475 (
    .clk(clk), .abajo(pixel_cuadrito_476_sar), .izq(c14[5]), .der(pixel_cuadrito_507_siz), .dir(dir),
    .sar(pixel_cuadrito_475_sar), .siz(pixel_cuadrito_475_siz), .sde(c15[5]), .ZA_WARUDO(ZA_WARUDO),
    .reset(reset));  // open: in_7
  pixel_cuadrito pixel_cuadrito_476 (
    .clk(clk), .abajo(pixel_cuadrito_477_sar), .izq(c14[4]), .der(pixel_cuadrito_508_siz), .dir(dir),
    .sar(pixel_cuadrito_476_sar), .siz(pixel_cuadrito_476_siz), .sde(c15[4]), .ZA_WARUDO(ZA_WARUDO),
    .reset(reset));  // open: in_7
  pixel_cuadrito pixel_cuadrito_477 (
    .clk(clk), .abajo(pixel_cuadrito_478_sar), .izq(c14[3]), .der(pixel_cuadrito_509_siz), .dir(dir),
    .sar(pixel_cuadrito_477_sar), .siz(pixel_cuadrito_477_siz), .sde(c15[3]), .ZA_WARUDO(ZA_WARUDO),
    .reset(reset));  // open: in_7
  pixel_cuadrito pixel_cuadrito_478 (
    .clk(clk), .abajo(pixel_cuadrito_479_sar), .izq(c14[2]), .der(pixel_cuadrito_510_siz), .dir(dir),
    .sar(pixel_cuadrito_478_sar), .siz(pixel_cuadrito_478_siz), .sde(c15[2]), .in_7(s14os15),
    .ZA_WARUDO(ZA_WARUDO), .reset(reset));
  pixel_cuadrito pixel_cuadrito_479 (
    .clk(clk), .abajo(pixel_cuadrito_480_sar), .izq(c14[1]), .der(pixel_cuadrito_511_siz), .dir(dir),
    .sar(pixel_cuadrito_479_sar), .siz(pixel_cuadrito_479_siz), .sde(c15[1]), .in_7(s14os15),
    .ZA_WARUDO(ZA_WARUDO), .reset(reset));
  pixel_cuadrito pixel_cuadrito_480 (
    .clk(clk), .abajo(c15[31]), .izq(c14[0]), .der(pixel_cuadrito_512_siz), .dir(dir),
    .sar(pixel_cuadrito_480_sar), .siz(pixel_cuadrito_480_siz), .sde(c15[0]), .ZA_WARUDO(ZA_WARUDO),
    .reset(reset));  // open: in_7
  pixel_cuadrito pixel_cuadrito_481 (
    .clk(clk), .abajo(pixel_cuadrito_482_sar), .izq(c15[31]), .der(c1[31]), .dir(dir),
    .siz(pixel_cuadrito_481_siz), .sde(c16[31]), .ZA_WARUDO(ZA_WARUDO), .reset(reset));  // open: sar, in_7
  pixel_cuadrito pixel_cuadrito_482 (
    .clk(clk), .abajo(pixel_cuadrito_483_sar), .izq(c15[30]), .der(c1[30]), .dir(dir),
    .sar(pixel_cuadrito_482_sar), .siz(pixel_cuadrito_482_siz), .sde(c16[30]), .ZA_WARUDO(ZA_WARUDO),
    .reset(reset));  // open: in_7
  pixel_cuadrito pixel_cuadrito_483 (
    .clk(clk), .abajo(pixel_cuadrito_484_sar), .izq(c15[29]), .der(c1[29]), .dir(dir),
    .sar(pixel_cuadrito_483_sar), .siz(pixel_cuadrito_483_siz), .sde(c16[29]), .ZA_WARUDO(ZA_WARUDO));  // open: in_7, reset
  pixel_cuadrito pixel_cuadrito_484 (
    .clk(clk), .abajo(pixel_cuadrito_485_sar), .izq(c15[28]), .der(c1[28]), .dir(dir),
    .sar(pixel_cuadrito_484_sar), .siz(pixel_cuadrito_484_siz), .sde(c16[28]), .ZA_WARUDO(ZA_WARUDO),
    .reset(reset));  // open: in_7
  pixel_cuadrito pixel_cuadrito_485 (
    .clk(clk), .abajo(pixel_cuadrito_486_sar), .izq(c15[27]), .der(c1[27]), .dir(dir),
    .sar(pixel_cuadrito_485_sar), .siz(pixel_cuadrito_485_siz), .sde(c16[27]), .ZA_WARUDO(ZA_WARUDO),
    .reset(reset));  // open: in_7
  pixel_cuadrito pixel_cuadrito_486 (
    .clk(clk), .abajo(pixel_cuadrito_487_sar), .izq(c15[26]), .der(c1[26]), .dir(dir),
    .sar(pixel_cuadrito_486_sar), .siz(pixel_cuadrito_486_siz), .sde(c16[26]), .ZA_WARUDO(ZA_WARUDO),
    .reset(reset));  // open: in_7
  pixel_cuadrito pixel_cuadrito_487 (
    .clk(clk), .abajo(pixel_cuadrito_488_sar), .izq(c15[25]), .der(c1[25]), .dir(dir),
    .sar(pixel_cuadrito_487_sar), .siz(pixel_cuadrito_487_siz), .sde(c16[25]), .ZA_WARUDO(ZA_WARUDO),
    .reset(reset));  // open: in_7
  pixel_cuadrito pixel_cuadrito_488 (
    .clk(clk), .abajo(pixel_cuadrito_489_sar), .izq(c15[24]), .der(c1[24]), .dir(dir),
    .sar(pixel_cuadrito_488_sar), .siz(pixel_cuadrito_488_siz), .sde(c16[24]), .ZA_WARUDO(ZA_WARUDO),
    .reset(reset));  // open: in_7
  pixel_cuadrito pixel_cuadrito_489 (
    .clk(clk), .abajo(pixel_cuadrito_490_sar), .izq(c15[23]), .der(c1[23]), .dir(dir),
    .sar(pixel_cuadrito_489_sar), .siz(pixel_cuadrito_489_siz), .sde(c16[23]), .ZA_WARUDO(ZA_WARUDO),
    .reset(reset));  // open: in_7
  pixel_cuadrito pixel_cuadrito_490 (
    .clk(clk), .abajo(pixel_cuadrito_491_sar), .izq(c15[22]), .der(c1[22]), .dir(dir),
    .sar(pixel_cuadrito_490_sar), .siz(pixel_cuadrito_490_siz), .sde(c16[22]), .ZA_WARUDO(ZA_WARUDO),
    .reset(reset));  // open: in_7
  pixel_cuadrito pixel_cuadrito_491 (
    .clk(clk), .abajo(pixel_cuadrito_492_sar), .izq(c15[21]), .der(c1[21]), .dir(dir),
    .sar(pixel_cuadrito_491_sar), .siz(pixel_cuadrito_491_siz), .sde(c16[21]), .ZA_WARUDO(ZA_WARUDO),
    .reset(reset));  // open: in_7
  pixel_cuadrito pixel_cuadrito_492 (
    .clk(clk), .abajo(pixel_cuadrito_493_sar), .izq(c15[20]), .der(c1[20]), .dir(dir),
    .sar(pixel_cuadrito_492_sar), .siz(pixel_cuadrito_492_siz), .sde(c16[20]), .ZA_WARUDO(ZA_WARUDO),
    .reset(reset));  // open: in_7
  pixel_cuadrito pixel_cuadrito_493 (
    .clk(clk), .abajo(pixel_cuadrito_494_sar), .izq(c15[19]), .der(c1[19]), .dir(dir),
    .sar(pixel_cuadrito_493_sar), .siz(pixel_cuadrito_493_siz), .sde(c16[19]), .ZA_WARUDO(ZA_WARUDO),
    .reset(reset));  // open: in_7
  pixel_cuadrito pixel_cuadrito_494 (
    .clk(clk), .abajo(pixel_cuadrito_495_sar), .izq(c15[18]), .der(c1[18]), .dir(dir),
    .sar(pixel_cuadrito_494_sar), .siz(pixel_cuadrito_494_siz), .sde(c16[18]), .ZA_WARUDO(ZA_WARUDO),
    .reset(reset));  // open: in_7
  pixel_cuadrito pixel_cuadrito_495 (
    .clk(clk), .abajo(pixel_cuadrito_496_sar), .izq(c15[17]), .der(c1[17]), .dir(dir),
    .sar(pixel_cuadrito_495_sar), .siz(pixel_cuadrito_495_siz), .sde(c16[17]), .ZA_WARUDO(ZA_WARUDO),
    .reset(reset));  // open: in_7
  pixel_cuadrito pixel_cuadrito_496 (
    .clk(clk), .abajo(pixel_cuadrito_497_sar), .izq(c15[16]), .der(c1[16]), .dir(dir),
    .sar(pixel_cuadrito_496_sar), .siz(pixel_cuadrito_496_siz), .sde(c16[16]), .ZA_WARUDO(ZA_WARUDO),
    .reset(reset));  // open: in_7
  pixel_cuadrito pixel_cuadrito_497 (
    .clk(clk), .abajo(pixel_cuadrito_498_sar), .izq(c15[15]), .der(c1[15]), .dir(dir),
    .sar(pixel_cuadrito_497_sar), .siz(pixel_cuadrito_497_siz), .sde(c16[15]), .ZA_WARUDO(ZA_WARUDO),
    .reset(reset));  // open: in_7
  pixel_cuadrito pixel_cuadrito_498 (
    .clk(clk), .abajo(pixel_cuadrito_499_sar), .izq(c15[14]), .der(c1[14]), .dir(dir),
    .sar(pixel_cuadrito_498_sar), .siz(pixel_cuadrito_498_siz), .sde(c16[14]), .ZA_WARUDO(ZA_WARUDO),
    .reset(reset));  // open: in_7
  pixel_cuadrito pixel_cuadrito_499 (
    .clk(clk), .abajo(pixel_cuadrito_500_sar), .izq(c15[13]), .der(c1[13]), .dir(dir),
    .sar(pixel_cuadrito_499_sar), .siz(pixel_cuadrito_499_siz), .sde(c16[13]), .ZA_WARUDO(ZA_WARUDO),
    .reset(reset));  // open: in_7
  pixel_cuadrito pixel_cuadrito_500 (
    .clk(clk), .abajo(pixel_cuadrito_501_sar), .izq(c15[12]), .der(c1[12]), .dir(dir),
    .sar(pixel_cuadrito_500_sar), .siz(pixel_cuadrito_500_siz), .sde(c16[12]), .ZA_WARUDO(ZA_WARUDO),
    .reset(reset));  // open: in_7
  pixel_cuadrito pixel_cuadrito_501 (
    .clk(clk), .abajo(pixel_cuadrito_502_sar), .izq(c15[11]), .der(c1[11]), .dir(dir),
    .sar(pixel_cuadrito_501_sar), .siz(pixel_cuadrito_501_siz), .sde(c16[11]), .ZA_WARUDO(ZA_WARUDO),
    .reset(reset));  // open: in_7
  pixel_cuadrito pixel_cuadrito_502 (
    .clk(clk), .abajo(pixel_cuadrito_503_sar), .izq(c15[10]), .der(c1[10]), .dir(dir),
    .sar(pixel_cuadrito_502_sar), .siz(pixel_cuadrito_502_siz), .sde(c16[10]), .ZA_WARUDO(ZA_WARUDO),
    .reset(reset));  // open: in_7
  pixel_cuadrito pixel_cuadrito_503 (
    .clk(clk), .abajo(pixel_cuadrito_504_sar), .izq(c15[9]), .der(c1[9]), .dir(dir),
    .sar(pixel_cuadrito_503_sar), .siz(pixel_cuadrito_503_siz), .sde(c16[9]), .ZA_WARUDO(ZA_WARUDO),
    .reset(reset));  // open: in_7
  pixel_cuadrito pixel_cuadrito_504 (
    .clk(clk), .abajo(pixel_cuadrito_505_sar), .izq(c15[8]), .der(c1[8]), .dir(dir),
    .sar(pixel_cuadrito_504_sar), .siz(pixel_cuadrito_504_siz), .sde(c16[8]), .ZA_WARUDO(ZA_WARUDO),
    .reset(reset));  // open: in_7
  pixel_cuadrito pixel_cuadrito_505 (
    .clk(clk), .abajo(pixel_cuadrito_506_sar), .izq(c15[7]), .der(c1[7]), .dir(dir),
    .sar(pixel_cuadrito_505_sar), .siz(pixel_cuadrito_505_siz), .sde(c16[7]), .ZA_WARUDO(ZA_WARUDO),
    .reset(reset));  // open: in_7
  pixel_cuadrito pixel_cuadrito_506 (
    .clk(clk), .abajo(pixel_cuadrito_507_sar), .izq(c15[6]), .der(c1[6]), .dir(dir),
    .sar(pixel_cuadrito_506_sar), .siz(pixel_cuadrito_506_siz), .sde(c16[6]), .ZA_WARUDO(ZA_WARUDO),
    .reset(reset));  // open: in_7
  pixel_cuadrito pixel_cuadrito_507 (
    .clk(clk), .abajo(pixel_cuadrito_508_sar), .izq(c15[5]), .der(c1[5]), .dir(dir),
    .sar(pixel_cuadrito_507_sar), .siz(pixel_cuadrito_507_siz), .sde(c16[5]), .ZA_WARUDO(ZA_WARUDO),
    .reset(reset));  // open: in_7
  pixel_cuadrito pixel_cuadrito_508 (
    .clk(clk), .abajo(pixel_cuadrito_509_sar), .izq(c15[4]), .der(c1[4]), .dir(dir),
    .sar(pixel_cuadrito_508_sar), .siz(pixel_cuadrito_508_siz), .sde(c16[4]), .ZA_WARUDO(ZA_WARUDO),
    .reset(reset));  // open: in_7
  pixel_cuadrito pixel_cuadrito_509 (
    .clk(clk), .abajo(pixel_cuadrito_510_sar), .izq(c15[3]), .der(c1[3]), .dir(dir),
    .sar(pixel_cuadrito_509_sar), .siz(pixel_cuadrito_509_siz), .sde(c16[3]), .ZA_WARUDO(ZA_WARUDO),
    .reset(reset));  // open: in_7
  pixel_cuadrito pixel_cuadrito_510 (
    .clk(clk), .abajo(pixel_cuadrito_511_sar), .izq(c15[2]), .der(c1[2]), .dir(dir),
    .sar(pixel_cuadrito_510_sar), .siz(pixel_cuadrito_510_siz), .sde(c16[2]), .in_7(start16),
    .ZA_WARUDO(ZA_WARUDO), .reset(reset));
  pixel_cuadrito pixel_cuadrito_511 (
    .clk(clk), .abajo(pixel_cuadrito_512_sar), .izq(c15[1]), .der(c1[1]), .dir(dir),
    .sar(pixel_cuadrito_511_sar), .siz(pixel_cuadrito_511_siz), .sde(c16[1]), .in_7(start16),
    .ZA_WARUDO(ZA_WARUDO), .reset(reset));
  pixel_cuadrito pixel_cuadrito_512 (
    .clk(clk), .abajo(c16[31]), .izq(c15[0]), .der(c1[0]), .dir(dir), .sar(pixel_cuadrito_512_sar),
    .siz(pixel_cuadrito_512_siz), .sde(c16[0]), .ZA_WARUDO(ZA_WARUDO), .reset(reset));  // open: in_7
  Clock click (.out(clk));

  // Other names for the same wires on the sheet: _497 = c1[0]; _481 = c1[1]; _465 = c1[2]; _449 = c1[3]; _433 = c1[4];
  //   _417 = c1[5]; _401 = c1[6]; _385 = c1[7]; _369 = c1[8]; _353 = c1[9]; _337 = c1[10]; _321 = c1[11];
  //   _305 = c1[12]; _289 = c1[13]; _273 = c1[14]; _257 = c1[15]; _241 = c1[16]; _225 = c1[17]; _209 = c1[18];
  //   _193 = c1[19]; _177 = c1[20]; _161 = c1[21]; _145 = c1[22]; _129 = c1[23]; _113 = c1[24]; _97 = c1[25];
  //   _81 = c1[26]; _65 = c1[27]; _49 = c1[28]; _33 = c1[29]; _17 = c1[30]; _1 = c1[31]; _498 = c2[0]; _482 = c2[1];
  //   _466 = c2[2]; _450 = c2[3]; _434 = c2[4]; _418 = c2[5]; _402 = c2[6]; _386 = c2[7]; _370 = c2[8]; _354 = c2[9];
  //   _338 = c2[10]; _322 = c2[11]; _306 = c2[12]; _290 = c2[13]; _274 = c2[14]; _258 = c2[15]; _242 = c2[16];
  //   _226 = c2[17]; _210 = c2[18]; _194 = c2[19]; _178 = c2[20]; _162 = c2[21]; _146 = c2[22]; _130 = c2[23];
  //   _114 = c2[24]; _98 = c2[25]; _82 = c2[26]; _66 = c2[27]; _50 = c2[28]; _34 = c2[29]; _18 = c2[30]; _2 = c2[31];
  //   _499 = c3[0]; _483 = c3[1]; _467 = c3[2]; _451 = c3[3]; _435 = c3[4]; _419 = c3[5]; _403 = c3[6]; _387 = c3[7];
  //   _371 = c3[8]; _355 = c3[9]; _339 = c3[10]; _323 = c3[11]; _307 = c3[12]; _291 = c3[13]; _275 = c3[14];
  //   _259 = c3[15]; _243 = c3[16]; _227 = c3[17]; _211 = c3[18]; _195 = c3[19]; _179 = c3[20]; _163 = c3[21];
  //   _147 = c3[22]; _131 = c3[23]; _115 = c3[24]; _99 = c3[25]; _83 = c3[26]; _67 = c3[27]; _51 = c3[28];
  //   _35 = c3[29]; _19 = c3[30]; _3 = c3[31]; _500 = c4[0]; _484 = c4[1]; _468 = c4[2]; _452 = c4[3]; _436 = c4[4];
  //   _420 = c4[5]; _404 = c4[6]; _388 = c4[7]; _372 = c4[8]; _356 = c4[9]; _340 = c4[10]; _324 = c4[11];
  //   _308 = c4[12]; _292 = c4[13]; _276 = c4[14]; _260 = c4[15]; _244 = c4[16]; _228 = c4[17]; _212 = c4[18];
  //   _196 = c4[19]; _180 = c4[20]; _164 = c4[21]; _148 = c4[22]; _132 = c4[23]; _116 = c4[24]; _100 = c4[25];
  //   _84 = c4[26]; _68 = c4[27]; _52 = c4[28]; _36 = c4[29]; _20 = c4[30]; _4 = c4[31]; _501 = c5[0]; _485 = c5[1];
  //   _469 = c5[2]; _453 = c5[3]; _437 = c5[4]; _421 = c5[5]; _405 = c5[6]; _389 = c5[7]; _373 = c5[8]; _357 = c5[9];
  //   _341 = c5[10]; _325 = c5[11]; _309 = c5[12]; _293 = c5[13]; _277 = c5[14]; _261 = c5[15]; _245 = c5[16];
  //   _229 = c5[17]; _213 = c5[18]; _197 = c5[19]; _181 = c5[20]; _165 = c5[21]; _149 = c5[22]; _133 = c5[23];
  //   _117 = c5[24]; _101 = c5[25]; _85 = c5[26]; _69 = c5[27]; _53 = c5[28]; _37 = c5[29]; _21 = c5[30]; _5 = c5[31];
  //   _502 = c6[0]; _486 = c6[1]; _470 = c6[2]; _454 = c6[3]; _438 = c6[4]; _422 = c6[5]; _406 = c6[6]; _390 = c6[7];
  //   _374 = c6[8]; _358 = c6[9]; _342 = c6[10]; _326 = c6[11]; _310 = c6[12]; _294 = c6[13]; _278 = c6[14];
  //   _262 = c6[15]; _246 = c6[16]; _230 = c6[17]; _214 = c6[18]; _198 = c6[19]; _182 = c6[20]; _166 = c6[21];
  //   _150 = c6[22]; _134 = c6[23]; _118 = c6[24]; _102 = c6[25]; _86 = c6[26]; _70 = c6[27]; _54 = c6[28];
  //   _38 = c6[29]; _22 = c6[30]; _6 = c6[31]; _503 = c7[0]; _487 = c7[1]; _471 = c7[2]; _455 = c7[3]; _439 = c7[4];
  //   _423 = c7[5]; _407 = c7[6]; _391 = c7[7]; _375 = c7[8]; _359 = c7[9]; _343 = c7[10]; _327 = c7[11];
  //   _311 = c7[12]; _295 = c7[13]; _279 = c7[14]; _263 = c7[15]; _247 = c7[16]; _231 = c7[17]; _215 = c7[18];
  //   _199 = c7[19]; _183 = c7[20]; _167 = c7[21]; _151 = c7[22]; _135 = c7[23]; _119 = c7[24]; _103 = c7[25];
  //   _87 = c7[26]; _71 = c7[27]; _55 = c7[28]; _39 = c7[29]; _23 = c7[30]; _7 = c7[31]; _504 = c8[0]; _488 = c8[1];
  //   _472 = c8[2]; _456 = c8[3]; _440 = c8[4]; _424 = c8[5]; _408 = c8[6]; _392 = c8[7]; _376 = c8[8]; _360 = c8[9];
  //   _344 = c8[10]; _328 = c8[11]; _312 = c8[12]; _296 = c8[13]; _280 = c8[14]; _264 = c8[15]; _248 = c8[16];
  //   _232 = c8[17]; _216 = c8[18]; _200 = c8[19]; _184 = c8[20]; _168 = c8[21]; _152 = c8[22]; _136 = c8[23];
  //   _120 = c8[24]; _104 = c8[25]; _88 = c8[26]; _72 = c8[27]; _56 = c8[28]; _40 = c8[29]; _24 = c8[30]; _8 = c8[31];
  //   _505 = c9[0]; _489 = c9[1]; _473 = c9[2]; _457 = c9[3]; _441 = c9[4]; _425 = c9[5]; _409 = c9[6]; _393 = c9[7];
  //   _377 = c9[8]; _361 = c9[9]; _345 = c9[10]; _329 = c9[11]; _313 = c9[12]; _297 = c9[13]; _281 = c9[14];
  //   _265 = c9[15]; _249 = c9[16]; _233 = c9[17]; _217 = c9[18]; _201 = c9[19]; _185 = c9[20]; _169 = c9[21];
  //   _153 = c9[22]; _137 = c9[23]; _121 = c9[24]; _105 = c9[25]; _89 = c9[26]; _73 = c9[27]; _57 = c9[28];
  //   _41 = c9[29]; _25 = c9[30]; _9 = c9[31]; _506 = c10[0]; _490 = c10[1]; _474 = c10[2]; _458 = c10[3];
  //   _442 = c10[4]; _426 = c10[5]; _410 = c10[6]; _394 = c10[7]; _378 = c10[8]; _362 = c10[9]; _346 = c10[10];
  //   _330 = c10[11]; _314 = c10[12]; _298 = c10[13]; _282 = c10[14]; _266 = c10[15]; _250 = c10[16]; _234 = c10[17];
  //   _218 = c10[18]; _202 = c10[19]; _186 = c10[20]; _170 = c10[21]; _154 = c10[22]; _138 = c10[23]; _122 = c10[24];
  //   _106 = c10[25]; _90 = c10[26]; _74 = c10[27]; _58 = c10[28]; _42 = c10[29]; _26 = c10[30]; _10 = c10[31];
  //   _507 = c11[0]; _491 = c11[1]; _475 = c11[2]; _459 = c11[3]; _443 = c11[4]; _427 = c11[5]; _411 = c11[6];
  //   _395 = c11[7]; _379 = c11[8]; _363 = c11[9]; _347 = c11[10]; _331 = c11[11]; _315 = c11[12]; _299 = c11[13];
  //   _283 = c11[14]; _267 = c11[15]; _251 = c11[16]; _235 = c11[17]; _219 = c11[18]; _203 = c11[19]; _187 = c11[20];
  //   _171 = c11[21]; _155 = c11[22]; _139 = c11[23]; _123 = c11[24]; _107 = c11[25]; _91 = c11[26]; _75 = c11[27];
  //   _59 = c11[28]; _43 = c11[29]; _27 = c11[30]; _11 = c11[31]; _508 = c12[0]; _492 = c12[1]; _476 = c12[2];
  //   _460 = c12[3]; _444 = c12[4]; _428 = c12[5]; _412 = c12[6]; _396 = c12[7]; _380 = c12[8]; _364 = c12[9];
  //   _348 = c12[10]; _332 = c12[11]; _316 = c12[12]; _300 = c12[13]; _284 = c12[14]; _268 = c12[15]; _252 = c12[16];
  //   _236 = c12[17]; _220 = c12[18]; _204 = c12[19]; _188 = c12[20]; _172 = c12[21]; _156 = c12[22]; _140 = c12[23];
  //   _124 = c12[24]; _108 = c12[25]; _92 = c12[26]; _76 = c12[27]; _60 = c12[28]; _44 = c12[29]; _28 = c12[30];
  //   _12 = c12[31]; _509 = c13[0]; _493 = c13[1]; _477 = c13[2]; _461 = c13[3]; _445 = c13[4]; _429 = c13[5];
  //   _413 = c13[6]; _397 = c13[7]; _381 = c13[8]; _365 = c13[9]; _349 = c13[10]; _333 = c13[11]; _317 = c13[12];
  //   _301 = c13[13]; _285 = c13[14]; _269 = c13[15]; _253 = c13[16]; _237 = c13[17]; _221 = c13[18]; _205 = c13[19];
  //   _189 = c13[20]; _173 = c13[21]; _157 = c13[22]; _141 = c13[23]; _125 = c13[24]; _109 = c13[25]; _93 = c13[26];
  //   _77 = c13[27]; _61 = c13[28]; _45 = c13[29]; _29 = c13[30]; _13 = c13[31]; _510 = c14[0]; _494 = c14[1];
  //   _478 = c14[2]; _462 = c14[3]; _446 = c14[4]; _430 = c14[5]; _414 = c14[6]; _398 = c14[7]; _382 = c14[8];
  //   _366 = c14[9]; _350 = c14[10]; _334 = c14[11]; _318 = c14[12]; _302 = c14[13]; _286 = c14[14]; _270 = c14[15];
  //   _254 = c14[16]; _238 = c14[17]; _222 = c14[18]; _206 = c14[19]; _190 = c14[20]; _174 = c14[21]; _158 = c14[22];
  //   _142 = c14[23]; _126 = c14[24]; _110 = c14[25]; _94 = c14[26]; _78 = c14[27]; _62 = c14[28]; _46 = c14[29];
  //   _30 = c14[30]; _14 = c14[31]; _511 = c15[0]; _495 = c15[1]; _479 = c15[2]; _463 = c15[3]; _447 = c15[4];
  //   _431 = c15[5]; _415 = c15[6]; _399 = c15[7]; _383 = c15[8]; _367 = c15[9]; _351 = c15[10]; _335 = c15[11];
  //   _319 = c15[12]; _303 = c15[13]; _287 = c15[14]; _271 = c15[15]; _255 = c15[16]; _239 = c15[17]; _223 = c15[18];
  //   _207 = c15[19]; _191 = c15[20]; _175 = c15[21]; _159 = c15[22]; _143 = c15[23]; _127 = c15[24]; _111 = c15[25];
  //   _95 = c15[26]; _79 = c15[27]; _63 = c15[28]; _47 = c15[29]; _31 = c15[30]; _15 = c15[31]; _512 = c16[0];
  //   _496 = c16[1]; _480 = c16[2]; _464 = c16[3]; _448 = c16[4]; _432 = c16[5]; _416 = c16[6]; _400 = c16[7];
  //   _384 = c16[8]; _368 = c16[9]; _352 = c16[10]; _336 = c16[11]; _320 = c16[12]; _304 = c16[13]; _288 = c16[14];
  //   _272 = c16[15]; _256 = c16[16]; _240 = c16[17]; _224 = c16[18]; _208 = c16[19]; _192 = c16[20]; _176 = c16[21];
  //   _160 = c16[22]; _144 = c16[23]; _128 = c16[24]; _112 = c16[25]; _96 = c16[26]; _80 = c16[27]; _64 = c16[28];
  //   _48 = c16[29]; _32 = c16[30]; _16 = c16[31]; r = reset; z = ZA_WARUDO
endmodule

// generar_columna
module generar_barrera (
  input  generar,
  input  reset,
  input  activo,
  output [31:0] columna1,
  output [31:0] columna2,
  output [31:0] columna3,
  output [31:0] columna4,
  output [31:0] columna5,
  output [31:0] columna6,
  output [31:0] columna7,
  output [31:0] columna8,
  output [31:0] columna9,
  output [31:0] columna10,
  output [31:0] columna11,
  output [31:0] columna12,
  output [31:0] columna13,
  output [31:0] columna14,
  output [31:0] columna15,
  output [31:0] columna16
);

  wire and_1_out, comparator_1_lt, or_1_out;
  wire [3:0] columna_out, divider_1_rem;
  wire [4:0] adder_1_out, adder_2_out, anterior_q, fila_out_5;
  wire [31:0] demultiplexer_1_out1, demultiplexer_1_out2, demultiplexer_1_out3, demultiplexer_1_out4,
       demultiplexer_1_out5, demultiplexer_1_out6, demultiplexer_1_out7, demultiplexer_1_out8,
       demultiplexer_1_out9, demultiplexer_1_out10, demultiplexer_1_out11, demultiplexer_1_out12,
       demultiplexer_1_out13, demultiplexer_1_out14, demultiplexer_1_out15;
  wire [31:2] decoder_1_out29;

  and and_1 (and_1_out, activo, or_1_out);
  or or_1 (or_1_out, reset, comparator_1_lt);
  Register #(.width(5)) anterior (.D(fila_out_5), .en(and_1_out), .Q(anterior_q), .clk(generar));  // open: clr
  Random #(.width(4), .seed(-200)) columna (.clk(generar), .next(and_1_out), .out(columna_out));  // open: clr
  Adder #(.width(5)) adder_1 (.a(5'b00101), .b(anterior_q), .out(adder_1_out));  // open: cin, cout
  Adder #(.width(5)) adder_2 (.a(anterior_q), .b(5'b00011), .out(adder_2_out));  // open: cin, cout
  random fila (.sup(adder_1_out), .inf(adder_2_out), .click(generar), .activo(and_1_out), .out_5(fila_out_5));
  Comparator #(.width(5), .mode("unsigned")) comparator_1 (
    .a(anterior_q), .b(5'b11000), .lt(comparator_1_lt));  // open: gt, eq
  Decoder #(.select(5), .enable("false")) decoder_1 (
    .out0(decoder_1_out29[31]), .out1(decoder_1_out29[30]), .out2(decoder_1_out29[29]),
    .out3(decoder_1_out29[28]), .out4(decoder_1_out29[27]), .out5(decoder_1_out29[26]),
    .out6(decoder_1_out29[25]), .out7(decoder_1_out29[24]), .out8(decoder_1_out29[23]),
    .out9(decoder_1_out29[22]), .out10(decoder_1_out29[21]), .out11(decoder_1_out29[20]),
    .out12(decoder_1_out29[19]), .out13(decoder_1_out29[18]), .out14(decoder_1_out29[17]),
    .out15(decoder_1_out29[16]), .out16(decoder_1_out29[15]), .out17(decoder_1_out29[14]),
    .out18(decoder_1_out29[13]), .out19(decoder_1_out29[12]), .out20(decoder_1_out29[11]),
    .out21(decoder_1_out29[10]), .out22(decoder_1_out29[9]), .out23(decoder_1_out29[8]),
    .out24(decoder_1_out29[7]), .out25(decoder_1_out29[6]), .out26(decoder_1_out29[5]),
    .out27(decoder_1_out29[4]), .out28(decoder_1_out29[3]), .out29(decoder_1_out29[2]), .sel(fila_out_5));  // open: out30, out31
  Divider #(.width(4)) divider_1 (.a(columna_out), .b(4'b1011), .rem(divider_1_rem));  // open: out, upper
  Demultiplexer #(.select(4), .width(32), .disabled(0)) demultiplexer_1 (
    .out0(columna1), .out1(demultiplexer_1_out1), .out2(demultiplexer_1_out2), .out3(demultiplexer_1_out3),
    .out4(demultiplexer_1_out4), .out5(demultiplexer_1_out5), .out6(demultiplexer_1_out6),
    .out7(demultiplexer_1_out7), .out8(demultiplexer_1_out8), .out9(demultiplexer_1_out9),
    .out10(demultiplexer_1_out10), .out11(demultiplexer_1_out11), .out12(demultiplexer_1_out12),
    .out13(demultiplexer_1_out13), .out14(demultiplexer_1_out14), .out15(demultiplexer_1_out15),
    .in({decoder_1_out29, 2'b00}), .sel(divider_1_rem), .en(activo));
  assign columna2 = columna1 | demultiplexer_1_out1;  // OR_Gate or_2, 32 bits wide
  assign columna3 = columna1 | demultiplexer_1_out1 | demultiplexer_1_out2;  // OR_Gate or_3, 32 bits wide
  assign columna4 = columna1 | demultiplexer_1_out1 | demultiplexer_1_out2 | demultiplexer_1_out3;  // OR_Gate or_4, 32 bits wide
  assign columna5 = columna1 | demultiplexer_1_out1 | demultiplexer_1_out2 | demultiplexer_1_out3 | demultiplexer_1_out4;  // OR_Gate or_5, 32 bits wide
  assign columna6 = columna1 | demultiplexer_1_out1 | demultiplexer_1_out2 | demultiplexer_1_out3 | demultiplexer_1_out4 | demultiplexer_1_out5;  // OR_Gate or_6, 32 bits wide
  assign columna7 = demultiplexer_1_out1 | demultiplexer_1_out2 | demultiplexer_1_out3 | demultiplexer_1_out4 | demultiplexer_1_out5 | demultiplexer_1_out6;  // OR_Gate or_7, 32 bits wide
  assign columna8 = demultiplexer_1_out2 | demultiplexer_1_out3 | demultiplexer_1_out4 | demultiplexer_1_out5 | demultiplexer_1_out6 | demultiplexer_1_out7;  // OR_Gate or_8, 32 bits wide
  assign columna9 = demultiplexer_1_out3 | demultiplexer_1_out4 | demultiplexer_1_out5 | demultiplexer_1_out6 | demultiplexer_1_out7 | demultiplexer_1_out8;  // OR_Gate or_9, 32 bits wide
  assign columna10 = demultiplexer_1_out4 | demultiplexer_1_out5 | demultiplexer_1_out6 | demultiplexer_1_out7 | demultiplexer_1_out8 | demultiplexer_1_out9;  // OR_Gate or_10, 32 bits wide
  assign columna11 = demultiplexer_1_out5 | demultiplexer_1_out6 | demultiplexer_1_out7 | demultiplexer_1_out8 | demultiplexer_1_out9 | demultiplexer_1_out10;  // OR_Gate or_11, 32 bits wide
  assign columna12 = demultiplexer_1_out6 | demultiplexer_1_out7 | demultiplexer_1_out8 | demultiplexer_1_out9 | demultiplexer_1_out10 | demultiplexer_1_out11;  // OR_Gate or_12, 32 bits wide
  assign columna13 = demultiplexer_1_out7 | demultiplexer_1_out8 | demultiplexer_1_out9 | demultiplexer_1_out10 | demultiplexer_1_out11 | demultiplexer_1_out12;  // OR_Gate or_13, 32 bits wide
  assign columna14 = demultiplexer_1_out8 | demultiplexer_1_out9 | demultiplexer_1_out10 | demultiplexer_1_out11 | demultiplexer_1_out12 | demultiplexer_1_out13;  // OR_Gate or_14, 32 bits wide
  assign columna15 = demultiplexer_1_out9 | demultiplexer_1_out10 | demultiplexer_1_out11 | demultiplexer_1_out12 | demultiplexer_1_out13 | demultiplexer_1_out14;  // OR_Gate or_15, 32 bits wide
  assign columna16 = demultiplexer_1_out10 | demultiplexer_1_out11 | demultiplexer_1_out12 | demultiplexer_1_out13 | demultiplexer_1_out14 | demultiplexer_1_out15;  // OR_Gate or_16, 32 bits wide
endmodule

module pixel (
  input  reset,
  input  click,
  input  entrada,
  output salida
);

  wire or_1_out;

  or or_1 (or_1_out, salida, entrada);
  D_Flip_Flop d_ff_1 (.clk(click), .D(or_1_out), .Q(salida), .reset(reset));  // open: Qn, preset, en
endmodule

// col
module columna (
  input  reset,
  input  [31:0] entrada,
  input  click,
  output [31:0] salida
);

  pixel pixel_1 (.reset(reset), .click(click), .entrada(entrada[0]), .salida(salida[0]));
  pixel pixel_2 (.reset(reset), .click(click), .entrada(entrada[1]), .salida(salida[1]));
  pixel pixel_3 (.reset(reset), .click(click), .entrada(entrada[2]), .salida(salida[2]));
  pixel pixel_4 (.reset(reset), .click(click), .entrada(entrada[3]), .salida(salida[3]));
  pixel pixel_5 (.reset(reset), .click(click), .entrada(entrada[4]), .salida(salida[4]));
  pixel pixel_6 (.reset(reset), .click(click), .entrada(entrada[5]), .salida(salida[5]));
  pixel pixel_7 (.reset(reset), .click(click), .entrada(entrada[6]), .salida(salida[6]));
  pixel pixel_8 (.reset(reset), .click(click), .entrada(entrada[7]), .salida(salida[7]));
  pixel pixel_9 (.reset(reset), .click(click), .entrada(entrada[8]), .salida(salida[8]));
  pixel pixel_10 (.reset(reset), .click(click), .entrada(entrada[9]), .salida(salida[9]));
  pixel pixel_11 (.reset(reset), .click(click), .entrada(entrada[10]), .salida(salida[10]));
  pixel pixel_12 (.reset(reset), .click(click), .entrada(entrada[11]), .salida(salida[11]));
  pixel pixel_13 (.reset(reset), .click(click), .entrada(entrada[12]), .salida(salida[12]));
  pixel pixel_14 (.reset(reset), .click(click), .entrada(entrada[13]), .salida(salida[13]));
  pixel pixel_15 (.reset(reset), .click(click), .entrada(entrada[14]), .salida(salida[14]));
  pixel pixel_16 (.reset(reset), .click(click), .entrada(entrada[15]), .salida(salida[15]));
  pixel pixel_17 (.reset(reset), .click(click), .entrada(entrada[16]), .salida(salida[16]));
  pixel pixel_18 (.reset(reset), .click(click), .entrada(entrada[17]), .salida(salida[17]));
  pixel pixel_19 (.reset(reset), .click(click), .entrada(entrada[18]), .salida(salida[18]));
  pixel pixel_20 (.reset(reset), .click(click), .entrada(entrada[19]), .salida(salida[19]));
  pixel pixel_21 (.reset(reset), .click(click), .entrada(entrada[20]), .salida(salida[20]));
  pixel pixel_22 (.reset(reset), .click(click), .entrada(entrada[21]), .salida(salida[21]));
  pixel pixel_23 (.reset(reset), .click(click), .entrada(entrada[22]), .salida(salida[22]));
  pixel pixel_24 (.reset(reset), .click(click), .entrada(entrada[23]), .salida(salida[23]));
  pixel pixel_25 (.reset(reset), .click(click), .entrada(entrada[24]), .salida(salida[24]));
  pixel pixel_26 (.reset(reset), .click(click), .entrada(entrada[25]), .salida(salida[25]));
  pixel pixel_27 (.reset(reset), .click(click), .entrada(entrada[26]), .salida(salida[26]));
  pixel pixel_28 (.reset(reset), .click(click), .entrada(entrada[27]), .salida(salida[27]));
  pixel pixel_29 (.reset(reset), .click(click), .entrada(entrada[28]), .salida(salida[28]));
  pixel pixel_30 (.reset(reset), .click(click), .entrada(entrada[29]), .salida(salida[29]));
  pixel pixel_31 (.reset(reset), .click(click), .entrada(entrada[30]), .salida(salida[30]));
  pixel pixel_32 (.reset(reset), .click(click), .entrada(entrada[31]), .salida(salida[31]));
endmodule

// rand
module random (
  input  [4:0] sup,
  input  [4:0] inf,
  input  click,
  input  activo,
  output [4:0] out_5
);

  wire [4:0] adder_1_out, divider_1_rem, random_1_out, subtractor_1_out;

  Random #(.width(5), .seed(-2000)) random_1 (.clk(click), .next(activo), .out(random_1_out));  // open: clr
  Adder #(.width(5)) adder_1 (.a(5'b00001), .b(subtractor_1_out), .out(adder_1_out));  // open: cin, cout
  Subtractor #(.width(5)) subtractor_1 (.a(sup), .b(inf), .out(subtractor_1_out));  // open: bin, bout
  Divider #(.width(5)) divider_1 (.a(random_1_out), .b(adder_1_out), .rem(divider_1_rem));  // open: out, upper
  Adder #(.width(5)) adder_2 (.a(divider_1_rem), .b(inf), .out(out_5));  // open: cin, cout
endmodule

module teclado (
  input  e6,
  input  e5,
  input  e4,
  input  e3,
  input  e2,
  input  e1,
  input  e0,
  output s1,
  output s0
);

  wire and_1_out, and_2_out, not_1_out, not_2_out, not_3_out, not_4_out, not_5_out, not_6_out, not_7_out,
       not_8_out, not_9_out, not_10_out, not_11_out;

  not not_1 (not_1_out, e4);
  not not_2 (not_2_out, e3);
  not not_3 (not_3_out, e2);
  not not_4 (not_4_out, e1);
  not not_5 (not_5_out, e4);
  not not_6 (not_6_out, e3);
  not not_7 (not_7_out, e1);
  not not_8 (not_8_out, e0);
  not not_9 (not_9_out, e6);
  not not_10 (not_10_out, e5);
  not not_11 (not_11_out, e2);
  and and_1 (and_1_out, e6, e5, not_1_out, not_2_out, not_3_out, not_4_out, e0);
  and and_2 (and_2_out, e6, e5, not_5_out, not_6_out, e2, not_7_out, not_8_out);
  or or_1 (s0, not_9_out, not_10_out, not_11_out, e0, e1, e3, e4);
  or or_2 (s1, and_1_out, and_2_out);
endmodule

// cont
module contador (
  input  diez_en_diez,
  input  generar,
  output [3:0] decenas,
  output [3:0] unidades,
  output [7:0] numero
);

  wire [7:0] adder_1_out, adder_2_out, multiplexer_1_out;
  wire [7:4] divider_1_out, divider_1_rem;

  Adder adder_1 (.a(numero), .b(8'h1), .out(adder_1_out));  // open: cin, cout
  Adder adder_2 (.a(8'ha), .b(numero), .out(adder_2_out));  // open: cin, cout
  Multiplexer #(.width(8)) multiplexer_1 (
    .in0(adder_1_out), .in1(adder_2_out), .out(multiplexer_1_out), .sel(diez_en_diez), .en(1'b1));
  Register register_1 (.D(multiplexer_1_out), .Q(numero), .clk(generar));  // open: en, clr
  Divider divider_1 (
    .a(numero), .b(8'ha), .out({divider_1_out, decenas}), .rem({divider_1_rem, unidades}));  // open: upper
endmodule

// cols
module detector_colision (
  input  [31:0] columna,
  input  [31:0] personaje,
  input  [31:0] peligro,
  output colision,
  output destroy
);

  wire colision0, colision1, colision2, colision3, colision4, colision5, colision6, colision7, colision8,
       colision9, colision10, colision11, colision12, colision13, colision14, colision15, colision16,
       colision17, colision18, colision19, colision20, colision21, colision22, colision23, colision24,
       colision25, colision26, colision27, colision28, colision29, destroy0, destroy1, destroy2, destroy3,
       destroy4, destroy5, destroy6, destroy7, destroy8, destroy9, destroy10, destroy11, destroy12,
       destroy13, destroy14, destroy15, destroy16, destroy17, destroy18, destroy19, destroy20, destroy21,
       destroy22, destroy23, destroy24, destroy25, destroy26, destroy27, destroy28, destroy29, or_2_out;

  and and_1 (colision0, personaje[0], personaje[1], columna[2]);
  and and_2 (colision1, personaje[1], personaje[2], columna[3]);
  and and_3 (colision2, personaje[2], personaje[3], columna[4]);
  and and_4 (colision3, personaje[3], personaje[4], columna[5]);
  and and_5 (colision4, personaje[4], personaje[5], columna[6]);
  and and_6 (colision5, personaje[5], personaje[6], columna[7]);
  and and_7 (colision6, personaje[6], personaje[7], columna[8]);
  and and_8 (colision7, personaje[7], personaje[8], columna[9]);
  and and_9 (destroy0, personaje[0], personaje[1], peligro[2]);
  and and_10 (destroy1, personaje[1], personaje[2], peligro[3]);
  and and_11 (destroy2, personaje[2], personaje[3], peligro[4]);
  and and_12 (destroy3, personaje[3], personaje[4], peligro[5]);
  and and_13 (destroy4, personaje[4], personaje[5], peligro[6]);
  and and_14 (destroy5, personaje[5], personaje[6], peligro[7]);
  and and_15 (destroy6, personaje[6], personaje[7], peligro[8]);
  and and_16 (destroy7, personaje[7], personaje[8], peligro[9]);
  and and_17 (colision8, personaje[8], personaje[9], columna[10]);
  and and_18 (colision9, personaje[9], personaje[10], columna[11]);
  and and_19 (colision10, personaje[10], personaje[11], columna[12]);
  and and_20 (colision11, personaje[11], personaje[12], columna[13]);
  and and_21 (colision12, personaje[12], personaje[13], columna[14]);
  and and_22 (colision13, personaje[13], personaje[14], columna[15]);
  and and_23 (colision14, personaje[14], personaje[15], columna[16]);
  and and_24 (colision15, personaje[15], personaje[16], columna[17]);
  and and_25 (destroy8, personaje[8], personaje[9], peligro[10]);
  and and_26 (destroy9, personaje[9], personaje[10], peligro[11]);
  and and_27 (destroy10, personaje[10], personaje[11], peligro[12]);
  and and_28 (destroy11, personaje[11], personaje[12], peligro[13]);
  and and_29 (destroy12, personaje[12], personaje[13], peligro[14]);
  and and_30 (destroy13, personaje[13], personaje[14], peligro[15]);
  and and_31 (destroy14, personaje[14], personaje[15], peligro[16]);
  and and_32 (destroy15, personaje[15], personaje[16], peligro[17]);
  and and_33 (colision16, personaje[16], personaje[17], columna[18]);
  and and_34 (colision17, personaje[17], personaje[18], columna[19]);
  and and_35 (colision18, personaje[18], personaje[19], columna[20]);
  and and_36 (colision19, personaje[19], personaje[20], columna[21]);
  and and_37 (colision20, personaje[20], personaje[21], columna[22]);
  and and_38 (colision21, personaje[21], personaje[22], columna[23]);
  and and_39 (colision22, personaje[22], personaje[23], columna[24]);
  and and_40 (colision23, personaje[23], personaje[24], columna[25]);
  and and_41 (destroy16, personaje[16], personaje[17], peligro[18]);
  and and_42 (destroy17, personaje[17], personaje[18], peligro[19]);
  and and_43 (destroy18, personaje[18], personaje[19], peligro[20]);
  and and_44 (destroy19, personaje[19], personaje[20], peligro[21]);
  and and_45 (destroy20, personaje[20], personaje[21], peligro[22]);
  and and_46 (destroy21, personaje[21], personaje[22], peligro[23]);
  and and_47 (destroy22, personaje[22], personaje[23], peligro[24]);
  and and_48 (destroy23, personaje[23], personaje[24], peligro[25]);
  and and_49 (colision24, personaje[24], personaje[25], columna[26]);
  and and_50 (colision25, personaje[25], personaje[26], columna[27]);
  and and_51 (colision26, personaje[26], personaje[27], columna[28]);
  and and_52 (colision27, personaje[27], personaje[28], columna[29]);
  and and_53 (colision28, personaje[28], personaje[29], columna[30]);
  and and_54 (colision29, personaje[29], personaje[30], columna[31]);
  and and_55 (destroy24, personaje[24], personaje[25], peligro[26]);
  and and_56 (destroy25, personaje[25], personaje[26], peligro[27]);
  and and_57 (destroy26, personaje[26], personaje[27], peligro[28]);
  and and_58 (destroy27, personaje[27], personaje[28], peligro[29]);
  and and_59 (destroy28, personaje[28], personaje[29], peligro[30]);
  and and_60 (destroy29, personaje[29], personaje[30], peligro[31]);
  or or_1 (colision, colision0, colision8, colision1, colision9, colision2, colision10, colision3, colision11, colision4, colision12, colision5, colision13, colision6, colision14, colision7, colision15, colision16, colision24, colision17, colision25, colision18, colision26, colision19, colision27, colision20, colision28, colision21, colision29, colision22, colision23);
  or or_2 (or_2_out, destroy0, destroy8, destroy1, destroy9, destroy2, destroy10, destroy3, destroy11, destroy4, destroy12, destroy5, destroy13, destroy6, destroy14, destroy7, destroy15, destroy16, destroy24, destroy17, destroy25, destroy18, destroy26, destroy19, destroy27, destroy20, destroy28, destroy21, destroy29, destroy22, destroy23);
  and and_61 (destroy, or_2_out, colision);

  // Other names for the same wires on the sheet: r0 = columna[0]; r1 = columna[1]; r2 = columna[2]; r3 = columna[3];
  //   r4 = columna[4]; r5 = columna[5]; r6 = columna[6]; r7 = columna[7]; r8 = columna[8]; r9 = columna[9];
  //   r10 = columna[10]; r11 = columna[11]; r12 = columna[12]; r13 = columna[13]; r14 = columna[14];
  //   r15 = columna[15]; r16 = columna[16]; r17 = columna[17]; r18 = columna[18]; r19 = columna[19];
  //   r20 = columna[20]; r21 = columna[21]; r22 = columna[22]; r23 = columna[23]; r24 = columna[24];
  //   r25 = columna[25]; r26 = columna[26]; r27 = columna[27]; r28 = columna[28]; r29 = columna[29];
  //   r30 = columna[30]; r31 = columna[31]; p0 = peligro[0]; p1 = peligro[1]; p2 = peligro[2]; p3 = peligro[3];
  //   p4 = peligro[4]; p5 = peligro[5]; p6 = peligro[6]; p7 = peligro[7]; p8 = peligro[8]; p9 = peligro[9];
  //   p10 = peligro[10]; p11 = peligro[11]; p12 = peligro[12]; p13 = peligro[13]; p14 = peligro[14];
  //   p15 = peligro[15]; p16 = peligro[16]; p17 = peligro[17]; p18 = peligro[18]; p19 = peligro[19];
  //   p20 = peligro[20]; p21 = peligro[21]; p22 = peligro[22]; p23 = peligro[23]; p24 = peligro[24];
  //   p25 = peligro[25]; p26 = peligro[26]; p27 = peligro[27]; p28 = peligro[28]; p29 = peligro[29];
  //   p30 = peligro[30]; p31 = peligro[31]; c0 = personaje[0]; c1 = personaje[1]; c2 = personaje[2];
  //   c3 = personaje[3]; c4 = personaje[4]; c5 = personaje[5]; c6 = personaje[6]; c7 = personaje[7];
  //   c8 = personaje[8]; c9 = personaje[9]; c10 = personaje[10]; c11 = personaje[11]; c12 = personaje[12];
  //   c13 = personaje[13]; c14 = personaje[14]; c15 = personaje[15]; c16 = personaje[16]; c17 = personaje[17];
  //   c18 = personaje[18]; c19 = personaje[19]; c20 = personaje[20]; c21 = personaje[21]; c22 = personaje[22];
  //   c23 = personaje[23]; c24 = personaje[24]; c25 = personaje[25]; c26 = personaje[26]; c27 = personaje[27];
  //   c28 = personaje[28]; c29 = personaje[29]; c30 = personaje[30]; c31 = personaje[31]
endmodule
module segmentos (
  input  [3:0] in_1,
  output c,
  output d,
  output g,
  output f,
  output e,
  output b,
  output a
);

  wire and_4_out, and_7_out, and_8_out, b1nb0, b2b0, b2nb1, nb1nb0, nb2b1, nb2nb0, not_1_out, not_2_out,
       not_3_out;

  not not_1 (not_1_out, in_1[2]);
  not not_2 (not_2_out, in_1[1]);
  not not_3 (not_3_out, in_1[0]);
  and and_1 (b2b0, in_1[2], in_1[0]);
  and and_2 (nb2nb0, not_1_out, not_3_out);
  and and_3 (nb1nb0, not_2_out, not_3_out);
  and and_4 (and_4_out, in_1[1], in_1[0]);
  and and_5 (b1nb0, in_1[1], not_3_out);
  and and_6 (nb2b1, not_1_out, in_1[1]);
  and and_7 (and_7_out, b2b0, not_2_out);
  and and_8 (and_8_out, in_1[2], not_3_out);
  and and_9 (b2nb1, in_1[2], not_2_out);
  or or_1 (c, in_1[3], b2b0, nb2nb0, in_1[1]);
  or or_2 (d, in_1[3], not_1_out, nb1nb0, and_4_out);
  or or_3 (g, not_2_out, in_1[0], in_1[2]);
  or or_4 (f, nb2nb0, and_7_out, in_1[3], b1nb0, nb2b1);
  or or_5 (e, nb2nb0, b1nb0);
  or or_6 (b, nb1nb0, and_8_out, b2nb1, in_1[3]);
  or or_7 (a, in_1[3], b2nb1, b1nb0, nb2b1);
endmodule
